// Logisim project MiniMips32.circ as structural Verilog
module MiniMips32 (
  input  rst
);

  wire clk, cp0_in_delay, emreg, ewreg, exe_1_cp0_re_o, exe_1_cp0_we_o, exe_1_exe_in_delay_o,
       exe_1_exe_mreg_o, exe_1_exe_whilo_o, exe_1_exe_wreg_o, exemem_reg_1_mem_cp0_we,
       exemem_reg_1_mem_in_delay, exemem_reg_1_mem_mreg, exemem_reg_1_mem_whilo, exemem_reg_1_mem_wreg,
       flush, flush_im, id_1_id_in_delay_o, id_1_id_mreg_o, id_1_id_whilo_o, id_1_id_wreg_o,
       id_1_next_delay_o, idexe_reg_1_exe_in_delay, idexe_reg_1_exe_mreg, idexe_reg_1_exe_whilo,
       idexe_reg_1_exe_wreg, if_1_ice, mcp0we, mem_1_dce, mem_1_mem_mreg_o, mem_1_mem_whilo_o,
       mem_1_mem_wreg_o, memwb_reg_1_wb_cp0_we, memwb_reg_1_wb_mreg, memwb_reg_1_wb_whilo,
       memwb_reg_1_wb_wreg, mmreg, mwhilo, mwreg, next_delay, re1, re2, stallreq_exe, stallreq_id, wbcp0we,
       wbwhilo, wbwreg, wwhilo;
  wire [1:0] jtsel;
  wire [2:0] id_1_id_alutype_o, idexe_reg_1_exe_alutype;
  wire [3:0] mem_1_dre, mem_1_we, memwb_reg_1_wb_dre, stall;
  wire [4:0] cp0_exccode, ewa, exe_1_cp0_raddr_o, exe_1_cp0_waddr_o, exe_1_exe_exccode_o, exe_1_exe_wa_o,
       exemem_reg_1_mem_cp0_waddr, exemem_reg_1_mem_exccode, exemem_reg_1_mem_wa, id_1_cp0_addr,
       id_1_id_exccode_o, id_1_id_wa_o, idexe_reg_1_exe_cp0_addr, idexe_reg_1_exe_exccode,
       idexe_reg_1_exe_wa, mcp0wa, mem_1_mem_wa_o, memwb_reg_1_wb_cp0_waddr, memwb_reg_1_wb_wa, mwa, ra1,
       ra2, wbcp0wa, wbwa;
  wire [7:0] exe_1_exe_aluop_o, exemem_reg_1_mem_aluop, id_1_id_aluop_o, idexe_reg_1_exe_aluop,
       mem_1_mem_aluop_o, memwb_reg_1_wb_aluop;
  wire [23:0] if_1_iaddr, mem_1_daddr;
  wire [31:0] addr1, addr2, addr3, cp0_badvaddr, cp0_data, cp0_excaddr, cp0_pc, cp0_reg_1_cause_o,
       cp0_reg_1_status_o, dm_1_dout, ewd, exe_1_cp0_wdata_o, exe_1_exe_din_o, exe_1_exe_hi_o,
       exe_1_exe_lo_o, exe_1_exe_pc_o, exe_1_exe_wd_o, exemem_reg_1_mem_cp0_wdata, exemem_reg_1_mem_din,
       exemem_reg_1_mem_hi, exemem_reg_1_mem_lo, exemem_reg_1_mem_pc, exemem_reg_1_mem_wd, hilo_1_out_5,
       hilo_1_out_6, id_1_id_din_o, id_1_id_pc_o, id_1_id_src1_o, id_1_id_src2_o, id_1_ret_addr,
       idexe_reg_1_exe_din, idexe_reg_1_exe_pc, idexe_reg_1_exe_ret_addr, idexe_reg_1_exe_src1,
       idexe_reg_1_exe_src2, if_1_pc, ifid_reg_1_id_inst, ifid_reg_1_id_pc, im_1_inst, mcp0wd, mem_1_din,
       mem_1_mem_dreg_o, mem_1_mem_hi_o, mem_1_mem_lo_o, memwb_reg_1_wb_cp0_wdata, memwb_reg_1_wb_dm,
       memwb_reg_1_wb_dreg, memwb_reg_1_wb_hi, memwb_reg_1_wb_lo, mhi, mlo, multiplexer_1_out,
       multiplexer_2_out, mwd, regfile_1_rd1, regfile_1_rd2, wbcp0wd, wbhi, wblo, wbwd, whi, wlo;

  Clock u_clk (.out(clk));
  \if  if_1 (
    .clk(clk), .pc(if_1_pc), .iaddr(if_1_iaddr), .ice(if_1_ice), .rst(rst), .addr1(addr1), .addr2(addr2),
    .addr3(addr3), .jtsel(jtsel), .stall(stall), .flush(flush), .cp0_excaddr(cp0_excaddr));
  IM im_1 (.iaddr(if_1_iaddr), .ice(if_1_ice), .inst(im_1_inst));
  ifid_reg ifid_reg_1 (
    .if_pc(if_1_pc), .rst(rst), .clk(clk), .id_pc(ifid_reg_1_id_pc), .if_inst(im_1_inst),
    .id_inst(ifid_reg_1_id_inst), .stall(stall), .flush(flush));
  RegFile regfile_1 (
    .we(wbwreg), .ra1(ra1), .ra2(ra2), .rd1(regfile_1_rd1), .wa(wbwa), .rd2(regfile_1_rd2), .wd(wbwd),
    .clk(clk), .re1(re1), .re1_2(re2));
  id id_1 (
    .id_inst_i(ifid_reg_1_id_inst), .rd1(regfile_1_rd1), .rd2(regfile_1_rd2), .rst(rst),
    .id_mreg_o(id_1_id_mreg_o), .id_whilo_o(id_1_id_whilo_o), .id_wreg_o(id_1_id_wreg_o),
    .id_alutype_o(id_1_id_alutype_o), .id_aluop_o(id_1_id_aluop_o), .id_wa_o(id_1_id_wa_o),
    .id_src1_o(id_1_id_src1_o), .ra1(ra1), .ra2(ra2), .id_src2_o(id_1_id_src2_o), .id_din_o(id_1_id_din_o),
    .rreg1(re1), .rreg2(re2), .exe2id_wa(ewa), .mem2id_wa(mwa), .exe2id_wreg(ewreg), .mem2id_wreg(mwreg),
    .exe2id_wd(ewd), .mem2id_wd(mwd), .jtsel(jtsel), .addr1(addr1), .addr3(addr3), .addr2(addr2),
    .id_pc_i(ifid_reg_1_id_pc), .ret_addr(id_1_ret_addr), .stallreq_id(stallreq_id), .exe2id_mreg(emreg),
    .mem2id_mreg(mmreg), .flush_im(flush_im), .id_in_delay_i(next_delay), .cp0_addr(id_1_cp0_addr),
    .id_pc_o(id_1_id_pc_o), .id_in_delay_o(id_1_id_in_delay_o), .next_delay_o(id_1_next_delay_o),
    .id_exccode_o(id_1_id_exccode_o));
  HILO hilo_1 (.we(wbwhilo), .in_2(wbhi), .in_3(wblo), .clk(clk), .out_5(hilo_1_out_5), .out_6(hilo_1_out_6));
  Multiplexer #(.select(2), .width(32), .enable("false")) multiplexer_1 (
    .in0(hilo_1_out_5), .in1(whi), .in2(mhi), .in3(mhi), .out(multiplexer_1_out), .sel({mwhilo, wwhilo}));
  idexe_reg idexe_reg_1 (
    .id_mreg(id_1_id_mreg_o), .id_whilo(id_1_id_whilo_o), .id_wreg(id_1_id_wreg_o),
    .id_alutype(id_1_id_alutype_o), .id_aluop(id_1_id_aluop_o), .id_wa(id_1_id_wa_o),
    .id_src1(id_1_id_src1_o), .id_src2(id_1_id_src2_o), .id_din(id_1_id_din_o),
    .exe_mreg(idexe_reg_1_exe_mreg), .exe_whilo(idexe_reg_1_exe_whilo), .exe_wreg(idexe_reg_1_exe_wreg),
    .exe_alutype(idexe_reg_1_exe_alutype), .exe_aluop(idexe_reg_1_exe_aluop), .exe_wa(idexe_reg_1_exe_wa),
    .exe_src1(idexe_reg_1_exe_src1), .exe_src2(idexe_reg_1_exe_src2), .exe_din(idexe_reg_1_exe_din),
    .id_ret_addr(id_1_ret_addr), .exe_ret_addr(idexe_reg_1_exe_ret_addr), .stall(stall), .rst(rst),
    .clk(clk), .id_cp0_addr(id_1_cp0_addr), .id_pc(id_1_id_pc_o), .id_in_delay(id_1_id_in_delay_o),
    .next_delay_i(id_1_next_delay_o), .id_exccode(id_1_id_exccode_o), .flush(flush),
    .exe_cp0_addr(idexe_reg_1_exe_cp0_addr), .exe_pc(idexe_reg_1_exe_pc),
    .exe_in_delay(idexe_reg_1_exe_in_delay), .next_delay_o(next_delay), .exe_exccode(idexe_reg_1_exe_exccode));
  Multiplexer #(.select(2), .width(32), .enable("false")) multiplexer_2 (
    .in0(hilo_1_out_6), .in1(wlo), .in2(mlo), .in3(mlo), .out(multiplexer_2_out), .sel({mwhilo, wwhilo}));
  SCU scu_1 (.stallreq_id(stallreq_id), .stallreq_exe(stallreq_exe), .stall(stall));
  exe exe_1 (
    .exe_mreg_i(idexe_reg_1_exe_mreg), .exe_whilo_i(idexe_reg_1_exe_whilo),
    .exe_wreg_i(idexe_reg_1_exe_wreg), .exe_alutype_i(idexe_reg_1_exe_alutype),
    .exe_aluop_i(idexe_reg_1_exe_aluop), .exe_wa_i(idexe_reg_1_exe_wa), .exe_src1_i(idexe_reg_1_exe_src1),
    .exe_src2_i(idexe_reg_1_exe_src2), .exe_din_i(idexe_reg_1_exe_din), .hi_i(multiplexer_1_out),
    .lo_i(multiplexer_2_out), .rst(rst), .exe_mreg_o(exe_1_exe_mreg_o), .exe_whilo_o(exe_1_exe_whilo_o),
    .exe_wreg_o(exe_1_exe_wreg_o), .exe_aluop_o(exe_1_exe_aluop_o), .exe_wa_o(exe_1_exe_wa_o),
    .exe_hi_o(exe_1_exe_hi_o), .exe_lo_o(exe_1_exe_lo_o), .exe_wd_o(exe_1_exe_wd_o),
    .exe_din_o(exe_1_exe_din_o), .exe2id_wreg(ewreg), .exe2id_wa(ewa), .exe2id_wd(ewd),
    .exe_ret_addr(idexe_reg_1_exe_ret_addr), .clk(clk), .stallreq_exe(stallreq_exe), .exe2id_mreg(emreg),
    .cp0_addr_i(idexe_reg_1_exe_cp0_addr), .cp0_data_i(cp0_data), .mem2exe_cp0_we(mcp0we),
    .mem2exe_cp0_wa(mcp0wa), .mem2exe_cp0_wd(mcp0wd), .wb2exe_cp0_we(wbcp0we), .wb2exe_cp0_wa(wbcp0wa),
    .wb2exe_cp0_wd(wbcp0wd), .exe_pc_i(idexe_reg_1_exe_pc), .exe_in_delay_i(idexe_reg_1_exe_in_delay),
    .exe_exccode_i(idexe_reg_1_exe_exccode), .cp0_re_o(exe_1_cp0_re_o), .cp0_raddr_o(exe_1_cp0_raddr_o),
    .cp0_we_o(exe_1_cp0_we_o), .cp0_waddr_o(exe_1_cp0_waddr_o), .cp0_wdata_o(exe_1_cp0_wdata_o),
    .exe_pc_o(exe_1_exe_pc_o), .exe_in_delay_o(exe_1_exe_in_delay_o), .exe_exccode_o(exe_1_exe_exccode_o));
  exemem_reg exemem_reg_1 (
    .exe_mreg(exe_1_exe_mreg_o), .exe_whilo(exe_1_exe_whilo_o), .exe_wreg(exe_1_exe_wreg_o),
    .exe_aluop(exe_1_exe_aluop_o), .exe_wa(exe_1_exe_wa_o), .exe_hi(exe_1_exe_hi_o), .exe_lo(exe_1_exe_lo_o),
    .exe_wd(exe_1_exe_wd_o), .exe_din(exe_1_exe_din_o), .mem_mreg(exemem_reg_1_mem_mreg),
    .mem_whilo(exemem_reg_1_mem_whilo), .mem_wreg(exemem_reg_1_mem_wreg), .mem_aluop(exemem_reg_1_mem_aluop),
    .mem_wa(exemem_reg_1_mem_wa), .mem_hi(exemem_reg_1_mem_hi), .mem_lo(exemem_reg_1_mem_lo),
    .mem_wd(exemem_reg_1_mem_wd), .mem_din(exemem_reg_1_mem_din), .rst(rst), .clk(clk), .stall(stall),
    .exe_cp0_we(exe_1_cp0_we_o), .exe_cp0_waddr(exe_1_cp0_waddr_o), .exe_cp0_wdata(exe_1_cp0_wdata_o),
    .exe_pc(exe_1_exe_pc_o), .exe_in_delay(exe_1_exe_in_delay_o), .exe_exccode(exe_1_exe_exccode_o),
    .mem_cp0_we(exemem_reg_1_mem_cp0_we), .mem_cp0_waddr(exemem_reg_1_mem_cp0_waddr),
    .mem_cp0_wdata(exemem_reg_1_mem_cp0_wdata), .mem_pc(exemem_reg_1_mem_pc),
    .mem_in_delay(exemem_reg_1_mem_in_delay), .mem_exccode(exemem_reg_1_mem_exccode), .flush(flush));
  cp0_reg cp0_reg_1 (
    .rst(rst), .we(wbcp0we), .waddr(wbcp0wa), .wdata(wbcp0wd), .in_delay_i(cp0_in_delay),
    .raddr(exe_1_cp0_raddr_o), .re(exe_1_cp0_re_o), .int_i({8{1'b0}}), .pc_i(cp0_pc),
    .exccode_i(cp0_exccode), .clk(clk), .status_o(cp0_reg_1_status_o), .cause_o(cp0_reg_1_cause_o),
    .data_o(cp0_data), .flush_im(flush_im), .flush(flush), .cp0_excaddr(cp0_excaddr),
    .badvaddr_i(cp0_badvaddr));
  mem mem_1 (
    .mem_mreg_i(exemem_reg_1_mem_mreg), .mem_whilo_i(exemem_reg_1_mem_whilo),
    .mem_wreg_i(exemem_reg_1_mem_wreg), .mem_aluop_i(exemem_reg_1_mem_aluop), .mem_wa_i(exemem_reg_1_mem_wa),
    .mem_hi_i(exemem_reg_1_mem_hi), .mem_lo_i(exemem_reg_1_mem_lo), .mem_wd_i(exemem_reg_1_mem_wd),
    .mem_din_i(exemem_reg_1_mem_din), .rst(rst), .mem_mreg_o(mem_1_mem_mreg_o),
    .mem_whilo_o(mem_1_mem_whilo_o), .mem_wreg_o(mem_1_mem_wreg_o), .mem_wa_o(mem_1_mem_wa_o),
    .mem_hi_o(mem_1_mem_hi_o), .mem_lo_o(mem_1_mem_lo_o), .mem_dreg_o(mem_1_mem_dreg_o), .dre(mem_1_dre),
    .dce(mem_1_dce), .daddr(mem_1_daddr), .we(mem_1_we), .din(mem_1_din), .mem2id_wa(mwa),
    .mem2id_wreg(mwreg), .mem2id_wd(mwd), .mem2exe_whilo(mwhilo), .mem2exe_hi(mhi), .mem2exe_lo(mlo),
    .mem2id_mreg(mmreg), .cp0_pc(cp0_pc), .cp0_we_i(exemem_reg_1_mem_cp0_we),
    .cp0_waddr_i(exemem_reg_1_mem_cp0_waddr), .cp0_wdata_i(exemem_reg_1_mem_cp0_wdata),
    .wb2mem_cp0_we(wbcp0we), .wb2mem_cp0_wa(wbcp0wa), .wb2mem_cp0_wd(wbcp0wd),
    .mem_pc_i(exemem_reg_1_mem_pc), .mem_in_delay_i(exemem_reg_1_mem_in_delay),
    .mem_exccode_i(exemem_reg_1_mem_exccode), .cp0_status(cp0_reg_1_status_o), .cp0_cause(cp0_reg_1_cause_o),
    .cp0_we_o(mcp0we), .cp0_waddr_o(mcp0wa), .cp0_wdata_o(mcp0wd), .cp0_in_delay(cp0_in_delay),
    .cp0_exccode(cp0_exccode), .mem_aluop_o(mem_1_mem_aluop_o), .cp0_badvaddr(cp0_badvaddr));
  DM dm_1 (
    .daddr(mem_1_daddr), .we(mem_1_we), .dce(mem_1_dce), .din(mem_1_din), .dout(dm_1_dout), .clk(clk),
    .rst(rst));
  memwb_reg memwb_reg_1 (
    .mem_mreg(mem_1_mem_mreg_o), .mem_whilo(mem_1_mem_whilo_o), .mem_wreg(mem_1_mem_wreg_o),
    .mem_wa(mem_1_mem_wa_o), .mem_hi(mem_1_mem_hi_o), .mem_lo(mem_1_mem_lo_o), .mem_dreg(mem_1_mem_dreg_o),
    .mem_dre(mem_1_dre), .rst(rst), .clk(clk), .wb_mreg(memwb_reg_1_wb_mreg),
    .wb_whilo(memwb_reg_1_wb_whilo), .wb_wreg(memwb_reg_1_wb_wreg), .wb_wa(memwb_reg_1_wb_wa),
    .wb_hi(memwb_reg_1_wb_hi), .wb_lo(memwb_reg_1_wb_lo), .wb_dreg(memwb_reg_1_wb_dreg),
    .wb_dre(memwb_reg_1_wb_dre), .mem_dm(dm_1_dout), .wb_dm(memwb_reg_1_wb_dm), .mem_cp0_we(mcp0we),
    .mem_cp0_waddr(mcp0wa), .mem_cp0_wdata(mcp0wd), .wb_cp0_we(memwb_reg_1_wb_cp0_we),
    .wb_cp0_waddr(memwb_reg_1_wb_cp0_waddr), .wb_cp0_wdata(memwb_reg_1_wb_cp0_wdata), .flush(flush),
    .mem_aluop(mem_1_mem_aluop_o), .wb_aluop(memwb_reg_1_wb_aluop));
  wb wb_1 (
    .wb_mreg_i(memwb_reg_1_wb_mreg), .wb_whilo_i(memwb_reg_1_wb_whilo), .wb_wreg_i(memwb_reg_1_wb_wreg),
    .wb_wa_i(memwb_reg_1_wb_wa), .wb_hi_i(memwb_reg_1_wb_hi), .wb_lo_i(memwb_reg_1_wb_lo),
    .wb_dreg_i(memwb_reg_1_wb_dreg), .dm(memwb_reg_1_wb_dm), .clk(clk), .wb_whilo_o(wbwhilo),
    .wb_wreg_o(wbwreg), .wb_wa_o(wbwa), .wb_hi_o(wbhi), .wb_lo_o(wblo), .wb_wd_o(wbwd),
    .wb_dre_i(memwb_reg_1_wb_dre), .wb2exe_whilo(wwhilo), .wb2exe_hi(whi), .wb2exe_lo(wlo),
    .cp0_we_i(memwb_reg_1_wb_cp0_we), .cp0_waddr_i(memwb_reg_1_wb_cp0_waddr),
    .cp0_wdata_i(memwb_reg_1_wb_cp0_wdata), .cp0_we_o(wbcp0we), .cp0_waddr_o(wbcp0wa), .cp0_wdata_o(wbcp0wd),
    .wb_aluop_i(memwb_reg_1_wb_aluop));
endmodule

module IM (
  input  [23:0] iaddr,
  input  ice,
  output [31:0] inst
);

  ROM #(.addrWidth(24), .dataWidth(32)) rom_1 (.addr(iaddr), .data(inst), .sel(ice));

  // Notes on the sheet:
  //   contents of rom_1 (hex, n*v repeats v):
  //   ff7f013c ff7f023c 20302200 1111033c 1111043c 1111053c 58*0 1111013c 1111023c 18000042
endmodule

module DM (
  input  [23:0] daddr,
  input  dce,
  input  [3:0] we,
  input  [31:0] din,
  input  clk,
  input  rst,
  output [31:0] dout
);

  wire not_1_out, not_2_out, not_3_out, not_4_out;

  not not_1 (not_1_out, rst);
  RAM #(.addrWidth(24), .bus("separate")) ram_1 (
    .addr(daddr), .din(din[7:0]), .data(dout[7:0]), .str(we[0]), .sel(dce), .clk(clk), .ld(1'b1),
    .clr(not_1_out));
  RAM #(.addrWidth(24), .bus("separate")) ram_2 (
    .addr(daddr), .din(din[15:8]), .data(dout[15:8]), .str(we[1]), .sel(dce), .clk(clk), .ld(1'b1),
    .clr(not_2_out));
  not not_2 (not_2_out, rst);
  RAM #(.addrWidth(24), .bus("separate")) ram_3 (
    .addr(daddr), .din(din[23:16]), .data(dout[23:16]), .str(we[2]), .sel(dce), .clk(clk), .ld(1'b1),
    .clr(not_3_out));
  not not_3 (not_3_out, rst);
  not not_4 (not_4_out, rst);
  RAM #(.addrWidth(24), .bus("separate")) ram_4 (
    .addr(daddr), .din(din[31:24]), .data(dout[31:24]), .str(we[3]), .sel(dce), .clk(clk), .ld(1'b1),
    .clr(not_4_out));
endmodule

module RegFile (
  input  clk,
  input  [31:0] wd,
  input  we,
  input  [4:0] ra1,
  input  [4:0] wa,
  input  re1,
  input  [4:0] ra2,
  input  re1_2,
  output [31:0] rd1,
  output [31:0] rd2
);

  wire and_1_out, and_2_out, comparator_1_eq, comparator_2_eq, demultiplexer_1_out0, demultiplexer_1_out1,
       demultiplexer_1_out2, demultiplexer_1_out3, demultiplexer_1_out4, demultiplexer_1_out5,
       demultiplexer_1_out6, demultiplexer_1_out7, demultiplexer_1_out8, demultiplexer_1_out9,
       demultiplexer_1_out10, demultiplexer_1_out11, demultiplexer_1_out12, demultiplexer_1_out13,
       demultiplexer_1_out14, demultiplexer_1_out15, demultiplexer_1_out16, demultiplexer_1_out17,
       demultiplexer_1_out18, demultiplexer_1_out19, demultiplexer_1_out20, demultiplexer_1_out21,
       demultiplexer_1_out22, demultiplexer_1_out23, demultiplexer_1_out24, demultiplexer_1_out25,
       demultiplexer_1_out26, demultiplexer_1_out27, demultiplexer_1_out28, demultiplexer_1_out29,
       demultiplexer_1_out30, demultiplexer_1_out31;
  wire [31:0] multiplexer_1_out, multiplexer_2_out, register_1_q, register_2_q, register_3_q, register_4_q,
       register_5_q, register_6_q, register_7_q, register_8_q, register_9_q, register_10_q, register_11_q,
       register_12_q, register_13_q, register_14_q, register_15_q, register_16_q, register_17_q,
       register_18_q, register_19_q, register_20_q, register_21_q, register_22_q, register_23_q,
       register_24_q, register_25_q, register_26_q, register_27_q, register_28_q, register_29_q,
       register_30_q, register_31_q, register_32_q;

  Demultiplexer #(.select(5), .enable("false")) demultiplexer_1 (
    .out0(demultiplexer_1_out0), .out1(demultiplexer_1_out1), .out2(demultiplexer_1_out2),
    .out3(demultiplexer_1_out3), .out4(demultiplexer_1_out4), .out5(demultiplexer_1_out5),
    .out6(demultiplexer_1_out6), .out7(demultiplexer_1_out7), .out8(demultiplexer_1_out8),
    .out9(demultiplexer_1_out9), .out10(demultiplexer_1_out10), .out11(demultiplexer_1_out11),
    .out12(demultiplexer_1_out12), .out13(demultiplexer_1_out13), .out14(demultiplexer_1_out14),
    .out15(demultiplexer_1_out15), .out16(demultiplexer_1_out16), .out17(demultiplexer_1_out17),
    .out18(demultiplexer_1_out18), .out19(demultiplexer_1_out19), .out20(demultiplexer_1_out20),
    .out21(demultiplexer_1_out21), .out22(demultiplexer_1_out22), .out23(demultiplexer_1_out23),
    .out24(demultiplexer_1_out24), .out25(demultiplexer_1_out25), .out26(demultiplexer_1_out26),
    .out27(demultiplexer_1_out27), .out28(demultiplexer_1_out28), .out29(demultiplexer_1_out29),
    .out30(demultiplexer_1_out30), .out31(demultiplexer_1_out31), .in(we), .sel(wa));
  Register #(.width(32)) register_1 (.D(wd), .en(demultiplexer_1_out0), .Q(register_1_q), .clk(clk));  // open: clr
  Register #(.width(32)) register_2 (.D(wd), .en(demultiplexer_1_out1), .Q(register_2_q), .clk(clk));  // open: clr
  Register #(.width(32)) register_3 (.D(wd), .en(demultiplexer_1_out2), .Q(register_3_q), .clk(clk));  // open: clr
  Register #(.width(32)) register_4 (.D(wd), .en(demultiplexer_1_out3), .Q(register_4_q), .clk(clk));  // open: clr
  Register #(.width(32)) register_5 (.D(wd), .en(demultiplexer_1_out4), .Q(register_5_q), .clk(clk));  // open: clr
  Register #(.width(32)) register_6 (.D(wd), .en(demultiplexer_1_out5), .Q(register_6_q), .clk(clk));  // open: clr
  Register #(.width(32)) register_7 (.D(wd), .en(demultiplexer_1_out6), .Q(register_7_q), .clk(clk));  // open: clr
  Register #(.width(32)) register_8 (.D(wd), .en(demultiplexer_1_out7), .Q(register_8_q), .clk(clk));  // open: clr
  Register #(.width(32)) register_9 (.D(wd), .en(demultiplexer_1_out8), .Q(register_9_q), .clk(clk));  // open: clr
  Register #(.width(32)) register_10 (.D(wd), .en(demultiplexer_1_out9), .Q(register_10_q), .clk(clk));  // open: clr
  Register #(.width(32)) register_11 (.D(wd), .en(demultiplexer_1_out10), .Q(register_11_q), .clk(clk));  // open: clr
  Register #(.width(32)) register_12 (.D(wd), .en(demultiplexer_1_out11), .Q(register_12_q), .clk(clk));  // open: clr
  Register #(.width(32)) register_13 (.D(wd), .en(demultiplexer_1_out12), .Q(register_13_q), .clk(clk));  // open: clr
  Register #(.width(32)) register_14 (.D(wd), .en(demultiplexer_1_out13), .Q(register_14_q), .clk(clk));  // open: clr
  Register #(.width(32)) register_15 (.D(wd), .en(demultiplexer_1_out14), .Q(register_15_q), .clk(clk));  // open: clr
  Register #(.width(32)) register_16 (.D(wd), .en(demultiplexer_1_out15), .Q(register_16_q), .clk(clk));  // open: clr
  Register #(.width(32)) register_17 (.D(wd), .en(demultiplexer_1_out16), .Q(register_17_q), .clk(clk));  // open: clr
  Register #(.width(32)) register_18 (.D(wd), .en(demultiplexer_1_out17), .Q(register_18_q), .clk(clk));  // open: clr
  Register #(.width(32)) register_19 (.D(wd), .en(demultiplexer_1_out18), .Q(register_19_q), .clk(clk));  // open: clr
  Register #(.width(32)) register_20 (.D(wd), .en(demultiplexer_1_out19), .Q(register_20_q), .clk(clk));  // open: clr
  Register #(.width(32)) register_21 (.D(wd), .en(demultiplexer_1_out20), .Q(register_21_q), .clk(clk));  // open: clr
  Register #(.width(32)) register_22 (.D(wd), .en(demultiplexer_1_out21), .Q(register_22_q), .clk(clk));  // open: clr
  Register #(.width(32)) register_23 (.D(wd), .en(demultiplexer_1_out22), .Q(register_23_q), .clk(clk));  // open: clr
  Register #(.width(32)) register_24 (.D(wd), .en(demultiplexer_1_out23), .Q(register_24_q), .clk(clk));  // open: clr
  Register #(.width(32)) register_25 (.D(wd), .en(demultiplexer_1_out24), .Q(register_25_q), .clk(clk));  // open: clr
  Register #(.width(32)) register_26 (.D(wd), .en(demultiplexer_1_out25), .Q(register_26_q), .clk(clk));  // open: clr
  Register #(.width(32)) register_27 (.D(wd), .en(demultiplexer_1_out26), .Q(register_27_q), .clk(clk));  // open: clr
  Register #(.width(32)) register_28 (.D(wd), .en(demultiplexer_1_out27), .Q(register_28_q), .clk(clk));  // open: clr
  Register #(.width(32)) register_29 (.D(wd), .en(demultiplexer_1_out28), .Q(register_29_q), .clk(clk));  // open: clr
  Register #(.width(32)) register_30 (.D(wd), .en(demultiplexer_1_out29), .Q(register_30_q), .clk(clk));  // open: clr
  Register #(.width(32)) register_31 (.D(wd), .en(demultiplexer_1_out30), .Q(register_31_q), .clk(clk));  // open: clr
  Register #(.width(32)) register_32 (.D(wd), .en(demultiplexer_1_out31), .Q(register_32_q), .clk(clk));  // open: clr
  Multiplexer #(.select(5), .width(32)) multiplexer_1 (
    .in0(register_1_q), .in1(register_2_q), .in2(register_3_q), .in3(register_4_q), .in4(register_5_q),
    .in5(register_6_q), .in6(register_7_q), .in7(register_8_q), .in8(register_9_q), .in9(register_10_q),
    .in10(register_11_q), .in11(register_12_q), .in12(register_13_q), .in13(register_14_q),
    .in14(register_15_q), .in15(register_16_q), .in16(register_17_q), .in17(register_18_q),
    .in18(register_19_q), .in19(register_20_q), .in20(register_21_q), .in21(register_22_q),
    .in22(register_23_q), .in23(register_24_q), .in24(register_25_q), .in25(register_26_q),
    .in26(register_27_q), .in27(register_28_q), .in28(register_29_q), .in29(register_30_q),
    .in30(register_31_q), .in31(register_32_q), .out(multiplexer_1_out), .sel(ra1), .en(re1));
  Multiplexer #(.select(5), .width(32)) multiplexer_2 (
    .in0(register_1_q), .in1(register_2_q), .in2(register_3_q), .in3(register_4_q), .in4(register_5_q),
    .in5(register_6_q), .in6(register_7_q), .in7(register_8_q), .in8(register_9_q), .in9(register_10_q),
    .in10(register_11_q), .in11(register_12_q), .in12(register_13_q), .in13(register_14_q),
    .in14(register_15_q), .in15(register_16_q), .in16(register_17_q), .in17(register_18_q),
    .in18(register_19_q), .in19(register_20_q), .in20(register_21_q), .in21(register_22_q),
    .in22(register_23_q), .in23(register_24_q), .in24(register_25_q), .in25(register_26_q),
    .in26(register_27_q), .in27(register_28_q), .in28(register_29_q), .in29(register_30_q),
    .in30(register_31_q), .in31(register_32_q), .out(multiplexer_2_out), .sel(ra2), .en(re1_2));
  Comparator #(.width(5), .mode("unsigned")) comparator_1 (.a(ra1), .b(wa), .eq(comparator_1_eq));  // open: gt, lt
  Comparator #(.width(5), .mode("unsigned")) comparator_2 (.a(ra2), .b(wa), .eq(comparator_2_eq));  // open: gt, lt
  and and_1 (and_1_out, comparator_1_eq, we);
  and and_2 (and_2_out, comparator_2_eq, we);
  Multiplexer #(.width(32)) multiplexer_3 (.in0(multiplexer_1_out), .in1(wd), .out(rd1), .sel(and_1_out), .en(re1));
  Multiplexer #(.width(32)) multiplexer_4 (.in0(multiplexer_2_out), .in1(wd), .out(rd2), .sel(and_2_out), .en(re1_2));
endmodule

module \if  (
  input  flush,
  input  [31:0] cp0_excaddr,
  input  [31:0] addr3,
  input  [31:0] addr1,
  input  [1:0] jtsel,
  input  [31:0] addr2,
  input  [3:0] stall,
  input  rst,
  input  clk,
  output [31:0] pc,
  output [23:0] iaddr,
  output ice
);

  wire and_1_out, not_1_out, not_2_out, not_3_out, not_4_out, not_5_out;
  wire [31:0] adder_1_out, multiplexer_1_out, multiplexer_2_out;

  not not_1 (not_1_out, stall[0]);
  Multiplexer #(.width(32), .enable("false")) multiplexer_1 (
    .in0(multiplexer_2_out), .in1(cp0_excaddr), .out(multiplexer_1_out), .sel(flush));
  Register #(.width(32)) u_PC (
    .D(multiplexer_1_out), .en(not_1_out), .Q({pc[31:26], iaddr, pc[1:0]}), .clk(clk), .clr(not_2_out));
  not not_2 (not_2_out, rst);
  Multiplexer #(.select(2), .width(32), .enable("false")) multiplexer_2 (
    .in0(adder_1_out), .in1(addr3), .in2(addr1), .in3(addr2), .out(multiplexer_2_out), .sel(jtsel));
  Adder #(.width(32)) adder_1 (.a(32'h4), .b({pc[31:26], iaddr, pc[1:0]}), .out(adder_1_out));  // open: cin, cout
  not not_3 (not_3_out, stall[1]);
  and and_1 (and_1_out, stall[0], not_3_out);
  not not_4 (not_4_out, flush);
  not not_5 (not_5_out, and_1_out);
  and and_2 (ice, not_5_out, rst, not_4_out);

  assign pc[25:2] = iaddr;
endmodule

module ifid_reg (
  input  [31:0] if_pc,
  input  [31:0] if_inst,
  input  flush,
  input  [3:0] stall,
  input  rst,
  input  clk,
  output [31:0] id_pc,
  output [31:0] id_inst
);

  wire and_1_out, and_2_out, not_1_out, not_2_out, or_1_out;
  wire [31:0] multiplexer_1_out, multiplexer_2_out;

  not not_1 (not_1_out, stall[2]);
  and and_1 (and_1_out, stall[1], not_1_out);
  or or_1 (or_1_out, flush, and_1_out);
  Multiplexer #(.width(32), .enable("false")) multiplexer_1 (
    .in0(if_pc), .in1({32{1'b0}}), .out(multiplexer_1_out), .sel(or_1_out));
  Multiplexer #(.width(32), .enable("false")) multiplexer_2 (
    .in0(if_inst), .in1({32{1'b0}}), .out(multiplexer_2_out), .sel(or_1_out));
  and and_2 (and_2_out, not_1_out, rst);
  not not_2 (not_2_out, rst);
  Register #(.width(32)) pc (.D(multiplexer_1_out), .en(and_2_out), .Q(id_pc), .clk(clk), .clr(not_2_out));
  Register #(.width(32)) register_1 (.D(multiplexer_2_out), .en(and_2_out), .Q(id_inst), .clk(clk), .clr(not_2_out));
endmodule

module id (
  input  [31:0] id_pc_i,
  input  [4:0] exe2id_wa,
  input  [4:0] mem2id_wa,
  input  exe2id_wreg,
  input  mem2id_wreg,
  input  flush_im,
  input  [31:0] id_inst_i,
  input  [31:0] rd1,
  input  [31:0] rd2,
  input  rst,
  input  [31:0] exe2id_wd,
  input  [31:0] mem2id_wd,
  input  exe2id_mreg,
  input  mem2id_mreg,
  input  id_in_delay_i,
  output [31:0] ret_addr,
  output [31:0] addr3,
  output [31:0] addr1,
  output [31:0] addr2,
  output [1:0] jtsel,
  output id_mreg_o,
  output id_whilo_o,
  output id_wreg_o,
  output [2:0] id_alutype_o,
  output [7:0] id_aluop_o,
  output next_delay_o,
  output [4:0] id_exccode_o,
  output rreg1,
  output rreg2,
  output [4:0] cp0_addr,
  output [4:0] id_wa_o,
  output [31:0] id_src1_o,
  output [4:0] ra1,
  output [4:0] ra2,
  output [31:0] id_src2_o,
  output [31:0] id_din_o,
  output stallreq_id,
  output [31:0] id_pc_o,
  output id_in_delay_o
);

  wire and_1_out, and_2_out, and_3_out, and_4_out, and_5_out, and_6_out, comparator_1_eq, comparator_2_eq,
       comparator_3_eq, comparator_4_eq, dcu_1_immsel, dcu_1_jal, dcu_1_rtsel, dcu_1_sext, dcu_1_shift,
       dcu_1_upper, id_equ_1_equ, or_1_out, or_2_out;
  wire [1:0] dcu_1_fwrd1, dcu_1_fwrd2;
  wire [4:0] multiplexer_2_out;
  wire [5:0] multiplexer_1_out;
  wire [31:0] bit_extender_1_out, bit_extender_2_out, bit_extender_3_out, multiplexer_3_out,
       multiplexer_4_out, multiplexer_5_out, shifter_1_out;
  wire [31:6] multiplexer_1_out_2;

  Multiplexer #(.width(32), .enable("false")) multiplexer_1 (
    .in0({id_inst_i[7:0], id_inst_i[15:8], id_inst_i[23:16], id_inst_i[31:24]}), .in1({32{1'b0}}),
    .out({multiplexer_1_out_2[31:26], ra1, ra2, cp0_addr, multiplexer_1_out_2[10:6], multiplexer_1_out}),
    .sel(flush_im));
  Adder #(.width(32)) adder_1 (.a(32'h8), .b(id_pc_i), .out(ret_addr));  // open: cin, cout
  id_addr1 id_addr1_1 (
    .instr_index({ra1, ra2, cp0_addr, multiplexer_1_out_2[10:6], multiplexer_1_out}), .pc(id_pc_i),
    .addr1(addr1));
  id_addr2 id_addr2_1 (.pc(id_pc_i), .imm({cp0_addr, multiplexer_1_out_2[10:6], multiplexer_1_out}), .addr2(addr2));
  assign bit_extender_1_out = {{27{1'b0}}, multiplexer_1_out_2[10:6]};  // Bit_Extender bit_extender_1
  assign bit_extender_2_out = {{16{1'b0}}, {cp0_addr, multiplexer_1_out_2[10:6], multiplexer_1_out}};  // Bit_Extender bit_extender_2
  assign bit_extender_3_out = {{16{cp0_addr[4]}}, {cp0_addr, multiplexer_1_out_2[10:6], multiplexer_1_out}};  // Bit_Extender bit_extender_3
  Multiplexer #(.width(5), .enable("false")) multiplexer_2 (
    .in0(cp0_addr), .in1(ra2), .out(multiplexer_2_out), .sel(dcu_1_rtsel));
  Comparator #(.width(5), .mode("unsigned")) comparator_1 (
    .a(exe2id_wa), .b(ra1), .eq(comparator_1_eq));  // open: gt, lt
  Comparator #(.width(5), .mode("unsigned")) comparator_2 (
    .a(exe2id_wa), .b(ra2), .eq(comparator_2_eq));  // open: gt, lt
  Comparator #(.width(5), .mode("unsigned")) comparator_3 (
    .a(mem2id_wa), .b(ra1), .eq(comparator_3_eq));  // open: gt, lt
  Comparator #(.width(5), .mode("unsigned")) comparator_4 (
    .a(mem2id_wa), .b(ra2), .eq(comparator_4_eq));  // open: gt, lt
  DCU dcu_1 (
    .op(multiplexer_1_out_2[31:26]), .func(multiplexer_1_out), .aluop(id_aluop_o), .alutype(id_alutype_o),
    .rreg1(rreg1), .rreg2(rreg2), .wreg(id_wreg_o), .whilo(id_whilo_o), .immsel(dcu_1_immsel),
    .rtsel(dcu_1_rtsel), .sext(dcu_1_sext), .upper(dcu_1_upper), .mreg(id_mreg_o), .shift(dcu_1_shift),
    .rs(ra1), .rt(ra2), .exe2id_wa(exe2id_wa), .mem2id_wa(mem2id_wa), .exe2id_wreg(exe2id_wreg),
    .mem2id_wreg(mem2id_wreg), .fwrd1(dcu_1_fwrd1), .fwrd2(dcu_1_fwrd2), .equ(id_equ_1_equ), .jal(dcu_1_jal),
    .jtsel(jtsel), .next_delay(next_delay_o), .exc_code(id_exccode_o));
  Multiplexer #(.width(32), .enable("false")) multiplexer_3 (
    .in0(bit_extender_2_out), .in1(bit_extender_3_out), .out(multiplexer_3_out), .sel(dcu_1_sext));
  Shifter #(.width(32)) shifter_1 (.in(bit_extender_2_out), .\dist (5'b10000), .out(shifter_1_out));
  Multiplexer #(.width(32), .enable("false")) multiplexer_4 (
    .in0(multiplexer_3_out), .in1(shifter_1_out), .out(multiplexer_4_out), .sel(dcu_1_upper));
  and and_1 (and_1_out, exe2id_wreg, rreg1, comparator_1_eq);
  and and_2 (and_2_out, exe2id_wreg, rreg2, comparator_2_eq);
  and and_3 (and_3_out, mem2id_wreg, comparator_3_eq, rreg1);
  and and_4 (and_4_out, mem2id_wreg, comparator_4_eq, rreg2);
  Multiplexer #(.select(2), .width(32), .enable("false")) multiplexer_5 (
    .in0(rd1), .in1(exe2id_wd), .in2(mem2id_wd), .in3(exe2id_wd), .out(multiplexer_5_out), .sel(dcu_1_fwrd1));
  Multiplexer #(.select(2), .width(32), .enable("false")) multiplexer_6 (
    .in0(rd2), .in1(exe2id_wd), .in2(mem2id_wd), .in3(exe2id_wd), .out(id_din_o), .sel(dcu_1_fwrd2));
  Multiplexer #(.width(5), .enable("false")) multiplexer_7 (
    .in0(multiplexer_2_out), .in1({5{1'b1}}), .out(id_wa_o), .sel(dcu_1_jal));
  or or_1 (or_1_out, and_1_out, and_2_out);
  or or_2 (or_2_out, and_3_out, and_4_out);
  Multiplexer #(.width(32), .enable("false")) multiplexer_8 (
    .in0(multiplexer_5_out), .in1(bit_extender_1_out), .out(addr3), .sel(dcu_1_shift));
  Multiplexer #(.width(32), .enable("false")) multiplexer_9 (
    .in0(id_din_o), .in1(multiplexer_4_out), .out(id_src2_o), .sel(dcu_1_immsel));
  and and_5 (and_5_out, or_1_out, exe2id_mreg);
  and and_6 (and_6_out, mem2id_mreg, or_2_out);
  or or_3 (stallreq_id, and_5_out, and_6_out);
  id_equ id_equ_1 (.aluop(id_aluop_o), .src2(id_src2_o), .src1(addr3), .equ(id_equ_1_equ));

  assign id_in_delay_o = id_in_delay_i;
  assign id_pc_o = id_pc_i;
  assign id_src1_o = addr3;

  // Notes on the sheet:
  //   instr_index
  //   op
  //   func
  //   rd
  //   rs
  //   rt
  //   rt
  //   sa
  //   imm
endmodule

module id_addr1 (
  input  [25:0] instr_index,
  input  [31:0] pc,
  output [31:0] addr1
);

  wire [27:0] adder_1_out;

  Adder #(.width(32)) adder_1 (.a(32'h4), .b(pc), .out({addr1[31:28], adder_1_out}));  // open: cin, cout

  assign addr1[27:0] = {instr_index, 2'b00};
endmodule

module id_addr2 (
  input  [31:0] pc,
  input  [15:0] imm,
  output [31:0] addr2
);

  wire [31:0] adder_1_out, bit_extender_1_out;

  Adder #(.width(32)) adder_1 (.a(32'h4), .b(pc), .out(adder_1_out));  // open: cin, cout
  assign bit_extender_1_out = {{14{imm[15]}}, {imm, 2'b00}};  // Bit_Extender bit_extender_1
  Adder #(.width(32)) adder_2 (.a(adder_1_out), .b(bit_extender_1_out), .out(addr2));  // open: cin, cout
endmodule

module id_equ (
  input  [7:0] aluop,
  input  [31:0] src2,
  input  [31:0] src1,
  output equ
);

  wire comparator_1_eq, comparator_2_eq, comparator_3_eq, comparator_4_eq, comparator_5_eq, comparator_6_eq,
       comparator_7_eq, comparator_8_eq, comparator_9_eq, comparator_10_eq, comparator_10_lt,
       comparator_11_gt, comparator_12_lt, comparator_13_eq, comparator_13_gt, not_1_out, or_1_out, or_2_out,
       or_3_out, or_4_out, priority_encoder_1_gs;
  wire [2:0] priority_encoder_1_out;

  Comparator comparator_1 (.a(8'h30), .b(aluop), .eq(comparator_1_eq));  // open: gt, lt
  Comparator comparator_2 (.a(8'h31), .b(aluop), .eq(comparator_2_eq));  // open: gt, lt
  Comparator comparator_3 (.a(8'h32), .b(aluop), .eq(comparator_3_eq));  // open: gt, lt
  Comparator comparator_4 (.a(8'h33), .b(aluop), .eq(comparator_4_eq));  // open: gt, lt
  Comparator comparator_5 (.a(8'h34), .b(aluop), .eq(comparator_5_eq));  // open: gt, lt
  Comparator comparator_6 (.a(8'h36), .b(aluop), .eq(comparator_6_eq));  // open: gt, lt
  Comparator comparator_7 (.a(8'h35), .b(aluop), .eq(comparator_7_eq));  // open: gt, lt
  Comparator comparator_8 (.a(8'h37), .b(aluop), .eq(comparator_8_eq));  // open: gt, lt
  Comparator #(.width(32)) comparator_9 (.a(src2), .b(src1), .eq(comparator_9_eq));  // open: gt, lt
  Comparator #(.width(32)) comparator_10 (
    .a(src1), .b({32{1'b0}}), .eq(comparator_10_eq), .lt(comparator_10_lt));  // open: gt
  Comparator #(.width(32)) comparator_11 (.a(src1), .b({32{1'b0}}), .gt(comparator_11_gt));  // open: eq, lt
  Comparator #(.width(32)) comparator_12 (.a(src1), .b({32{1'b0}}), .lt(comparator_12_lt));  // open: gt, eq
  Comparator #(.width(32)) comparator_13 (
    .a(src1), .b({32{1'b0}}), .gt(comparator_13_gt), .eq(comparator_13_eq));  // open: lt
  or or_1 (or_1_out, comparator_5_eq, comparator_6_eq);
  or or_2 (or_2_out, comparator_7_eq, comparator_8_eq);
  not not_1 (not_1_out, comparator_9_eq);
  or or_3 (or_3_out, comparator_10_eq, comparator_10_lt);
  or or_4 (or_4_out, comparator_13_gt, comparator_13_eq);
  Priority_Encoder priority_encoder_1 (
    .in0(comparator_1_eq), .in1(comparator_2_eq), .in2(comparator_3_eq), .in3(comparator_4_eq),
    .in4(or_1_out), .in5(or_2_out), .out(priority_encoder_1_out), .gs(priority_encoder_1_gs));  // open: in6, in7, en_in, en_out
  Multiplexer #(.select(3), .disabled(0)) multiplexer_1 (
    .in0(comparator_9_eq), .in1(not_1_out), .in2(or_3_out), .in3(comparator_11_gt), .in4(comparator_12_lt),
    .in5(or_4_out), .out(equ), .sel(priority_encoder_1_out), .en(priority_encoder_1_gs));  // open: in6, in7
endmodule

module idexe_reg (
  input  id_mreg,
  input  id_whilo,
  input  id_wreg,
  input  [2:0] id_alutype,
  input  [7:0] id_aluop,
  input  [4:0] id_wa,
  input  [31:0] id_src1,
  input  [31:0] id_src2,
  input  [31:0] id_din,
  input  [31:0] id_ret_addr,
  input  [4:0] id_cp0_addr,
  input  [31:0] id_pc,
  input  id_in_delay,
  input  next_delay_i,
  input  [4:0] id_exccode,
  input  flush,
  input  [3:0] stall,
  input  rst,
  input  clk,
  output exe_mreg,
  output exe_whilo,
  output exe_wreg,
  output [2:0] exe_alutype,
  output [7:0] exe_aluop,
  output [4:0] exe_wa,
  output [31:0] exe_src1,
  output [31:0] exe_src2,
  output [31:0] exe_din,
  output [31:0] exe_ret_addr,
  output [4:0] exe_cp0_addr,
  output [31:0] exe_pc,
  output exe_in_delay,
  output next_delay_o,
  output [4:0] exe_exccode
);

  wire and_1_out, and_2_out, multiplexer_1_out, multiplexer_2_out, multiplexer_3_out, multiplexer_13_out,
       multiplexer_14_out, not_1_out, not_2_out, or_1_out;
  wire [2:0] multiplexer_4_out;
  wire [4:0] multiplexer_6_out, multiplexer_11_out, multiplexer_15_out;
  wire [7:0] multiplexer_5_out;
  wire [31:0] multiplexer_7_out, multiplexer_8_out, multiplexer_9_out, multiplexer_10_out, multiplexer_12_out;

  not not_1 (not_1_out, stall[3]);
  and and_1 (and_1_out, stall[2], not_1_out);
  or or_1 (or_1_out, flush, and_1_out);
  Multiplexer #(.enable("false")) multiplexer_1 (.in0(id_mreg), .in1(1'b0), .out(multiplexer_1_out), .sel(or_1_out));
  Multiplexer #(.enable("false")) multiplexer_2 (.in0(id_whilo), .in1(1'b0), .out(multiplexer_2_out), .sel(or_1_out));
  Multiplexer #(.enable("false")) multiplexer_3 (.in0(id_wreg), .in1(1'b0), .out(multiplexer_3_out), .sel(or_1_out));
  Multiplexer #(.width(3), .enable("false")) multiplexer_4 (
    .in0(id_alutype), .in1(3'b000), .out(multiplexer_4_out), .sel(or_1_out));
  Multiplexer #(.width(8), .enable("false")) multiplexer_5 (
    .in0(id_aluop), .in1({8{1'b0}}), .out(multiplexer_5_out), .sel(or_1_out));
  Multiplexer #(.width(5), .enable("false")) multiplexer_6 (
    .in0(id_wa), .in1({5{1'b0}}), .out(multiplexer_6_out), .sel(or_1_out));
  Multiplexer #(.width(32), .enable("false")) multiplexer_7 (
    .in0(id_src1), .in1({32{1'b0}}), .out(multiplexer_7_out), .sel(or_1_out));
  Multiplexer #(.width(32), .enable("false")) multiplexer_8 (
    .in0(id_src2), .in1({32{1'b0}}), .out(multiplexer_8_out), .sel(or_1_out));
  Multiplexer #(.width(32), .enable("false")) multiplexer_9 (
    .in0(id_din), .in1({32{1'b0}}), .out(multiplexer_9_out), .sel(or_1_out));
  Multiplexer #(.width(32), .enable("false")) multiplexer_10 (
    .in0(id_ret_addr), .in1({32{1'b0}}), .out(multiplexer_10_out), .sel(or_1_out));
  Multiplexer #(.width(5), .enable("false")) multiplexer_11 (
    .in0(id_cp0_addr), .in1({5{1'b0}}), .out(multiplexer_11_out), .sel(or_1_out));
  Multiplexer #(.width(32), .enable("false")) multiplexer_12 (
    .in0(id_pc), .in1({32{1'b0}}), .out(multiplexer_12_out), .sel(or_1_out));
  Multiplexer #(.enable("false")) multiplexer_13 (
    .in0(id_in_delay), .in1(1'b0), .out(multiplexer_13_out), .sel(or_1_out));
  Multiplexer #(.enable("false")) multiplexer_14 (
    .in0(next_delay_i), .in1(1'b0), .out(multiplexer_14_out), .sel(or_1_out));
  Multiplexer #(.width(5), .enable("false")) multiplexer_15 (
    .in0(id_exccode), .in1({5{1'b0}}), .out(multiplexer_15_out), .sel(or_1_out));
  and and_2 (and_2_out, not_1_out, rst);
  not not_2 (not_2_out, rst);
  Register #(.width(1)) register_1 (.D(multiplexer_1_out), .en(and_2_out), .Q(exe_mreg), .clk(clk), .clr(not_2_out));
  Register #(.width(1)) register_2 (.D(multiplexer_2_out), .en(and_2_out), .Q(exe_whilo), .clk(clk), .clr(not_2_out));
  Register #(.width(1)) register_3 (.D(multiplexer_3_out), .en(and_2_out), .Q(exe_wreg), .clk(clk), .clr(not_2_out));
  Register #(.width(3)) register_4 (.D(multiplexer_4_out), .en(and_2_out), .Q(exe_alutype), .clk(clk), .clr(not_2_out));
  Register register_5 (.D(multiplexer_5_out), .en(and_2_out), .Q(exe_aluop), .clk(clk), .clr(not_2_out));
  Register #(.width(5)) register_6 (.D(multiplexer_6_out), .en(and_2_out), .Q(exe_wa), .clk(clk), .clr(not_2_out));
  Register #(.width(32)) register_7 (.D(multiplexer_7_out), .en(and_2_out), .Q(exe_src1), .clk(clk), .clr(not_2_out));
  Register #(.width(32)) register_8 (.D(multiplexer_8_out), .en(and_2_out), .Q(exe_src2), .clk(clk), .clr(not_2_out));
  Register #(.width(32)) register_9 (.D(multiplexer_9_out), .en(and_2_out), .Q(exe_din), .clk(clk), .clr(not_2_out));
  Register #(.width(32)) register_10 (
    .D(multiplexer_10_out), .en(and_2_out), .Q(exe_ret_addr), .clk(clk), .clr(not_2_out));
  Register #(.width(5)) register_11 (
    .D(multiplexer_11_out), .en(and_2_out), .Q(exe_cp0_addr), .clk(clk), .clr(not_2_out));
  Register #(.width(32)) register_12 (.D(multiplexer_12_out), .en(and_2_out), .Q(exe_pc), .clk(clk), .clr(not_2_out));
  Register #(.width(1)) register_13 (
    .D(multiplexer_13_out), .en(and_2_out), .Q(exe_in_delay), .clk(clk), .clr(not_2_out));
  Register #(.width(1)) register_14 (
    .D(multiplexer_14_out), .en(and_2_out), .Q(next_delay_o), .clk(clk), .clr(not_2_out));
  Register #(.width(5)) register_15 (
    .D(multiplexer_15_out), .en(and_2_out), .Q(exe_exccode), .clk(clk), .clr(not_2_out));
endmodule

module exe (
  input  exe_mreg_i,
  input  exe_whilo_i,
  input  exe_wreg_i,
  input  [2:0] exe_alutype_i,
  input  [7:0] exe_aluop_i,
  input  [4:0] exe_wa_i,
  input  [31:0] exe_src1_i,
  input  [31:0] exe_src2_i,
  input  [31:0] exe_din_i,
  input  [31:0] hi_i,
  input  [31:0] lo_i,
  input  [31:0] exe_ret_addr,
  input  clk,
  input  rst,
  input  [31:0] exe_pc_i,
  input  exe_in_delay_i,
  input  [4:0] cp0_addr_i,
  input  wb2exe_cp0_we,
  input  [4:0] wb2exe_cp0_wa,
  input  [31:0] cp0_data_i,
  input  mem2exe_cp0_we,
  input  [4:0] mem2exe_cp0_wa,
  input  [31:0] wb2exe_cp0_wd,
  input  [31:0] mem2exe_cp0_wd,
  input  [4:0] exe_exccode_i,
  output stallreq_exe,
  output [4:0] exe2id_wa,
  output exe2id_mreg,
  output exe2id_wreg,
  output exe_mreg_o,
  output exe_whilo_o,
  output exe_wreg_o,
  output [7:0] exe_aluop_o,
  output [4:0] exe_wa_o,
  output [31:0] exe_hi_o,
  output [31:0] exe_lo_o,
  output [31:0] exe_wd_o,
  output [31:0] exe_din_o,
  output [31:0] exe2id_wd,
  output [31:0] exe_pc_o,
  output exe_in_delay_o,
  output cp0_we_o,
  output [31:0] cp0_wdata_o,
  output [4:0] cp0_raddr_o,
  output [4:0] cp0_waddr_o,
  output cp0_re_o,
  output [4:0] exe_exccode_o
);

  wire and_1_out, and_2_out, and_3_out, and_4_out, and_5_out, comparator_1_eq, comparator_2_eq,
       comparator_3_eq, comparator_4_eq, comparator_5_eq, comparator_6_eq, comparator_7_eq, comparator_8_eq,
       comparator_9_eq, comparator_12_eq, comparator_13_eq, comparator_14_eq, comparator_15_eq,
       comparator_16_eq, comparator_17_eq, comparator_18_eq, not_1_out, not_2_out, not_3_out, or_1_out,
       or_2_out, or_3_out, or_4_out, or_5_out, priority_encoder_2_gs;
  wire [1:0] priority_encoder_1_out, priority_encoder_2_out, priority_encoder_3_out;
  wire [31:0] alu_1_arithres, alu_1_divres_hi, alu_1_divres_lo, alu_1_logicres, alu_1_mulres_hi,
       alu_1_mulres_lo, alu_1_shiftres, arith_tmp, cp0_t, exe_src2_t, multiplexer_3_out, negator_1_out;

  Comparator comparator_1 (.a(exe_aluop_i), .b(8'he), .eq(comparator_1_eq));  // open: gt, lt
  Comparator comparator_2 (.a(exe_aluop_i), .b(8'hf), .eq(comparator_2_eq));  // open: gt, lt
  Comparator comparator_3 (.a(exe_aluop_i), .b(8'h14), .eq(comparator_3_eq));  // open: gt, lt
  Comparator comparator_4 (.a(exe_aluop_i), .b(8'h15), .eq(comparator_4_eq));  // open: gt, lt
  Comparator comparator_5 (.a(exe_aluop_i), .b(8'h16), .eq(comparator_5_eq));  // open: gt, lt
  Comparator comparator_6 (.a(exe_aluop_i), .b(8'h17), .eq(comparator_6_eq));  // open: gt, lt
  ALU alu_1 (
    .aluop(exe_aluop_i), .src1(exe_src1_i), .src2(exe_src2_i), .logicres(alu_1_logicres),
    .arithres(alu_1_arithres), .shiftres(alu_1_shiftres), .mulres_lo(alu_1_mulres_lo),
    .mulres_hi(alu_1_mulres_hi), .clk(clk), .divres_lo(alu_1_divres_lo), .divres_hi(alu_1_divres_hi),
    .stallreq_exe(stallreq_exe));
  Comparator #(.mode("unsigned")) comparator_7 (.a(8'hc), .b(exe_aluop_i), .eq(comparator_7_eq));  // open: gt, lt
  Comparator #(.mode("unsigned")) comparator_8 (.a(8'hd), .b(exe_aluop_i), .eq(comparator_8_eq));  // open: gt, lt
  Comparator #(.mode("unsigned")) comparator_9 (.a(8'h8c), .b(exe_aluop_i), .eq(comparator_9_eq));  // open: gt, lt
  Comparator comparator_10 (.a(8'h8d), .b(exe_aluop_i), .eq(cp0_we_o));  // open: gt, lt
  Comparator comparator_11 (.a(8'h8c), .b(exe_aluop_i), .eq(cp0_re_o));  // open: gt, lt
  Comparator #(.width(5), .mode("unsigned")) comparator_12 (
    .a(wb2exe_cp0_wa), .b(cp0_addr_i), .eq(comparator_12_eq));  // open: gt, lt
  Comparator #(.width(5), .mode("unsigned")) comparator_13 (
    .a(mem2exe_cp0_wa), .b(cp0_addr_i), .eq(comparator_13_eq));  // open: gt, lt
  Comparator comparator_14 (.a(8'h1b), .b(exe_aluop_i), .eq(comparator_14_eq));  // open: gt, lt
  Comparator comparator_15 (.a(8'h4b), .b(exe_aluop_i), .eq(comparator_15_eq));  // open: gt, lt
  Negator #(.width(32)) negator_1 (.in(exe_src2_i), .out(negator_1_out));
  Comparator comparator_16 (.a(8'h18), .b(exe_aluop_i), .eq(comparator_16_eq));  // open: gt, lt
  Comparator comparator_17 (.a(8'h48), .b(exe_aluop_i), .eq(comparator_17_eq));  // open: gt, lt
  Comparator comparator_18 (.a(8'h4b), .b(exe_aluop_i), .eq(comparator_18_eq));  // open: gt, lt
  or or_1 (or_1_out, comparator_3_eq, comparator_4_eq);
  or or_2 (or_2_out, comparator_5_eq, comparator_6_eq);
  Multiplexer #(.width(32), .enable("false")) multiplexer_1 (
    .in0({32{1'b0}}), .in1(exe_src2_i), .out(cp0_wdata_o), .sel(cp0_we_o));
  or or_3 (or_3_out, comparator_14_eq, comparator_15_eq);
  not not_1 (not_1_out, exe_src1_i[31]);
  not not_2 (not_2_out, exe_src2_t[31]);
  not not_3 (not_3_out, arith_tmp[31]);
  Priority_Encoder #(.select(2)) priority_encoder_1 (
    .in0(1'b1), .in1(comparator_7_eq), .in2(comparator_8_eq), .in3(comparator_9_eq),
    .out(priority_encoder_1_out));  // open: gs, en_out, en_in
  and and_1 (and_1_out, wb2exe_cp0_we, comparator_12_eq);
  and and_2 (and_2_out, mem2exe_cp0_we, comparator_13_eq);
  Multiplexer #(.width(32), .enable("false")) multiplexer_2 (
    .in0(exe_src2_i), .in1(negator_1_out), .out(exe_src2_t), .sel(or_3_out));
  and and_3 (and_3_out, not_1_out, not_2_out, arith_tmp[31]);
  and and_4 (and_4_out, exe_src1_i[31], exe_src2_t[31], not_3_out);
  Priority_Encoder #(.select(2)) priority_encoder_2 (
    .in0(comparator_1_eq), .in1(comparator_2_eq), .in2(or_1_out), .in3(or_2_out),
    .out(priority_encoder_2_out), .gs(priority_encoder_2_gs));  // open: en_out, en_in
  Multiplexer #(.select(2), .width(32), .enable("false")) multiplexer_3 (
    .in0({32{1'b0}}), .in1(hi_i), .in2(lo_i), .in3(cp0_t), .out(multiplexer_3_out),
    .sel(priority_encoder_1_out));
  or or_4 (or_4_out, and_3_out, and_4_out);
  or or_5 (or_5_out, comparator_16_eq, comparator_17_eq, comparator_18_eq);
  Adder #(.width(32)) adder_1 (.a(exe_src2_t), .b(exe_src1_i), .out(arith_tmp));  // open: cin, cout
  and and_5 (and_5_out, or_4_out, or_5_out);
  Multiplexer #(.select(2), .width(32)) multiplexer_4 (
    .in0(exe_src1_i), .in1(hi_i), .in2(alu_1_mulres_hi), .in3(alu_1_divres_hi), .out(exe_hi_o),
    .sel(priority_encoder_2_out), .en(priority_encoder_2_gs));
  Multiplexer #(.select(2), .width(32)) multiplexer_5 (
    .in0(lo_i), .in1(exe_src1_i), .in2(alu_1_mulres_lo), .in3(alu_1_divres_lo), .out(exe_lo_o),
    .sel(priority_encoder_2_out), .en(priority_encoder_2_gs));
  Multiplexer #(.select(3), .width(32), .enable("false")) multiplexer_6 (
    .in1(alu_1_arithres), .in2(alu_1_logicres), .in3(multiplexer_3_out), .in4(alu_1_shiftres),
    .in5(exe_ret_addr), .out(exe2id_wd), .sel(exe_alutype_i));  // open: in0, in6, in7
  Priority_Encoder #(.select(2)) priority_encoder_3 (
    .in0(1'b1), .in1(and_1_out), .in2(and_2_out), .out(priority_encoder_3_out));  // open: in3, gs, en_out, en_in
  Multiplexer #(.width(5), .enable("false")) multiplexer_7 (
    .in0(exe_exccode_i), .in1(5'b01100), .out(exe_exccode_o), .sel(and_5_out));
  Multiplexer #(.select(2), .width(32), .disabled(0)) multiplexer_8 (
    .in0(cp0_data_i), .in1(wb2exe_cp0_wd), .in2(mem2exe_cp0_wd), .out(cp0_t), .sel(priority_encoder_3_out),
    .en(cp0_re_o));  // open: in3

  assign cp0_raddr_o = cp0_addr_i;
  assign cp0_waddr_o = cp0_addr_i;
  assign exe2id_mreg = exe_mreg_i;
  assign exe2id_wa = exe_wa_i;
  assign exe2id_wreg = exe_wreg_i;
  assign exe_aluop_o = exe_aluop_i;
  assign exe_din_o = exe_din_i;
  assign exe_in_delay_o = exe_in_delay_i;
  assign exe_mreg_o = exe_mreg_i;
  assign exe_pc_o = exe_pc_i;
  assign exe_wa_o = exe_wa_i;
  assign exe_wd_o = exe2id_wd;
  assign exe_whilo_o = exe_whilo_i;
  assign exe_wreg_o = exe_wreg_i;
endmodule

module exemem_reg (
  input  exe_mreg,
  input  exe_whilo,
  input  exe_wreg,
  input  [7:0] exe_aluop,
  input  [4:0] exe_wa,
  input  [31:0] exe_hi,
  input  [31:0] exe_lo,
  input  [31:0] exe_wd,
  input  [31:0] exe_din,
  input  exe_cp0_we,
  input  [4:0] exe_cp0_waddr,
  input  [31:0] exe_cp0_wdata,
  input  [31:0] exe_pc,
  input  exe_in_delay,
  input  [4:0] exe_exccode,
  input  flush,
  input  [3:0] stall,
  input  rst,
  input  clk,
  output mem_mreg,
  output mem_whilo,
  output mem_wreg,
  output [7:0] mem_aluop,
  output [4:0] mem_wa,
  output [31:0] mem_hi,
  output [31:0] mem_lo,
  output [31:0] mem_wd,
  output [31:0] mem_din,
  output mem_cp0_we,
  output [4:0] mem_cp0_waddr,
  output [31:0] mem_cp0_wdata,
  output [31:0] mem_pc,
  output mem_in_delay,
  output [4:0] mem_exccode
);

  wire multiplexer_1_out, multiplexer_2_out, multiplexer_3_out, multiplexer_10_out, multiplexer_14_out,
       not_1_out, or_1_out;
  wire [4:0] multiplexer_5_out, multiplexer_11_out, multiplexer_15_out;
  wire [7:0] multiplexer_4_out;
  wire [31:0] multiplexer_6_out, multiplexer_7_out, multiplexer_8_out, multiplexer_9_out, multiplexer_12_out,
       multiplexer_13_out;

  or or_1 (or_1_out, flush, stall[3]);
  Multiplexer #(.enable("false")) multiplexer_1 (.in0(exe_mreg), .in1(1'b0), .out(multiplexer_1_out), .sel(or_1_out));
  Multiplexer #(.enable("false")) multiplexer_2 (.in0(exe_whilo), .in1(1'b0), .out(multiplexer_2_out), .sel(or_1_out));
  Multiplexer #(.enable("false")) multiplexer_3 (.in0(exe_wreg), .in1(1'b0), .out(multiplexer_3_out), .sel(or_1_out));
  Multiplexer #(.width(8), .enable("false")) multiplexer_4 (
    .in0(exe_aluop), .in1({8{1'b0}}), .out(multiplexer_4_out), .sel(or_1_out));
  Multiplexer #(.width(5), .enable("false")) multiplexer_5 (
    .in0(exe_wa), .in1({5{1'b0}}), .out(multiplexer_5_out), .sel(or_1_out));
  Multiplexer #(.width(32), .enable("false")) multiplexer_6 (
    .in0(exe_hi), .in1({32{1'b0}}), .out(multiplexer_6_out), .sel(or_1_out));
  Multiplexer #(.width(32), .enable("false")) multiplexer_7 (
    .in0(exe_lo), .in1({32{1'b0}}), .out(multiplexer_7_out), .sel(or_1_out));
  Multiplexer #(.width(32), .enable("false")) multiplexer_8 (
    .in0(exe_wd), .in1({32{1'b0}}), .out(multiplexer_8_out), .sel(or_1_out));
  Multiplexer #(.width(32), .enable("false")) multiplexer_9 (
    .in0(exe_din), .in1({32{1'b0}}), .out(multiplexer_9_out), .sel(or_1_out));
  Multiplexer #(.enable("false")) multiplexer_10 (
    .in0(exe_cp0_we), .in1(1'b0), .out(multiplexer_10_out), .sel(or_1_out));
  Multiplexer #(.width(5), .enable("false")) multiplexer_11 (
    .in0(exe_cp0_waddr), .in1({5{1'b0}}), .out(multiplexer_11_out), .sel(or_1_out));
  Multiplexer #(.width(32), .enable("false")) multiplexer_12 (
    .in0(exe_cp0_wdata), .in1({32{1'b0}}), .out(multiplexer_12_out), .sel(or_1_out));
  Multiplexer #(.width(32), .enable("false")) multiplexer_13 (
    .in0(exe_pc), .in1({32{1'b0}}), .out(multiplexer_13_out), .sel(or_1_out));
  Multiplexer #(.enable("false")) multiplexer_14 (
    .in0(exe_in_delay), .in1(1'b0), .out(multiplexer_14_out), .sel(or_1_out));
  Multiplexer #(.width(5), .enable("false")) multiplexer_15 (
    .in0(exe_exccode), .in1({5{1'b0}}), .out(multiplexer_15_out), .sel(or_1_out));
  not not_1 (not_1_out, rst);
  Register #(.width(1)) register_1 (.D(multiplexer_1_out), .en(rst), .Q(mem_mreg), .clk(clk), .clr(not_1_out));
  Register #(.width(1)) register_2 (.D(multiplexer_2_out), .en(rst), .Q(mem_whilo), .clk(clk), .clr(not_1_out));
  Register #(.width(1)) register_3 (.D(multiplexer_3_out), .en(rst), .Q(mem_wreg), .clk(clk), .clr(not_1_out));
  Register register_4 (.D(multiplexer_4_out), .en(rst), .Q(mem_aluop), .clk(clk), .clr(not_1_out));
  Register #(.width(5)) register_5 (.D(multiplexer_5_out), .en(rst), .Q(mem_wa), .clk(clk), .clr(not_1_out));
  Register #(.width(32)) register_6 (.D(multiplexer_6_out), .en(rst), .Q(mem_hi), .clk(clk), .clr(not_1_out));
  Register #(.width(32)) register_7 (.D(multiplexer_7_out), .en(rst), .Q(mem_lo), .clk(clk), .clr(not_1_out));
  Register #(.width(32)) register_8 (.D(multiplexer_8_out), .en(rst), .Q(mem_wd), .clk(clk), .clr(not_1_out));
  Register #(.width(32)) register_9 (.D(multiplexer_9_out), .en(rst), .Q(mem_din), .clk(clk), .clr(not_1_out));
  Register #(.width(1)) register_10 (.D(multiplexer_10_out), .en(rst), .Q(mem_cp0_we), .clk(clk), .clr(not_1_out));
  Register #(.width(5)) register_11 (.D(multiplexer_11_out), .en(rst), .Q(mem_cp0_waddr), .clk(clk), .clr(not_1_out));
  Register #(.width(32)) register_12 (.D(multiplexer_12_out), .en(rst), .Q(mem_cp0_wdata), .clk(clk), .clr(not_1_out));
  Register #(.width(32)) register_13 (.D(multiplexer_13_out), .en(rst), .Q(mem_pc), .clk(clk), .clr(not_1_out));
  Register #(.width(1)) register_14 (.D(multiplexer_14_out), .en(rst), .Q(mem_in_delay), .clk(clk), .clr(not_1_out));
  Register #(.width(5)) register_15 (.D(multiplexer_15_out), .en(rst), .Q(mem_exccode), .clk(clk), .clr(not_1_out));
endmodule

module mem (
  input  mem_mreg_i,
  input  mem_whilo_i,
  input  mem_wreg_i,
  input  [7:0] mem_aluop_i,
  input  [4:0] mem_wa_i,
  input  [31:0] mem_hi_i,
  input  [31:0] mem_lo_i,
  input  [31:0] mem_wd_i,
  input  [31:0] mem_din_i,
  input  rst,
  input  cp0_we_i,
  input  [4:0] cp0_waddr_i,
  input  [31:0] cp0_wdata_i,
  input  [31:0] cp0_status,
  input  [31:0] wb2mem_cp0_wd,
  input  wb2mem_cp0_we,
  input  [4:0] wb2mem_cp0_wa,
  input  [31:0] cp0_cause,
  input  [31:0] mem_pc_i,
  input  mem_in_delay_i,
  input  [4:0] mem_exccode_i,
  output [7:0] mem_aluop_o,
  output [4:0] mem2id_wa,
  output mem2id_mreg,
  output mem2id_wreg,
  output mem_mreg_o,
  output mem_whilo_o,
  output mem_wreg_o,
  output mem2exe_whilo,
  output [4:0] mem_wa_o,
  output [31:0] mem_hi_o,
  output [31:0] mem_lo_o,
  output [31:0] mem_dreg_o,
  output [31:0] mem2exe_hi,
  output [31:0] mem2exe_lo,
  output [3:0] dre,
  output [23:0] daddr,
  output dce,
  output [3:0] we,
  output [31:0] din,
  output [31:0] mem2id_wd,
  output cp0_we_o,
  output [4:0] cp0_waddr_o,
  output [31:0] cp0_wdata_o,
  output [31:0] cp0_pc,
  output cp0_in_delay,
  output [4:0] cp0_exccode,
  output [31:0] cp0_badvaddr
);

  wire and_2_out, and_3_out, and_4_out, and_5_out, and_6_out, and_7_out, and_8_out, comparator_1_eq,
       comparator_2_eq, comparator_3_eq, comparator_4_eq, comparator_5_eq, comparator_6_eq, comparator_7_eq,
       comparator_8_eq, comparator_9_eq, comparator_10_eq, comparator_11_eq, exc_none, mcu_1_dce, not_1_out,
       not_2_out, not_3_out, not_4_out, not_5_out, not_6_out, or_1_out;
  wire [2:0] priority_encoder_1_out;
  wire [5:0] and_1_out;
  wire [31:0] cause, status;

  assign and_1_out = cause[15:10] & status[15:10];  // AND_Gate and_1, 6 bits wide
  Comparator #(.width(2), .mode("unsigned")) comparator_1 (
    .a(2'b00), .b(mem_pc_i[1:0]), .eq(comparator_1_eq));  // open: gt, lt
  Comparator #(.mode("unsigned")) comparator_2 (.a(8'h91), .b(mem_aluop_i), .eq(comparator_2_eq));  // open: gt, lt
  Comparator #(.mode("unsigned")) comparator_3 (.a(8'h9c), .b(mem_aluop_i), .eq(comparator_3_eq));  // open: gt, lt
  Comparator #(.mode("unsigned")) comparator_4 (.a(8'h92), .b(mem_aluop_i), .eq(comparator_4_eq));  // open: gt, lt
  Comparator #(.mode("unsigned")) comparator_5 (.a(8'h99), .b(mem_aluop_i), .eq(comparator_5_eq));  // open: gt, lt
  Comparator #(.mode("unsigned")) comparator_6 (.a(8'h9a), .b(mem_aluop_i), .eq(comparator_6_eq));  // open: gt, lt
  Comparator #(.width(1), .mode("unsigned")) comparator_7 (
    .a(1'b0), .b(mem_wd_i[0]), .eq(comparator_7_eq));  // open: gt, lt
  Comparator #(.width(2), .mode("unsigned")) comparator_8 (
    .a(mem_wd_i[1:0]), .b(2'b00), .eq(comparator_8_eq));  // open: gt, lt
  MCU mcu_1 (.maddr(mem_wd_i), .aluop(mem_aluop_i), .dre(dre), .we(we), .dce(mcu_1_dce));
  not not_1 (not_1_out, comparator_1_eq);
  not not_2 (not_2_out, comparator_7_eq);
  not not_3 (not_3_out, comparator_8_eq);
  Comparator #(.width(6), .mode("unsigned")) comparator_9 (
    .a({6{1'b0}}), .b(and_1_out), .eq(comparator_9_eq));  // open: gt, lt
  or or_1 (or_1_out, comparator_2_eq, comparator_3_eq);
  Comparator #(.width(5), .mode("unsigned")) comparator_10 (
    .a(5'b01100), .b(wb2mem_cp0_wa), .eq(comparator_10_eq));  // open: gt, lt
  Comparator #(.width(5), .mode("unsigned")) comparator_11 (
    .a(5'b01101), .b(wb2mem_cp0_wa), .eq(comparator_11_eq));  // open: gt, lt
  not not_4 (not_4_out, comparator_9_eq);
  not not_5 (not_5_out, status[1]);
  and and_2 (and_2_out, wb2mem_cp0_we, comparator_10_eq);
  and and_3 (and_3_out, wb2mem_cp0_we, comparator_11_eq);
  Multiplexer #(.width(32), .enable("false")) multiplexer_1 (
    .in0(cp0_status), .in1(wb2mem_cp0_wd), .out(status), .sel(and_2_out));
  Multiplexer #(.width(32), .enable("false")) multiplexer_2 (
    .in0(cp0_cause), .in1(wb2mem_cp0_wd), .out(cause), .sel(and_3_out));
  and and_4 (and_4_out, not_4_out, status[0], not_5_out);
  and and_5 (and_5_out, or_1_out, not_2_out);
  and and_6 (and_6_out, comparator_4_eq, not_3_out);
  and and_7 (and_7_out, comparator_5_eq, not_2_out);
  and and_8 (and_8_out, comparator_6_eq, not_3_out);
  Priority_Encoder priority_encoder_1 (
    .in0(1'b1), .in1(and_5_out), .in2(and_6_out), .in3(and_7_out), .in4(and_8_out), .in5(not_1_out),
    .in6(and_4_out), .out(priority_encoder_1_out));  // open: in7, en_in, gs, en_out
  not not_6 (not_6_out, exc_none);
  Multiplexer #(.width(32), .disabled(0), .enable("false")) multiplexer_3 (
    .in0(mem_wd_i), .in1(mem_pc_i), .out(cp0_badvaddr), .sel(not_1_out));
  and and_9 (dce, mcu_1_dce, not_6_out);
  Multiplexer #(.select(3), .width(5), .enable("false")) multiplexer_4 (
    .in0(mem_exccode_i), .in1(5'b00100), .in2(5'b00100), .in3(5'b00101), .in4(5'b00101), .in5(5'b00100),
    .in6(5'b10000), .out(cp0_exccode), .sel(priority_encoder_1_out));  // open: in7
  Comparator #(.width(5), .mode("unsigned")) comparator_12 (
    .a({5{1'b0}}), .b(cp0_exccode), .eq(exc_none));  // open: gt, lt

  assign cp0_in_delay = mem_in_delay_i;
  assign cp0_pc = mem_pc_i;
  assign cp0_waddr_o = cp0_waddr_i;
  assign cp0_wdata_o = cp0_wdata_i;
  assign cp0_we_o = cp0_we_i;
  assign daddr = mem_wd_i[25:2];
  assign din = {mem_din_i[7:0], mem_din_i[15:8], mem_din_i[23:16], mem_din_i[31:24]};
  assign mem2exe_hi = mem_hi_i;
  assign mem2exe_lo = mem_lo_i;
  assign mem2exe_whilo = mem_whilo_i;
  assign mem2id_mreg = mem_mreg_i;
  assign mem2id_wa = mem_wa_i;
  assign mem2id_wd = mem_wd_i;
  assign mem2id_wreg = mem_wreg_i;
  assign mem_aluop_o = mem_aluop_i;
  assign mem_dreg_o = mem_wd_i;
  assign mem_hi_o = mem_hi_i;
  assign mem_lo_o = mem_lo_i;
  assign mem_mreg_o = mem_mreg_i;
  assign mem_wa_o = mem_wa_i;
  assign mem_whilo_o = mem_whilo_i;
  assign mem_wreg_o = mem_wreg_i;
endmodule

module memwb_reg (
  input  [7:0] mem_aluop,
  input  mem_mreg,
  input  mem_whilo,
  input  mem_wreg,
  input  [4:0] mem_wa,
  input  [31:0] mem_hi,
  input  [31:0] mem_lo,
  input  [31:0] mem_dreg,
  input  [3:0] mem_dre,
  input  [31:0] mem_dm,
  input  mem_cp0_we,
  input  [4:0] mem_cp0_waddr,
  input  [31:0] mem_cp0_wdata,
  input  flush,
  input  rst,
  input  clk,
  output [7:0] wb_aluop,
  output wb_mreg,
  output wb_whilo,
  output wb_wreg,
  output [4:0] wb_wa,
  output [31:0] wb_hi,
  output [31:0] wb_lo,
  output [31:0] wb_dreg,
  output [3:0] wb_dre,
  output [31:0] wb_dm,
  output wb_cp0_we,
  output [4:0] wb_cp0_waddr,
  output [31:0] wb_cp0_wdata
);

  wire multiplexer_2_out, multiplexer_3_out, multiplexer_4_out, multiplexer_11_out, not_1_out;
  wire [3:0] multiplexer_9_out;
  wire [4:0] multiplexer_5_out, multiplexer_12_out;
  wire [7:0] multiplexer_1_out;
  wire [31:0] multiplexer_6_out, multiplexer_7_out, multiplexer_8_out, multiplexer_10_out, multiplexer_13_out;

  Multiplexer #(.width(8), .enable("false")) multiplexer_1 (
    .in0(mem_aluop), .in1({8{1'b0}}), .out(multiplexer_1_out), .sel(flush));
  Multiplexer #(.enable("false")) multiplexer_2 (.in0(mem_mreg), .in1(1'b0), .out(multiplexer_2_out), .sel(flush));
  Multiplexer #(.enable("false")) multiplexer_3 (.in0(mem_whilo), .in1(1'b0), .out(multiplexer_3_out), .sel(flush));
  Multiplexer #(.enable("false")) multiplexer_4 (.in0(mem_wreg), .in1(1'b0), .out(multiplexer_4_out), .sel(flush));
  Multiplexer #(.width(5), .enable("false")) multiplexer_5 (
    .in0(mem_wa), .in1({5{1'b0}}), .out(multiplexer_5_out), .sel(flush));
  Multiplexer #(.width(32), .enable("false")) multiplexer_6 (
    .in0(mem_hi), .in1({32{1'b0}}), .out(multiplexer_6_out), .sel(flush));
  Multiplexer #(.width(32), .enable("false")) multiplexer_7 (
    .in0(mem_lo), .in1({32{1'b0}}), .out(multiplexer_7_out), .sel(flush));
  Multiplexer #(.width(32), .enable("false")) multiplexer_8 (
    .in0(mem_dreg), .in1({32{1'b0}}), .out(multiplexer_8_out), .sel(flush));
  Multiplexer #(.width(4), .enable("false")) multiplexer_9 (
    .in0(mem_dre), .in1(4'b0000), .out(multiplexer_9_out), .sel(flush));
  Multiplexer #(.width(32), .enable("false")) multiplexer_10 (
    .in0(mem_dm), .in1({32{1'b0}}), .out(multiplexer_10_out), .sel(flush));
  Multiplexer #(.enable("false")) multiplexer_11 (.in0(mem_cp0_we), .in1(1'b0), .out(multiplexer_11_out), .sel(flush));
  Multiplexer #(.width(5), .enable("false")) multiplexer_12 (
    .in0(mem_cp0_waddr), .in1({5{1'b0}}), .out(multiplexer_12_out), .sel(flush));
  Multiplexer #(.width(32), .enable("false")) multiplexer_13 (
    .in0(mem_cp0_wdata), .in1({32{1'b0}}), .out(multiplexer_13_out), .sel(flush));
  not not_1 (not_1_out, rst);
  Register register_1 (.D(multiplexer_1_out), .en(rst), .Q(wb_aluop), .clk(clk), .clr(not_1_out));
  Register #(.width(1)) register_2 (.D(multiplexer_2_out), .en(rst), .Q(wb_mreg), .clk(clk), .clr(not_1_out));
  Register #(.width(1)) register_3 (.D(multiplexer_3_out), .en(rst), .Q(wb_whilo), .clk(clk), .clr(not_1_out));
  Register #(.width(1)) register_4 (.D(multiplexer_4_out), .en(rst), .Q(wb_wreg), .clk(clk), .clr(not_1_out));
  Register #(.width(5)) register_5 (.D(multiplexer_5_out), .en(rst), .Q(wb_wa), .clk(clk), .clr(not_1_out));
  Register #(.width(32)) register_6 (.D(multiplexer_6_out), .en(rst), .Q(wb_hi), .clk(clk), .clr(not_1_out));
  Register #(.width(32)) register_7 (.D(multiplexer_7_out), .en(rst), .Q(wb_lo), .clk(clk), .clr(not_1_out));
  Register #(.width(32)) register_8 (.D(multiplexer_8_out), .en(rst), .Q(wb_dreg), .clk(clk), .clr(not_1_out));
  Register #(.width(4)) register_9 (.D(multiplexer_9_out), .en(rst), .Q(wb_dre), .clk(clk), .clr(not_1_out));
  Register #(.width(32)) register_10 (.D(multiplexer_10_out), .en(rst), .Q(wb_dm), .clk(clk), .clr(not_1_out));
  Register #(.width(1)) register_11 (.D(multiplexer_11_out), .en(rst), .Q(wb_cp0_we), .clk(clk), .clr(not_1_out));
  Register #(.width(5)) register_12 (.D(multiplexer_12_out), .en(rst), .Q(wb_cp0_waddr), .clk(clk), .clr(not_1_out));
  Register #(.width(32)) register_13 (.D(multiplexer_13_out), .en(rst), .Q(wb_cp0_wdata), .clk(clk), .clr(not_1_out));
endmodule

module wb (
  input  wb_mreg_i,
  input  wb_whilo_i,
  input  wb_wreg_i,
  input  [4:0] wb_wa_i,
  input  [31:0] wb_hi_i,
  input  [31:0] wb_lo_i,
  input  [31:0] wb_dreg_i,
  input  [3:0] wb_dre_i,
  input  [7:0] wb_aluop_i,
  input  [31:0] dm,
  input  cp0_we_i,
  input  [4:0] cp0_waddr_i,
  input  [31:0] cp0_wdata_i,
  input  clk,
  output wb2exe_whilo,
  output wb_whilo_o,
  output wb_wreg_o,
  output [4:0] wb_wa_o,
  output [31:0] wb_hi_o,
  output [31:0] wb_lo_o,
  output [31:0] wb2exe_hi,
  output [31:0] wb_wd_o,
  output [31:0] wb2exe_lo,
  output cp0_we_o,
  output [4:0] cp0_waddr_o,
  output [31:0] cp0_wdata_o
);

  wire comparator_1_eq, comparator_2_eq, comparator_3_eq, comparator_4_eq, comparator_5_eq, comparator_6_eq,
       equal8_1_eq, equal8_2_eq, equal8_3_eq, equal8_4_eq, equal8_5_eq, priority_encoder_1_gs,
       priority_encoder_2_gs, priority_encoder_2_out, priority_encoder_3_gs;
  wire [1:0] priority_encoder_1_out;
  wire [2:0] priority_encoder_3_out;
  wire [7:0] multiplexer_2_out;
  wire [15:0] multiplexer_1_out;
  wire [31:0] bit_extender_1_out, bit_extender_2_out, bit_extender_3_out, bit_extender_4_out,
       multiplexer_4_out;

  Comparator #(.width(4), .mode("unsigned")) comparator_1 (
    .a(4'b0001), .b(wb_dre_i), .eq(comparator_1_eq));  // open: gt, lt
  Comparator #(.width(4), .mode("unsigned")) comparator_2 (
    .a(4'b0010), .b(wb_dre_i), .eq(comparator_2_eq));  // open: gt, lt
  Comparator #(.width(4), .mode("unsigned")) comparator_3 (
    .a(4'b0100), .b(wb_dre_i), .eq(comparator_3_eq));  // open: gt, lt
  Comparator #(.width(4), .mode("unsigned")) comparator_4 (
    .a(4'b1000), .b(wb_dre_i), .eq(comparator_4_eq));  // open: gt, lt
  Comparator #(.width(4), .mode("unsigned")) comparator_5 (
    .a(4'b0011), .b(wb_dre_i), .eq(comparator_5_eq));  // open: gt, lt
  Comparator #(.width(4), .mode("unsigned")) comparator_6 (
    .a(4'b1100), .b(wb_dre_i), .eq(comparator_6_eq));  // open: gt, lt
  Priority_Encoder #(.select(2)) priority_encoder_1 (
    .in0(comparator_1_eq), .in1(comparator_2_eq), .in2(comparator_3_eq), .in3(comparator_4_eq),
    .out(priority_encoder_1_out), .gs(priority_encoder_1_gs));  // open: en_out, en_in
  Priority_Encoder #(.select(1)) priority_encoder_2 (
    .in0(comparator_5_eq), .in1(comparator_6_eq), .out(priority_encoder_2_out), .gs(priority_encoder_2_gs));  // open: en_out, en_in
  Multiplexer #(.width(16), .disabled(0)) multiplexer_1 (
    .in0(dm[15:0]), .in1(dm[31:16]), .out(multiplexer_1_out), .sel(priority_encoder_2_out),
    .en(priority_encoder_2_gs));
  Multiplexer #(.select(2), .width(8), .disabled(0)) multiplexer_2 (
    .in0(dm[7:0]), .in1(dm[15:8]), .in2(dm[23:16]), .in3(dm[31:24]), .out(multiplexer_2_out),
    .sel(priority_encoder_1_out), .en(priority_encoder_1_gs));
  Multiplexer #(.width(32), .enable("false")) multiplexer_3 (
    .in0(wb_dreg_i), .in1(multiplexer_4_out), .out(wb_wd_o), .sel(wb_mreg_i));
  Equal8 equal8_1 (.a(wb_aluop_i), .b(8'h90), .eq(equal8_1_eq));
  Equal8 equal8_2 (.a(wb_aluop_i), .b(8'h9b), .eq(equal8_2_eq));
  Equal8 equal8_3 (.a(wb_aluop_i), .b(8'h91), .eq(equal8_3_eq));
  Equal8 equal8_4 (.a(wb_aluop_i), .b(8'h9c), .eq(equal8_4_eq));
  Equal8 equal8_5 (.a(wb_aluop_i), .b(8'h92), .eq(equal8_5_eq));
  assign bit_extender_1_out = {{24{multiplexer_2_out[7]}}, multiplexer_2_out};  // Bit_Extender bit_extender_1
  assign bit_extender_2_out = {{24{1'b0}}, multiplexer_2_out};  // Bit_Extender bit_extender_2
  assign bit_extender_3_out = {{16{multiplexer_1_out[7]}}, {multiplexer_1_out[7:0], multiplexer_1_out[15:8]}};  // Bit_Extender bit_extender_3
  assign bit_extender_4_out = {{16{1'b0}}, {multiplexer_1_out[7:0], multiplexer_1_out[15:8]}};  // Bit_Extender bit_extender_4
  Priority_Encoder priority_encoder_3 (
    .in0(equal8_1_eq), .in1(equal8_2_eq), .in2(equal8_3_eq), .in3(equal8_4_eq), .in4(equal8_5_eq),
    .out(priority_encoder_3_out), .gs(priority_encoder_3_gs));  // open: in5, in6, in7, en_in, en_out
  Multiplexer #(.select(3), .width(32), .disabled(0)) multiplexer_4 (
    .in0(bit_extender_1_out), .in1(bit_extender_2_out), .in2(bit_extender_3_out), .in3(bit_extender_4_out),
    .in4({dm[7:0], dm[15:8], dm[23:16], dm[31:24]}), .out(multiplexer_4_out), .sel(priority_encoder_3_out),
    .en(priority_encoder_3_gs));  // open: in5, in6, in7

  assign cp0_waddr_o = cp0_waddr_i;
  assign cp0_wdata_o = cp0_wdata_i;
  assign cp0_we_o = cp0_we_i;
  assign wb2exe_hi = wb_hi_i;
  assign wb2exe_lo = wb_lo_i;
  assign wb2exe_whilo = wb_whilo_i;
  assign wb_hi_o = wb_hi_i;
  assign wb_lo_o = wb_lo_i;
  assign wb_wa_o = wb_wa_i;
  assign wb_whilo_o = wb_whilo_i;
  assign wb_wreg_o = wb_wreg_i;
endmodule

module DCU (
  input  equ,
  input  [5:0] op,
  input  [5:0] func,
  input  [4:0] rs,
  input  [4:0] rt,
  input  [4:0] exe2id_wa,
  input  [4:0] mem2id_wa,
  input  exe2id_wreg,
  input  mem2id_wreg,
  output [7:0] aluop,
  output [2:0] alutype,
  output rreg1,
  output rreg2,
  output whilo,
  output wreg,
  output immsel,
  output rtsel,
  output sext,
  output upper,
  output mreg,
  output shift,
  output jal,
  output [1:0] jtsel,
  output next_delay,
  output [4:0] exc_code,
  output [1:0] fwrd1,
  output [1:0] fwrd2
);

  wire comparator_1_eq, dcu_inst_b_1_inst_bgez, dcu_inst_b_1_inst_bgezal, dcu_inst_b_1_inst_bltz,
       dcu_inst_b_1_inst_bltzal, dcu_inst_exc_1_inst_eret, dcu_inst_exc_1_inst_mfc0,
       dcu_inst_exc_1_inst_mtc0, dcu_inst_exc_1_inst_syscall, dcu_inst_imm_1_inst_addi,
       dcu_inst_imm_1_inst_addiu, dcu_inst_imm_1_inst_andi, dcu_inst_imm_1_inst_beq,
       dcu_inst_imm_1_inst_bgtz, dcu_inst_imm_1_inst_blez, dcu_inst_imm_1_inst_bne, dcu_inst_imm_1_inst_j,
       dcu_inst_imm_1_inst_jal, dcu_inst_imm_1_inst_lb, dcu_inst_imm_1_inst_lbu, dcu_inst_imm_1_inst_lh,
       dcu_inst_imm_1_inst_lhu, dcu_inst_imm_1_inst_lui, dcu_inst_imm_1_inst_lw, dcu_inst_imm_1_inst_ori,
       dcu_inst_imm_1_inst_sb, dcu_inst_imm_1_inst_sh, dcu_inst_imm_1_inst_slti, dcu_inst_imm_1_inst_sltiu,
       dcu_inst_imm_1_inst_sw, dcu_inst_imm_1_inst_xori, dcu_inst_reg_1_inst_add, dcu_inst_reg_1_inst_addu,
       dcu_inst_reg_1_inst_and, dcu_inst_reg_1_inst_div, dcu_inst_reg_1_inst_divu, dcu_inst_reg_1_inst_jalr,
       dcu_inst_reg_1_inst_jr, dcu_inst_reg_1_inst_mfhi, dcu_inst_reg_1_inst_mflo, dcu_inst_reg_1_inst_mult,
       dcu_inst_reg_1_inst_multu, dcu_inst_reg_1_inst_nor, dcu_inst_reg_1_inst_or, dcu_inst_reg_1_inst_sll,
       dcu_inst_reg_1_inst_sll_2, dcu_inst_reg_1_inst_sll_3, dcu_inst_reg_1_inst_sllv,
       dcu_inst_reg_1_inst_slt, dcu_inst_reg_1_inst_sltu, dcu_inst_reg_1_inst_sra, dcu_inst_reg_1_inst_srav,
       dcu_inst_reg_1_inst_srl, dcu_inst_reg_1_inst_srlv, dcu_inst_reg_1_inst_sub, dcu_inst_reg_1_inst_subu,
       dcu_inst_reg_1_inst_xor, dcu_reg_1_wreg, nor_1_out;
  wire [4:0] dcu_exc_1_exc_code;

  nor nor_1 (nor_1_out, op[0], op[1], op[2], op[3], op[4], op[5]);
  DCU_inst_imm dcu_inst_imm_1 (
    .op0(op[0]), .op1(op[1]), .op2(op[2]), .op3(op[3]), .op4(op[4]), .op5(op[5]),
    .inst_addiu(dcu_inst_imm_1_inst_addiu), .inst_sltiu(dcu_inst_imm_1_inst_sltiu),
    .inst_ori(dcu_inst_imm_1_inst_ori), .inst_lui(dcu_inst_imm_1_inst_lui), .inst_lb(dcu_inst_imm_1_inst_lb),
    .inst_lw(dcu_inst_imm_1_inst_lw), .inst_sb(dcu_inst_imm_1_inst_sb), .inst_sw(dcu_inst_imm_1_inst_sw),
    .inst_j(dcu_inst_imm_1_inst_j), .inst_jal(dcu_inst_imm_1_inst_jal), .inst_beq(dcu_inst_imm_1_inst_beq),
    .inst_bne(dcu_inst_imm_1_inst_bne), .inst_addi(dcu_inst_imm_1_inst_addi),
    .inst_slti(dcu_inst_imm_1_inst_slti), .inst_andi(dcu_inst_imm_1_inst_andi),
    .inst_xori(dcu_inst_imm_1_inst_xori), .inst_lh(dcu_inst_imm_1_inst_lh), .inst_sh(dcu_inst_imm_1_inst_sh),
    .inst_lbu(dcu_inst_imm_1_inst_lbu), .inst_lhu(dcu_inst_imm_1_inst_lhu),
    .inst_blez(dcu_inst_imm_1_inst_blez), .inst_bgtz(dcu_inst_imm_1_inst_bgtz));
  DCU_inst_reg dcu_inst_reg_1 (
    .inst_reg(nor_1_out), .func0(func[0]), .func1(func[1]), .func2(func[2]), .func3(func[3]),
    .func4(func[4]), .func5(func[5]), .inst_add(dcu_inst_reg_1_inst_add),
    .inst_subu(dcu_inst_reg_1_inst_subu), .inst_slt(dcu_inst_reg_1_inst_slt),
    .inst_and(dcu_inst_reg_1_inst_and), .inst_mult(dcu_inst_reg_1_inst_mult),
    .inst_mfhi(dcu_inst_reg_1_inst_mfhi), .inst_mflo(dcu_inst_reg_1_inst_mflo),
    .inst_sll(dcu_inst_reg_1_inst_sll), .inst_jr(dcu_inst_reg_1_inst_jr), .inst_div(dcu_inst_reg_1_inst_div),
    .inst_addu(dcu_inst_reg_1_inst_addu), .inst_sub(dcu_inst_reg_1_inst_sub),
    .inst_sltu(dcu_inst_reg_1_inst_sltu), .inst_or(dcu_inst_reg_1_inst_or),
    .inst_xor(dcu_inst_reg_1_inst_xor), .inst_nor(dcu_inst_reg_1_inst_nor),
    .inst_multu(dcu_inst_reg_1_inst_multu), .inst_sra(dcu_inst_reg_1_inst_sra),
    .inst_sllv(dcu_inst_reg_1_inst_sllv), .inst_srlv(dcu_inst_reg_1_inst_srlv),
    .inst_srav(dcu_inst_reg_1_inst_srav), .inst_srl(dcu_inst_reg_1_inst_srl),
    .inst_sll_2(dcu_inst_reg_1_inst_sll_2), .inst_sll_3(dcu_inst_reg_1_inst_sll_3),
    .inst_jalr(dcu_inst_reg_1_inst_jalr), .inst_divu(dcu_inst_reg_1_inst_divu));
  DCU_inst_exc dcu_inst_exc_1 (
    .inst_reg(nor_1_out), .func(func), .op(op), .id_inst_23(rs[2]),
    .inst_syscall(dcu_inst_exc_1_inst_syscall), .inst_eret(dcu_inst_exc_1_inst_eret),
    .inst_mfc0(dcu_inst_exc_1_inst_mfc0), .inst_mtc0(dcu_inst_exc_1_inst_mtc0));
  DCU_inst_b dcu_inst_b_1 (
    .op(op), .rt(rt), .inst_bltz(dcu_inst_b_1_inst_bltz), .inst_bgez(dcu_inst_b_1_inst_bgez),
    .inst_bltzal(dcu_inst_b_1_inst_bltzal), .inst_bgezal(dcu_inst_b_1_inst_bgezal));
  DCU_fwrd dcu_fwrd_1 (
    .rreg1(rreg1), .rs(rs), .exe2id_wa(exe2id_wa), .mem2id_wa(mem2id_wa), .exe2id_wreg(exe2id_wreg),
    .mem2id_wreg(mem2id_wreg), .rt(rt), .rreg2(rreg2), .fwrd1(fwrd1), .fwrd2(fwrd2));
  DCU_aluop dcu_aluop_1 (
    .inst_add(dcu_inst_reg_1_inst_add), .inst_subu(dcu_inst_reg_1_inst_subu),
    .inst_slt(dcu_inst_reg_1_inst_slt), .inst_and(dcu_inst_reg_1_inst_and),
    .inst_mult(dcu_inst_reg_1_inst_mult), .inst_mfhi(dcu_inst_reg_1_inst_mfhi),
    .inst_mflo(dcu_inst_reg_1_inst_mflo), .inst_sll(dcu_inst_reg_1_inst_sll),
    .inst_addiu(dcu_inst_imm_1_inst_addiu), .inst_sltiu(dcu_inst_imm_1_inst_sltiu),
    .inst_ori(dcu_inst_imm_1_inst_ori), .inst_lui(dcu_inst_imm_1_inst_lui), .inst_lb(dcu_inst_imm_1_inst_lb),
    .inst_lw(dcu_inst_imm_1_inst_lw), .inst_sb(dcu_inst_imm_1_inst_sb), .inst_sw(dcu_inst_imm_1_inst_sw),
    .aluop0(aluop[0]), .aluop1(aluop[1]), .aluop2(aluop[2]), .aluop3(aluop[3]), .aluop4(aluop[4]),
    .aluop5(aluop[5]), .aluop6(aluop[6]), .aluop7(aluop[7]), .inst_j(dcu_inst_imm_1_inst_j),
    .inst_jal(dcu_inst_imm_1_inst_jal), .inst_jr(dcu_inst_reg_1_inst_jr), .inst_beq(dcu_inst_imm_1_inst_beq),
    .inst_bne(dcu_inst_imm_1_inst_bne), .inst_div(dcu_inst_reg_1_inst_div),
    .inst_syscall(dcu_inst_exc_1_inst_syscall), .inst_eret(dcu_inst_exc_1_inst_eret),
    .inst_mfc0(dcu_inst_exc_1_inst_mfc0), .inst_mtc0(dcu_inst_exc_1_inst_mtc0),
    .inst_addi(dcu_inst_imm_1_inst_addi), .inst_addu(dcu_inst_reg_1_inst_addu),
    .inst_sub(dcu_inst_reg_1_inst_sub), .inst_slti(dcu_inst_imm_1_inst_slti),
    .inst_sltu(dcu_inst_reg_1_inst_sltu), .inst_andi(dcu_inst_imm_1_inst_andi),
    .inst_or(dcu_inst_reg_1_inst_or), .inst_xor(dcu_inst_reg_1_inst_xor),
    .inst_xori(dcu_inst_imm_1_inst_xori), .inst_nor(dcu_inst_reg_1_inst_nor),
    .inst_multu(dcu_inst_reg_1_inst_multu), .inst_srl(dcu_inst_reg_1_inst_srl),
    .inst_sra(dcu_inst_reg_1_inst_sra), .inst_sllv(dcu_inst_reg_1_inst_sllv),
    .inst_srlv(dcu_inst_reg_1_inst_srlv), .inst_srav(dcu_inst_reg_1_inst_srav),
    .inst_mthi(dcu_inst_reg_1_inst_sll_2), .inst_mtlo(dcu_inst_reg_1_inst_sll_3),
    .inst_lh(dcu_inst_imm_1_inst_lh), .inst_sh(dcu_inst_imm_1_inst_sh), .inst_lbu(dcu_inst_imm_1_inst_lbu),
    .inst_lhu(dcu_inst_imm_1_inst_lhu), .inst_blez(dcu_inst_imm_1_inst_blez),
    .inst_bgtz(dcu_inst_imm_1_inst_bgtz), .inst_bltz(dcu_inst_b_1_inst_bltz),
    .inst_bgez(dcu_inst_b_1_inst_bgez), .inst_bltzal(dcu_inst_b_1_inst_bltzal),
    .inst_bgezal(dcu_inst_b_1_inst_bgezal), .inst_jalr(dcu_inst_reg_1_inst_jalr),
    .inst_divu(dcu_inst_reg_1_inst_divu));
  DCU_alutype dcu_alutype_1 (
    .alutype0(alutype[0]), .alutype1(alutype[1]), .alutype2(alutype[2]), .inst_add(dcu_inst_reg_1_inst_add),
    .inst_subu(dcu_inst_reg_1_inst_subu), .inst_slt(dcu_inst_reg_1_inst_slt),
    .inst_and(dcu_inst_reg_1_inst_and), .inst_mult(dcu_inst_reg_1_inst_mult),
    .inst_mfhi(dcu_inst_reg_1_inst_mfhi), .inst_mflo(dcu_inst_reg_1_inst_mflo),
    .inst_sll(dcu_inst_reg_1_inst_sll), .inst_addiu(dcu_inst_imm_1_inst_addiu),
    .inst_sltiu(dcu_inst_imm_1_inst_sltiu), .inst_ori(dcu_inst_imm_1_inst_ori),
    .inst_lui(dcu_inst_imm_1_inst_lui), .inst_lb(dcu_inst_imm_1_inst_lb), .inst_lw(dcu_inst_imm_1_inst_lw),
    .inst_sb(dcu_inst_imm_1_inst_sb), .inst_sw(dcu_inst_imm_1_inst_sw), .inst_j(dcu_inst_imm_1_inst_j),
    .inst_jal(dcu_inst_imm_1_inst_jal), .inst_jr(dcu_inst_reg_1_inst_jr), .inst_beq(dcu_inst_imm_1_inst_beq),
    .inst_bne(dcu_inst_imm_1_inst_bne), .inst_div(dcu_inst_reg_1_inst_div),
    .inst_syscall(dcu_inst_exc_1_inst_syscall), .inst_eret(dcu_inst_exc_1_inst_eret),
    .inst_mfc0(dcu_inst_exc_1_inst_mfc0), .inst_mtc0(dcu_inst_exc_1_inst_mtc0),
    .inst_addi(dcu_inst_imm_1_inst_addi), .inst_addu(dcu_inst_reg_1_inst_addu),
    .inst_sub(dcu_inst_reg_1_inst_sub), .inst_slti(dcu_inst_imm_1_inst_slti),
    .inst_sltu(dcu_inst_reg_1_inst_sltu), .inst_andi(dcu_inst_imm_1_inst_andi),
    .inst_or(dcu_inst_reg_1_inst_or), .inst_xor(dcu_inst_reg_1_inst_xor),
    .inst_xori(dcu_inst_imm_1_inst_xori), .inst_nor(dcu_inst_reg_1_inst_nor),
    .inst_multu(dcu_inst_reg_1_inst_multu), .inst_srl(dcu_inst_reg_1_inst_srl),
    .inst_sra(dcu_inst_reg_1_inst_sra), .inst_sllv(dcu_inst_reg_1_inst_sllv),
    .inst_srlv(dcu_inst_reg_1_inst_srlv), .inst_srav(dcu_inst_reg_1_inst_srav),
    .inst_mthi(dcu_inst_reg_1_inst_sll_2), .inst_mtlo(dcu_inst_reg_1_inst_sll_3),
    .inst_lh(dcu_inst_imm_1_inst_lh), .inst_sh(dcu_inst_imm_1_inst_sh), .inst_lbu(dcu_inst_imm_1_inst_lbu),
    .inst_lhu(dcu_inst_imm_1_inst_lhu), .inst_blez(dcu_inst_imm_1_inst_blez),
    .inst_bgtz(dcu_inst_imm_1_inst_bgtz), .inst_bltz(dcu_inst_b_1_inst_bltz),
    .inst_bgez(dcu_inst_b_1_inst_bgez), .inst_bltzal(dcu_inst_b_1_inst_bltzal),
    .inst_bgezal(dcu_inst_b_1_inst_bgezal), .inst_jalr(dcu_inst_reg_1_inst_jalr),
    .inst_divu(dcu_inst_reg_1_inst_divu));
  DCU_reg dcu_reg_1 (
    .rreg1(rreg1), .rreg2(rreg2), .wreg(dcu_reg_1_wreg), .whilo(whilo), .inst_add(dcu_inst_reg_1_inst_add),
    .inst_subu(dcu_inst_reg_1_inst_subu), .inst_slt(dcu_inst_reg_1_inst_slt),
    .inst_and(dcu_inst_reg_1_inst_and), .inst_mult(dcu_inst_reg_1_inst_mult),
    .inst_mfhi(dcu_inst_reg_1_inst_mfhi), .inst_mflo(dcu_inst_reg_1_inst_mflo),
    .inst_sll(dcu_inst_reg_1_inst_sll), .inst_addiu(dcu_inst_imm_1_inst_addiu),
    .inst_sltiu(dcu_inst_imm_1_inst_sltiu), .inst_ori(dcu_inst_imm_1_inst_ori),
    .inst_lui(dcu_inst_imm_1_inst_lui), .inst_lb(dcu_inst_imm_1_inst_lb), .inst_lw(dcu_inst_imm_1_inst_lw),
    .inst_sb(dcu_inst_imm_1_inst_sb), .inst_sw(dcu_inst_imm_1_inst_sw), .inst_j(dcu_inst_imm_1_inst_j),
    .inst_jal(dcu_inst_imm_1_inst_jal), .inst_jr(dcu_inst_reg_1_inst_jr), .inst_beq(dcu_inst_imm_1_inst_beq),
    .inst_bne(dcu_inst_imm_1_inst_bne), .inst_div(dcu_inst_reg_1_inst_div),
    .inst_syscall(dcu_inst_exc_1_inst_syscall), .inst_eret(dcu_inst_exc_1_inst_eret),
    .inst_mfc0(dcu_inst_exc_1_inst_mfc0), .inst_mtc0(dcu_inst_exc_1_inst_mtc0),
    .inst_addi(dcu_inst_imm_1_inst_addi), .inst_addu(dcu_inst_reg_1_inst_addu),
    .inst_sub(dcu_inst_reg_1_inst_sub), .inst_slti(dcu_inst_imm_1_inst_slti),
    .inst_sltu(dcu_inst_reg_1_inst_sltu), .inst_andi(dcu_inst_imm_1_inst_andi),
    .inst_or(dcu_inst_reg_1_inst_or), .inst_xor(dcu_inst_reg_1_inst_xor),
    .inst_xori(dcu_inst_imm_1_inst_xori), .inst_nor(dcu_inst_reg_1_inst_nor),
    .inst_multu(dcu_inst_reg_1_inst_multu), .inst_srl(dcu_inst_reg_1_inst_srl),
    .inst_sra(dcu_inst_reg_1_inst_sra), .inst_sllv(dcu_inst_reg_1_inst_sllv),
    .inst_srlv(dcu_inst_reg_1_inst_srlv), .inst_srav(dcu_inst_reg_1_inst_srav),
    .inst_mthi(dcu_inst_reg_1_inst_sll_2), .inst_mtlo(dcu_inst_reg_1_inst_sll_3),
    .inst_lh(dcu_inst_imm_1_inst_lh), .inst_sh(dcu_inst_imm_1_inst_sh), .inst_lbu(dcu_inst_imm_1_inst_lbu),
    .inst_lhu(dcu_inst_imm_1_inst_lhu), .inst_blez(dcu_inst_imm_1_inst_blez),
    .inst_bgtz(dcu_inst_imm_1_inst_bgtz), .inst_bltz(dcu_inst_b_1_inst_bltz),
    .inst_bgez(dcu_inst_b_1_inst_bgez), .inst_bltzal(dcu_inst_b_1_inst_bltzal),
    .inst_bgezal(dcu_inst_b_1_inst_bgezal), .inst_jalr(dcu_inst_reg_1_inst_jalr),
    .inst_divu(dcu_inst_reg_1_inst_divu));
  DCU_other dcu_other_1 (
    .immsel(immsel), .rtsel(rtsel), .sext(sext), .upper(upper), .mreg(mreg), .shift(shift),
    .inst_add(dcu_inst_reg_1_inst_add), .inst_subu(dcu_inst_reg_1_inst_subu),
    .inst_slt(dcu_inst_reg_1_inst_slt), .inst_and(dcu_inst_reg_1_inst_and),
    .inst_mult(dcu_inst_reg_1_inst_mult), .inst_mfhi(dcu_inst_reg_1_inst_mfhi),
    .inst_mflo(dcu_inst_reg_1_inst_mflo), .inst_sll(dcu_inst_reg_1_inst_sll),
    .inst_addiu(dcu_inst_imm_1_inst_addiu), .inst_sltiu(dcu_inst_imm_1_inst_sltiu),
    .inst_ori(dcu_inst_imm_1_inst_ori), .inst_lui(dcu_inst_imm_1_inst_lui), .inst_lb(dcu_inst_imm_1_inst_lb),
    .inst_lw(dcu_inst_imm_1_inst_lw), .inst_sb(dcu_inst_imm_1_inst_sb), .inst_sw(dcu_inst_imm_1_inst_sw),
    .inst_j(dcu_inst_imm_1_inst_j), .inst_jal(dcu_inst_imm_1_inst_jal), .inst_jr(dcu_inst_reg_1_inst_jr),
    .inst_beq(dcu_inst_imm_1_inst_beq), .inst_bne(dcu_inst_imm_1_inst_bne),
    .inst_div(dcu_inst_reg_1_inst_div), .inst_syscall(dcu_inst_exc_1_inst_syscall),
    .inst_eret(dcu_inst_exc_1_inst_eret), .inst_mfc0(dcu_inst_exc_1_inst_mfc0),
    .inst_mtc0(dcu_inst_exc_1_inst_mtc0), .inst_addi(dcu_inst_imm_1_inst_addi),
    .inst_addu(dcu_inst_reg_1_inst_addu), .inst_sub(dcu_inst_reg_1_inst_sub),
    .inst_slti(dcu_inst_imm_1_inst_slti), .inst_sltu(dcu_inst_reg_1_inst_sltu),
    .inst_andi(dcu_inst_imm_1_inst_andi), .inst_or(dcu_inst_reg_1_inst_or),
    .inst_xor(dcu_inst_reg_1_inst_xor), .inst_xori(dcu_inst_imm_1_inst_xori),
    .inst_nor(dcu_inst_reg_1_inst_nor), .inst_multu(dcu_inst_reg_1_inst_multu),
    .inst_srl(dcu_inst_reg_1_inst_srl), .inst_sra(dcu_inst_reg_1_inst_sra),
    .inst_sllv(dcu_inst_reg_1_inst_sllv), .inst_srlv(dcu_inst_reg_1_inst_srlv),
    .inst_srav(dcu_inst_reg_1_inst_srav), .inst_mthi(dcu_inst_reg_1_inst_sll_2),
    .inst_mtlo(dcu_inst_reg_1_inst_sll_3), .inst_lh(dcu_inst_imm_1_inst_lh),
    .inst_sh(dcu_inst_imm_1_inst_sh), .inst_lbu(dcu_inst_imm_1_inst_lbu), .inst_lhu(dcu_inst_imm_1_inst_lhu),
    .inst_blez(dcu_inst_imm_1_inst_blez), .inst_bgtz(dcu_inst_imm_1_inst_bgtz),
    .inst_bltz(dcu_inst_b_1_inst_bltz), .inst_bgez(dcu_inst_b_1_inst_bgez),
    .inst_bltzal(dcu_inst_b_1_inst_bltzal), .inst_bgezal(dcu_inst_b_1_inst_bgezal),
    .inst_jalr(dcu_inst_reg_1_inst_jalr), .inst_divu(dcu_inst_reg_1_inst_divu));
  DCU_jump dcu_jump_1 (
    .inst_j(dcu_inst_imm_1_inst_j), .inst_jal(dcu_inst_imm_1_inst_jal), .inst_jr(dcu_inst_reg_1_inst_jr),
    .inst_beq(dcu_inst_imm_1_inst_beq), .inst_bne(dcu_inst_imm_1_inst_bne), .equ(dcu_inst_reg_1_inst_jalr),
    .jal(jal), .jtsel1(jtsel[1]), .jtsel0(jtsel[0]), .inst_blez(dcu_inst_imm_1_inst_blez),
    .inst_bgtz(dcu_inst_imm_1_inst_bgtz), .inst_bltz(dcu_inst_b_1_inst_bltz),
    .inst_bgez(dcu_inst_b_1_inst_bgez), .inst_bltzal(dcu_inst_b_1_inst_bltzal),
    .inst_bgezal(dcu_inst_b_1_inst_bgezal), .inst_jalr(equ));
  DCU_exc dcu_exc_1 (
    .inst_j(dcu_inst_imm_1_inst_j), .inst_jal(dcu_inst_imm_1_inst_jal), .inst_jr(dcu_inst_reg_1_inst_jr),
    .inst_beq(dcu_inst_imm_1_inst_beq), .inst_bne(dcu_inst_imm_1_inst_bne),
    .inst_syscall(dcu_inst_exc_1_inst_syscall), .inst_eret(dcu_inst_exc_1_inst_eret),
    .inst_mfc0(dcu_inst_exc_1_inst_mfc0), .inst_mtc0(dcu_inst_exc_1_inst_mtc0), .next_delay(next_delay),
    .exc_code(dcu_exc_1_exc_code), .inst_blez(dcu_inst_imm_1_inst_blez),
    .inst_bgtz(dcu_inst_imm_1_inst_bgtz), .inst_bltz(dcu_inst_b_1_inst_bltz),
    .inst_bgez(dcu_inst_b_1_inst_bgez), .inst_bltzal(dcu_inst_b_1_inst_bltzal),
    .inst_bgezal(dcu_inst_b_1_inst_bgezal), .inst_jalr(dcu_inst_reg_1_inst_jalr));
  Comparator #(.mode("unsigned")) comparator_1 (.a({8{1'b0}}), .b(aluop), .eq(comparator_1_eq));  // open: gt, lt
  Multiplexer #(.width(5), .disabled(0), .enable("false")) multiplexer_1 (
    .in0(dcu_exc_1_exc_code), .in1(5'b01010), .out(exc_code), .sel(comparator_1_eq));
  Multiplexer #(.enable("false")) multiplexer_2 (.in0(dcu_reg_1_wreg), .in1(1'b1), .out(wreg), .sel(jal));
endmodule

module DCU_inst_reg (
  input  inst_reg,
  input  func0,
  input  func1,
  input  func2,
  input  func3,
  input  func4,
  input  func5,
  output inst_add,
  output inst_subu,
  output inst_slt,
  output inst_and,
  output inst_mult,
  output inst_mfhi,
  output inst_mflo,
  output inst_sll,
  output inst_jr,
  output inst_div,
  output inst_addu,
  output inst_sub,
  output inst_sltu,
  output inst_or,
  output inst_xor,
  output inst_nor,
  output inst_multu,
  output inst_srl,
  output inst_sra,
  output inst_sllv,
  output inst_srlv,
  output inst_srav,
  output inst_sll_2,
  output inst_sll_3,
  output inst_jalr,
  output inst_divu
);

  wire not_1_out, not_2_out, not_3_out, not_4_out, not_5_out, not_6_out, not_7_out, not_8_out, not_9_out,
       not_10_out, not_11_out, not_12_out, not_13_out, not_14_out, not_15_out, not_16_out, not_17_out,
       not_18_out, not_19_out, not_20_out, not_21_out, not_22_out, not_23_out, not_24_out, not_25_out,
       not_26_out, not_27_out, not_28_out, not_29_out, not_30_out, not_31_out, not_32_out, not_33_out,
       not_34_out, not_35_out, not_36_out, not_37_out, not_38_out, not_39_out, not_40_out, not_41_out,
       not_42_out, not_43_out, not_44_out, not_45_out, not_46_out, not_47_out, not_48_out, not_49_out,
       not_50_out, not_51_out, not_52_out, not_53_out, not_54_out, not_55_out, not_56_out, not_57_out,
       not_58_out, not_59_out, not_60_out, not_61_out, not_62_out, not_63_out, not_64_out, not_65_out,
       not_66_out, not_67_out, not_68_out, not_69_out, not_70_out, not_71_out, not_72_out, not_73_out,
       not_74_out, not_75_out, not_76_out, not_77_out, not_78_out, not_79_out, not_80_out, not_81_out,
       not_82_out, not_83_out, not_84_out, not_85_out, not_86_out, not_87_out, not_88_out, not_89_out,
       not_90_out, not_91_out, not_92_out, not_93_out, not_94_out, not_95_out, not_96_out, not_97_out;

  not not_1 (not_1_out, func4);
  not not_2 (not_2_out, func3);
  not not_3 (not_3_out, func2);
  not not_4 (not_4_out, func1);
  not not_5 (not_5_out, func0);
  not not_6 (not_6_out, func4);
  not not_7 (not_7_out, func3);
  not not_8 (not_8_out, func2);
  not not_9 (not_9_out, func4);
  not not_10 (not_10_out, func2);
  not not_11 (not_11_out, func0);
  not not_12 (not_12_out, func4);
  not not_13 (not_13_out, func3);
  not not_14 (not_14_out, func1);
  not not_15 (not_15_out, func0);
  not not_16 (not_16_out, func5);
  not not_17 (not_17_out, func2);
  not not_18 (not_18_out, func1);
  not not_19 (not_19_out, func0);
  not not_20 (not_20_out, func5);
  not not_21 (not_21_out, func3);
  not not_22 (not_22_out, func2);
  not not_23 (not_23_out, func1);
  not not_24 (not_24_out, func0);
  not not_25 (not_25_out, func5);
  not not_26 (not_26_out, func3);
  not not_27 (not_27_out, func2);
  not not_28 (not_28_out, func0);
  not not_29 (not_29_out, func5);
  not not_30 (not_30_out, func4);
  not not_31 (not_31_out, func3);
  not not_32 (not_32_out, func2);
  not not_33 (not_33_out, func1);
  not not_34 (not_34_out, func0);
  not not_35 (not_35_out, func5);
  not not_36 (not_36_out, func4);
  not not_37 (not_37_out, func2);
  not not_38 (not_38_out, func1);
  not not_39 (not_39_out, func0);
  not not_40 (not_40_out, func5);
  not not_41 (not_41_out, func2);
  not not_42 (not_42_out, func0);
  not not_43 (not_43_out, func4);
  not not_44 (not_44_out, func3);
  not not_45 (not_45_out, func2);
  not not_46 (not_46_out, func1);
  not not_47 (not_47_out, func4);
  not not_48 (not_48_out, func3);
  not not_49 (not_49_out, func2);
  not not_50 (not_50_out, func0);
  not not_51 (not_51_out, func4);
  not not_52 (not_52_out, func2);
  not not_53 (not_53_out, func4);
  not not_54 (not_54_out, func3);
  not not_55 (not_55_out, func1);
  not not_56 (not_56_out, func4);
  not not_57 (not_57_out, func3);
  not not_58 (not_58_out, func0);
  not not_59 (not_59_out, func4);
  not not_60 (not_60_out, func3);
  not not_61 (not_61_out, func5);
  not not_62 (not_62_out, func2);
  not not_63 (not_63_out, func1);
  not not_64 (not_64_out, func5);
  not not_65 (not_65_out, func4);
  not not_66 (not_66_out, func3);
  not not_67 (not_67_out, func2);
  not not_68 (not_68_out, func0);
  not not_69 (not_69_out, func5);
  not not_70 (not_70_out, func4);
  not not_71 (not_71_out, func3);
  not not_72 (not_72_out, func2);
  not not_73 (not_73_out, func5);
  not not_74 (not_74_out, func4);
  not not_75 (not_75_out, func3);
  not not_76 (not_76_out, func1);
  not not_77 (not_77_out, func0);
  not not_78 (not_78_out, func5);
  not not_79 (not_79_out, func4);
  not not_80 (not_80_out, func3);
  not not_81 (not_81_out, func0);
  not not_82 (not_82_out, func5);
  not not_83 (not_83_out, func4);
  not not_84 (not_84_out, func3);
  not not_85 (not_85_out, func5);
  not not_86 (not_86_out, func3);
  not not_87 (not_87_out, func2);
  not not_88 (not_88_out, func1);
  not not_89 (not_89_out, func5);
  not not_90 (not_90_out, func3);
  not not_91 (not_91_out, func2);
  not not_92 (not_92_out, func5);
  not not_93 (not_93_out, func4);
  not not_94 (not_94_out, func2);
  not not_95 (not_95_out, func1);
  not not_96 (not_96_out, func5);
  not not_97 (not_97_out, func2);
  and and_1 (inst_add, inst_reg, func5, not_1_out, not_2_out, not_3_out, not_4_out, not_5_out);
  and and_2 (inst_subu, inst_reg, func5, not_6_out, not_7_out, not_8_out, func1, func0);
  and and_3 (inst_slt, inst_reg, func5, not_9_out, func3, not_10_out, func1, not_11_out);
  and and_4 (inst_and, inst_reg, func5, not_12_out, not_13_out, func2, not_14_out, not_15_out);
  and and_5 (inst_mult, inst_reg, not_16_out, func4, func3, not_17_out, not_18_out, not_19_out);
  and and_6 (inst_mfhi, inst_reg, not_20_out, func4, not_21_out, not_22_out, not_23_out, not_24_out);
  and and_7 (inst_mflo, inst_reg, not_25_out, func4, not_26_out, not_27_out, func1, not_28_out);
  and and_8 (inst_sll, inst_reg, not_29_out, not_30_out, not_31_out, not_32_out, not_33_out, not_34_out);
  and and_9 (inst_jr, inst_reg, not_35_out, not_36_out, func3, not_37_out, not_38_out, not_39_out);
  and and_10 (inst_div, inst_reg, not_40_out, func4, func3, not_41_out, func1, not_42_out);
  and and_11 (inst_addu, inst_reg, func5, not_43_out, not_44_out, not_45_out, not_46_out, func0);
  and and_12 (inst_sub, inst_reg, func5, not_47_out, not_48_out, not_49_out, func1, not_50_out);
  and and_13 (inst_sltu, inst_reg, func5, not_51_out, func3, not_52_out, func1, func0);
  and and_14 (inst_or, inst_reg, func5, not_53_out, not_54_out, func2, not_55_out, func0);
  and and_15 (inst_xor, inst_reg, func5, not_56_out, not_57_out, func2, func1, not_58_out);
  and and_16 (inst_nor, inst_reg, func5, not_59_out, not_60_out, func2, func1, func0);
  and and_17 (inst_multu, inst_reg, not_61_out, func4, func3, not_62_out, not_63_out, func0);
  and and_18 (inst_srl, inst_reg, not_64_out, not_65_out, not_66_out, not_67_out, func1, not_68_out);
  and and_19 (inst_sra, inst_reg, not_69_out, not_70_out, not_71_out, not_72_out, func1, func0);
  and and_20 (inst_sllv, inst_reg, not_73_out, not_74_out, not_75_out, func2, not_76_out, not_77_out);
  and and_21 (inst_srlv, inst_reg, not_78_out, not_79_out, not_80_out, func2, func1, not_81_out);
  and and_22 (inst_srav, inst_reg, not_82_out, not_83_out, not_84_out, func2, func1, func0);
  and and_23 (inst_sll_2, inst_reg, not_85_out, func4, not_86_out, not_87_out, not_88_out, func0);
  and and_24 (inst_sll_3, inst_reg, not_89_out, func4, not_90_out, not_91_out, func1, func0);
  and and_25 (inst_jalr, inst_reg, not_92_out, not_93_out, func3, not_94_out, not_95_out, func0);
  and and_26 (inst_divu, inst_reg, not_96_out, func4, func3, not_97_out, func1, func0);

  // Notes on the sheet:
  //   reg
  //   0
  //   0
  //   4
  //   3
  //   2
  //   1
  //   4
  //   3
  //   2
  //   1
  //   5
  //   5
endmodule

module DCU_inst_imm (
  input  op0,
  input  op1,
  input  op2,
  input  op3,
  input  op4,
  input  op5,
  output inst_addiu,
  output inst_sltiu,
  output inst_ori,
  output inst_lui,
  output inst_lb,
  output inst_lw,
  output inst_sb,
  output inst_sw,
  output inst_j,
  output inst_jal,
  output inst_beq,
  output inst_bne,
  output inst_addi,
  output inst_slti,
  output inst_andi,
  output inst_xori,
  output inst_lh,
  output inst_sh,
  output inst_lbu,
  output inst_lhu,
  output inst_blez,
  output inst_bgtz
);

  wire not_1_out, not_2_out, not_3_out, not_4_out, not_5_out, not_6_out, not_7_out, not_8_out, not_9_out,
       not_10_out, not_11_out, not_12_out, not_13_out, not_14_out, not_15_out, not_16_out, not_17_out,
       not_18_out, not_19_out, not_20_out, not_21_out, not_22_out, not_23_out, not_24_out, not_25_out,
       not_26_out, not_27_out, not_28_out, not_29_out, not_30_out, not_31_out, not_32_out, not_33_out,
       not_34_out, not_35_out, not_36_out, not_37_out, not_38_out, not_39_out, not_40_out, not_41_out,
       not_42_out, not_43_out, not_44_out, not_45_out, not_46_out, not_47_out, not_48_out, not_49_out,
       not_50_out, not_51_out, not_52_out, not_53_out, not_54_out, not_55_out, not_56_out, not_57_out,
       not_58_out, not_59_out, not_60_out, not_61_out, not_62_out, not_63_out, not_64_out, not_65_out,
       not_66_out, not_67_out, not_68_out, not_69_out, not_70_out, not_71_out, not_72_out, not_73_out,
       not_74_out, not_75_out, not_76_out, not_77_out, not_78_out, not_79_out, not_80_out, not_81_out;

  not not_1 (not_1_out, op5);
  not not_2 (not_2_out, op4);
  not not_3 (not_3_out, op2);
  not not_4 (not_4_out, op1);
  not not_5 (not_5_out, op5);
  not not_6 (not_6_out, op4);
  not not_7 (not_7_out, op2);
  not not_8 (not_8_out, op5);
  not not_9 (not_9_out, op4);
  not not_10 (not_10_out, op1);
  not not_11 (not_11_out, op5);
  not not_12 (not_12_out, op4);
  not not_13 (not_13_out, op4);
  not not_14 (not_14_out, op3);
  not not_15 (not_15_out, op2);
  not not_16 (not_16_out, op1);
  not not_17 (not_17_out, op0);
  not not_18 (not_18_out, op4);
  not not_19 (not_19_out, op3);
  not not_20 (not_20_out, op2);
  not not_21 (not_21_out, op4);
  not not_22 (not_22_out, op2);
  not not_23 (not_23_out, op1);
  not not_24 (not_24_out, op0);
  not not_25 (not_25_out, op4);
  not not_26 (not_26_out, op2);
  not not_27 (not_27_out, op5);
  not not_28 (not_28_out, op4);
  not not_29 (not_29_out, op3);
  not not_30 (not_30_out, op2);
  not not_31 (not_31_out, op0);
  not not_32 (not_32_out, op5);
  not not_33 (not_33_out, op4);
  not not_34 (not_34_out, op3);
  not not_35 (not_35_out, op2);
  not not_36 (not_36_out, op5);
  not not_37 (not_37_out, op4);
  not not_38 (not_38_out, op3);
  not not_39 (not_39_out, op1);
  not not_40 (not_40_out, op0);
  not not_41 (not_41_out, op5);
  not not_42 (not_42_out, op4);
  not not_43 (not_43_out, op3);
  not not_44 (not_44_out, op1);
  not not_45 (not_45_out, op5);
  not not_46 (not_46_out, op4);
  not not_47 (not_47_out, op2);
  not not_48 (not_48_out, op1);
  not not_49 (not_49_out, op0);
  not not_50 (not_50_out, op5);
  not not_51 (not_51_out, op4);
  not not_52 (not_52_out, op2);
  not not_53 (not_53_out, op0);
  not not_54 (not_54_out, op5);
  not not_55 (not_55_out, op4);
  not not_56 (not_56_out, op1);
  not not_57 (not_57_out, op0);
  not not_58 (not_58_out, op5);
  not not_59 (not_59_out, op4);
  not not_60 (not_60_out, op0);
  not not_61 (not_61_out, op4);
  not not_62 (not_62_out, op3);
  not not_63 (not_63_out, op2);
  not not_64 (not_64_out, op1);
  not not_65 (not_65_out, op4);
  not not_66 (not_66_out, op2);
  not not_67 (not_67_out, op1);
  not not_68 (not_68_out, op4);
  not not_69 (not_69_out, op3);
  not not_70 (not_70_out, op1);
  not not_71 (not_71_out, op0);
  not not_72 (not_72_out, op4);
  not not_73 (not_73_out, op3);
  not not_74 (not_74_out, op1);
  not not_75 (not_75_out, op5);
  not not_76 (not_76_out, op4);
  not not_77 (not_77_out, op3);
  not not_78 (not_78_out, op0);
  not not_79 (not_79_out, op5);
  not not_80 (not_80_out, op4);
  not not_81 (not_81_out, op3);
  and and_1 (inst_addiu, not_1_out, not_2_out, op3, not_3_out, not_4_out, op0);
  and and_2 (inst_sltiu, not_5_out, not_6_out, op3, not_7_out, op1, op0);
  and and_3 (inst_ori, not_8_out, not_9_out, op3, op2, not_10_out, op0);
  and and_4 (inst_lui, not_11_out, not_12_out, op3, op2, op1, op0);
  and and_5 (inst_lb, op5, not_13_out, not_14_out, not_15_out, not_16_out, not_17_out);
  and and_6 (inst_lw, op5, not_18_out, not_19_out, not_20_out, op1, op0);
  and and_7 (inst_sb, op5, not_21_out, op3, not_22_out, not_23_out, not_24_out);
  and and_8 (inst_sw, op5, not_25_out, op3, not_26_out, op1, op0);
  and and_9 (inst_j, not_27_out, not_28_out, not_29_out, not_30_out, op1, not_31_out);
  and and_10 (inst_jal, not_32_out, not_33_out, not_34_out, not_35_out, op1, op0);
  and and_11 (inst_beq, not_36_out, not_37_out, not_38_out, op2, not_39_out, not_40_out);
  and and_12 (inst_bne, not_41_out, not_42_out, not_43_out, op2, not_44_out, op0);
  and and_13 (inst_addi, not_45_out, not_46_out, op3, not_47_out, not_48_out, not_49_out);
  and and_14 (inst_slti, not_50_out, not_51_out, op3, not_52_out, op1, not_53_out);
  and and_15 (inst_andi, not_54_out, not_55_out, op3, op2, not_56_out, not_57_out);
  and and_16 (inst_xori, not_58_out, not_59_out, op3, op2, op1, not_60_out);
  and and_17 (inst_lh, op5, not_61_out, not_62_out, not_63_out, not_64_out, op0);
  and and_18 (inst_sh, op5, not_65_out, op3, not_66_out, not_67_out, op0);
  and and_19 (inst_lbu, op5, not_68_out, not_69_out, op2, not_70_out, not_71_out);
  and and_20 (inst_lhu, op5, not_72_out, not_73_out, op2, not_74_out, op0);
  and and_21 (inst_blez, not_75_out, not_76_out, not_77_out, op2, op1, not_78_out);
  and and_22 (inst_bgtz, not_79_out, not_80_out, not_81_out, op2, op1, op0);
  // AND_Gate and_23 is placed but not wired
endmodule

module DCU_inst_exc (
  input  inst_reg,
  input  [5:0] func,
  input  [5:0] op,
  input  id_inst_23,
  output inst_syscall,
  output inst_eret,
  output inst_mfc0,
  output inst_mtc0
);

  wire comparator_1_eq, comparator_2_eq, comparator_3_eq, comparator_4_eq, not_1_out;

  Comparator #(.width(6), .mode("unsigned")) comparator_1 (
    .a(6'b001100), .b(func), .eq(comparator_1_eq));  // open: gt, lt
  Comparator #(.width(6), .mode("unsigned")) comparator_2 (
    .a(6'b011000), .b(func), .eq(comparator_2_eq));  // open: gt, lt
  Comparator #(.width(6), .mode("unsigned")) comparator_3 (
    .a(6'b010000), .b(op), .eq(comparator_3_eq));  // open: gt, lt
  Comparator #(.width(6), .mode("unsigned")) comparator_4 (
    .a({6{1'b0}}), .b(func), .eq(comparator_4_eq));  // open: gt, lt
  and and_1 (inst_syscall, inst_reg, comparator_1_eq);
  not not_1 (not_1_out, id_inst_23);
  and and_2 (inst_eret, comparator_2_eq, comparator_3_eq);
  and and_3 (inst_mfc0, comparator_3_eq, comparator_4_eq, not_1_out);
  and and_4 (inst_mtc0, comparator_3_eq, comparator_4_eq, id_inst_23);
endmodule

module DCU_inst_b (
  input  [5:0] op,
  input  [4:0] rt,
  output inst_bltz,
  output inst_bgez,
  output inst_bltzal,
  output inst_bgezal
);

  wire comparator_1_eq, comparator_2_eq, comparator_3_eq, comparator_4_eq, comparator_5_eq;

  Comparator #(.width(6), .mode("unsigned")) comparator_1 (
    .a(6'b000001), .b(op), .eq(comparator_1_eq));  // open: gt, lt
  Comparator #(.width(5), .mode("unsigned")) comparator_2 (
    .a({5{1'b0}}), .b(rt), .eq(comparator_2_eq));  // open: gt, lt
  Comparator #(.width(5), .mode("unsigned")) comparator_3 (.a(5'b00001), .b(rt), .eq(comparator_3_eq));  // open: gt, lt
  Comparator #(.width(5), .mode("unsigned")) comparator_4 (.a(5'b10000), .b(rt), .eq(comparator_4_eq));  // open: gt, lt
  Comparator #(.width(5), .mode("unsigned")) comparator_5 (.a(5'b10001), .b(rt), .eq(comparator_5_eq));  // open: gt, lt
  and and_1 (inst_bltz, comparator_1_eq, comparator_2_eq);
  and and_2 (inst_bgez, comparator_1_eq, comparator_3_eq);
  and and_3 (inst_bltzal, comparator_1_eq, comparator_4_eq);
  and and_4 (inst_bgezal, comparator_1_eq, comparator_5_eq);
endmodule
module DCU_aluop (
  input  inst_add,
  input  inst_subu,
  input  inst_slt,
  input  inst_and,
  input  inst_mult,
  input  inst_mfhi,
  input  inst_mflo,
  input  inst_sll,
  input  inst_addiu,
  input  inst_sltiu,
  input  inst_ori,
  input  inst_lui,
  input  inst_lb,
  input  inst_lw,
  input  inst_sb,
  input  inst_sw,
  input  inst_j,
  input  inst_jal,
  input  inst_jr,
  input  inst_beq,
  input  inst_bne,
  input  inst_div,
  input  inst_syscall,
  input  inst_eret,
  input  inst_mfc0,
  input  inst_mtc0,
  input  inst_addi,
  input  inst_addu,
  input  inst_sub,
  input  inst_slti,
  input  inst_sltu,
  input  inst_andi,
  input  inst_or,
  input  inst_xor,
  input  inst_xori,
  input  inst_nor,
  input  inst_multu,
  input  inst_srl,
  input  inst_sra,
  input  inst_sllv,
  input  inst_srlv,
  input  inst_srav,
  input  inst_mthi,
  input  inst_mtlo,
  input  inst_lh,
  input  inst_sh,
  input  inst_lbu,
  input  inst_lhu,
  input  inst_blez,
  input  inst_bgtz,
  input  inst_bltz,
  input  inst_bgez,
  input  inst_bltzal,
  input  inst_bgezal,
  input  inst_jalr,
  input  inst_divu,
  output aluop0,
  output aluop1,
  output aluop2,
  output aluop3,
  output aluop4,
  output aluop5,
  output aluop6,
  output aluop7
);

  or or_1 (aluop0, inst_subu, inst_mflo, inst_sll, inst_addiu, inst_sltiu, inst_ori, inst_lui, inst_jr, inst_bne, inst_eret, inst_mtc0, inst_addu, inst_sub, inst_sltu, inst_or, inst_nor, inst_multu, inst_sra, inst_sllv, inst_srav, inst_mtlo, inst_lh, inst_sh, inst_lbu, inst_bgtz, inst_bgez, inst_bgezal, inst_jalr, inst_divu);
  or or_2 (aluop1, inst_subu, inst_slt, inst_sltiu, inst_lw, inst_sw, inst_jal, inst_div, inst_syscall, inst_eret, inst_sub, inst_xor, inst_xori, inst_nor, inst_srl, inst_sra, inst_srlv, inst_srav, inst_mthi, inst_mtlo, inst_lbu, inst_blez, inst_bgtz, inst_bltzal, inst_bgezal, inst_jalr, inst_divu);
  or or_3 (aluop2, inst_and, inst_slt, inst_mult, inst_mfhi, inst_mflo, inst_sltiu, inst_ori, inst_lui, inst_j, inst_jal, inst_jr, inst_div, inst_syscall, inst_eret, inst_mfc0, inst_mtc0, inst_andi, inst_or, inst_xor, inst_xori, inst_nor, inst_multu, inst_mthi, inst_mtlo, inst_lhu, inst_bltz, inst_bgez, inst_bltzal, inst_bgezal, inst_jalr, inst_divu);
  or or_4 (aluop3, inst_add, inst_subu, inst_and, inst_mfhi, inst_mflo, inst_addiu, inst_ori, inst_sb, inst_sw, inst_j, inst_jal, inst_jr, inst_mfc0, inst_mtc0, inst_addi, inst_addu, inst_sub, inst_slti, inst_sltu, inst_andi, inst_or, inst_xor, inst_xori, inst_nor, inst_mthi, inst_mtlo, inst_sh, inst_lbu, inst_lhu, inst_jalr);
  or or_5 (aluop4, inst_add, inst_subu, inst_and, inst_mult, inst_sll, inst_addiu, inst_ori, inst_lb, inst_lw, inst_sb, inst_sw, inst_beq, inst_bne, inst_div, inst_xor, inst_nor, inst_multu, inst_srl, inst_sra, inst_lh, inst_sh, inst_lbu, inst_lhu, inst_blez, inst_bgtz, inst_bltz, inst_bgez, inst_bltzal, inst_bgezal, inst_divu);
  or or_6 (aluop5, inst_slt, inst_sltiu, inst_j, inst_jal, inst_jr, inst_beq, inst_bne, inst_slti, inst_sltu, inst_blez, inst_bgtz, inst_bltz, inst_bgez, inst_bltzal, inst_bgezal, inst_jalr);
  or or_7 (aluop6, inst_addi, inst_addu, inst_sub, inst_andi, inst_or, inst_xori, inst_sllv, inst_srlv, inst_srav);
  or or_8 (aluop7, inst_lb, inst_lw, inst_sb, inst_sw, inst_syscall, inst_eret, inst_mfc0, inst_mtc0, inst_lh, inst_sh, inst_lbu, inst_lhu);
endmodule

module DCU_reg (
  input  inst_add,
  input  inst_subu,
  input  inst_slt,
  input  inst_and,
  input  inst_mult,
  input  inst_mfhi,
  input  inst_mflo,
  input  inst_sll,
  input  inst_addiu,
  input  inst_sltiu,
  input  inst_ori,
  input  inst_lui,
  input  inst_lb,
  input  inst_lw,
  input  inst_sb,
  input  inst_sw,
  input  inst_j,
  input  inst_jal,
  input  inst_jr,
  input  inst_beq,
  input  inst_bne,
  input  inst_div,
  input  inst_syscall,
  input  inst_eret,
  input  inst_mfc0,
  input  inst_mtc0,
  input  inst_addi,
  input  inst_addu,
  input  inst_sub,
  input  inst_slti,
  input  inst_sltu,
  input  inst_andi,
  input  inst_or,
  input  inst_xor,
  input  inst_xori,
  input  inst_nor,
  input  inst_multu,
  input  inst_srl,
  input  inst_sra,
  input  inst_sllv,
  input  inst_srlv,
  input  inst_srav,
  input  inst_mthi,
  input  inst_mtlo,
  input  inst_lh,
  input  inst_sh,
  input  inst_lbu,
  input  inst_lhu,
  input  inst_blez,
  input  inst_bgtz,
  input  inst_bltz,
  input  inst_bgez,
  input  inst_bltzal,
  input  inst_bgezal,
  input  inst_jalr,
  input  inst_divu,
  output rreg1,
  output rreg2,
  output wreg,
  output whilo
);

  wire or_1_out, or_2_out, or_4_out, or_5_out;

  or or_1 (or_1_out, inst_add, inst_subu, inst_slt, inst_and, inst_mult, inst_addiu, inst_sltiu, inst_ori, inst_lb, inst_lw, inst_sb, inst_sw, inst_jr, inst_beq, inst_bne, inst_div, inst_addi, inst_addu, inst_sub, inst_slti, inst_sltu, inst_andi, inst_or, inst_xor, inst_xori, inst_nor, inst_multu, inst_sllv, inst_srlv, inst_srav, inst_mthi, inst_mtlo);
  or or_2 (or_2_out, inst_lh, inst_sh, inst_lbu, inst_lhu, inst_blez, inst_bgtz, inst_bltz, inst_bgez, inst_bltzal, inst_bgezal, inst_jalr, inst_divu);
  or or_3 (rreg2, inst_add, inst_subu, inst_slt, inst_and, inst_mult, inst_sll, inst_sb, inst_sw, inst_beq, inst_bne, inst_div, inst_mtc0, inst_addu, inst_sub, inst_sltu, inst_or, inst_xor, inst_nor, inst_multu, inst_srl, inst_sra, inst_sllv, inst_srlv, inst_srav, inst_sh, inst_divu);
  or or_4 (or_4_out, inst_add, inst_subu, inst_slt, inst_and, inst_mfhi, inst_mflo, inst_sll, inst_addiu, inst_sltiu, inst_ori, inst_lui, inst_lb, inst_lw, inst_jr, inst_mfc0, inst_addi, inst_addu, inst_sub, inst_slti, inst_sltu, inst_andi, inst_or, inst_xor, inst_xori, inst_nor, inst_srl, inst_sra, inst_sllv, inst_srlv, inst_srav, inst_lh, inst_lbu);
  or or_5 (or_5_out, inst_lhu, inst_bltzal, inst_bgezal, inst_jalr);
  or or_6 (whilo, inst_mult, inst_div, inst_multu, inst_mthi, inst_mtlo, inst_divu);
  or or_7 (rreg1, or_1_out, or_2_out);
  or or_8 (wreg, or_4_out, or_5_out);
endmodule

module DCU_alutype (
  input  inst_add,
  input  inst_subu,
  input  inst_slt,
  input  inst_and,
  input  inst_mult,
  input  inst_mfhi,
  input  inst_mflo,
  input  inst_sll,
  input  inst_addiu,
  input  inst_sltiu,
  input  inst_ori,
  input  inst_lui,
  input  inst_lb,
  input  inst_lw,
  input  inst_sb,
  input  inst_sw,
  input  inst_j,
  input  inst_jal,
  input  inst_jr,
  input  inst_beq,
  input  inst_bne,
  input  inst_div,
  input  inst_syscall,
  input  inst_eret,
  input  inst_mfc0,
  input  inst_mtc0,
  input  inst_addi,
  input  inst_addu,
  input  inst_sub,
  input  inst_slti,
  input  inst_sltu,
  input  inst_andi,
  input  inst_or,
  input  inst_xor,
  input  inst_xori,
  input  inst_nor,
  input  inst_multu,
  input  inst_srl,
  input  inst_sra,
  input  inst_sllv,
  input  inst_srlv,
  input  inst_srav,
  input  inst_mthi,
  input  inst_mtlo,
  input  inst_lh,
  input  inst_sh,
  input  inst_lbu,
  input  inst_lhu,
  input  inst_blez,
  input  inst_bgtz,
  input  inst_bltz,
  input  inst_bgez,
  input  inst_bltzal,
  input  inst_bgezal,
  input  inst_jalr,
  input  inst_divu,
  output alutype0,
  output alutype1,
  output alutype2
);

  wire or_1_out, or_2_out;

  or or_1 (or_1_out, inst_add, inst_subu, inst_slt, inst_mfhi, inst_mflo, inst_addiu, inst_sltiu, inst_lb, inst_lw, inst_sb, inst_sw, inst_j, inst_jal, inst_jr, inst_beq, inst_bne);
  or or_2 (or_2_out, inst_mfc0, inst_addi, inst_addu, inst_sub, inst_slti, inst_sltu, inst_lh, inst_sh, inst_lbu, inst_lhu, inst_blez, inst_bgtz, inst_bltz, inst_bgez, inst_bltzal, inst_bgezal, inst_jalr);
  or or_3 (alutype1, inst_and, inst_mfhi, inst_mflo, inst_ori, inst_lui, inst_syscall, inst_eret, inst_mfc0, inst_mtc0, inst_andi, inst_or, inst_xor, inst_xori, inst_nor);
  or or_4 (alutype2, inst_sll, inst_j, inst_jal, inst_jr, inst_beq, inst_bne, inst_syscall, inst_eret, inst_mtc0, inst_multu, inst_srl, inst_sra, inst_sllv, inst_srlv, inst_blez, inst_bgtz, inst_bltz, inst_bgez, inst_bltzal, inst_bgezal, inst_jalr);
  or or_5 (alutype0, or_1_out, or_2_out);
endmodule

module DCU_other (
  input  inst_add,
  input  inst_subu,
  input  inst_slt,
  input  inst_and,
  input  inst_mult,
  input  inst_mfhi,
  input  inst_mflo,
  input  inst_sll,
  input  inst_addiu,
  input  inst_sltiu,
  input  inst_ori,
  input  inst_lui,
  input  inst_lb,
  input  inst_lw,
  input  inst_sb,
  input  inst_sw,
  input  inst_j,
  input  inst_jal,
  input  inst_jr,
  input  inst_beq,
  input  inst_bne,
  input  inst_div,
  input  inst_syscall,
  input  inst_eret,
  input  inst_mfc0,
  input  inst_mtc0,
  input  inst_addi,
  input  inst_addu,
  input  inst_sub,
  input  inst_slti,
  input  inst_sltu,
  input  inst_andi,
  input  inst_or,
  input  inst_xor,
  input  inst_xori,
  input  inst_nor,
  input  inst_multu,
  input  inst_srl,
  input  inst_sra,
  input  inst_sllv,
  input  inst_srlv,
  input  inst_srav,
  input  inst_mthi,
  input  inst_mtlo,
  input  inst_lh,
  input  inst_sh,
  input  inst_lbu,
  input  inst_lhu,
  input  inst_blez,
  input  inst_bgtz,
  input  inst_bltz,
  input  inst_bgez,
  input  inst_bltzal,
  input  inst_bgezal,
  input  inst_jalr,
  input  inst_divu,
  output immsel,
  output rtsel,
  output sext,
  output upper,
  output mreg,
  output shift
);

  or or_1 (immsel, inst_addiu, inst_sltiu, inst_ori, inst_lui, inst_lb, inst_lw, inst_sb, inst_sw, inst_addi, inst_slti, inst_andi, inst_xori, inst_lh, inst_sh, inst_lbu, inst_lhu);
  or or_2 (rtsel, inst_addiu, inst_sltiu, inst_ori, inst_lui, inst_lb, inst_lw, inst_sb, inst_sw, inst_mfc0, inst_addi, inst_slti, inst_andi, inst_xori, inst_lh, inst_sh, inst_lbu, inst_lhu);
  or or_3 (sext, inst_addiu, inst_sltiu, inst_lb, inst_lw, inst_sb, inst_sw, inst_addi, inst_slti, inst_lh, inst_sh, inst_lbu, inst_lhu);
  or or_4 (mreg, inst_lb, inst_lw, inst_lh, inst_lbu, inst_lhu);
  or or_5 (shift, inst_sll, inst_srl, inst_sra);

  assign upper = inst_lui;
endmodule

module DCU_fwrd (
  input  rreg1,
  input  [4:0] rs,
  input  [4:0] exe2id_wa,
  input  [4:0] mem2id_wa,
  input  exe2id_wreg,
  input  mem2id_wreg,
  input  [4:0] rt,
  input  rreg2,
  output [1:0] fwrd1,
  output [1:0] fwrd2
);

  wire nor_1_out, nor_2_out, nor_3_out, nor_4_out;
  wire [4:0] xor_1_out, xor_2_out, xor_3_out, xor_4_out;

  assign xor_1_out = rs ^ exe2id_wa;  // XOR_Gate xor_1, 5 bits wide
  assign xor_2_out = rs ^ mem2id_wa;  // XOR_Gate xor_2, 5 bits wide
  assign xor_3_out = rt ^ exe2id_wa;  // XOR_Gate xor_3, 5 bits wide
  assign xor_4_out = rt ^ mem2id_wa;  // XOR_Gate xor_4, 5 bits wide
  nor nor_1 (nor_1_out, xor_1_out[0], xor_1_out[1], xor_1_out[2], xor_1_out[3], xor_1_out[4]);
  nor nor_2 (nor_2_out, xor_2_out[0], xor_2_out[1], xor_2_out[2], xor_2_out[3], xor_2_out[4]);
  nor nor_3 (nor_3_out, xor_3_out[0], xor_3_out[1], xor_3_out[2], xor_3_out[3], xor_3_out[4]);
  nor nor_4 (nor_4_out, xor_4_out[0], xor_4_out[1], xor_4_out[2], xor_4_out[3], xor_4_out[4]);
  and and_1 (fwrd1[0], rreg1, exe2id_wreg, nor_1_out);
  and and_2 (fwrd1[1], rreg1, nor_2_out, mem2id_wreg);
  and and_3 (fwrd2[0], nor_3_out, exe2id_wreg, rreg2);
  and and_4 (fwrd2[1], nor_4_out, mem2id_wreg, rreg2);
endmodule

module DCU_jump (
  input  inst_j,
  input  inst_jal,
  input  inst_jr,
  input  inst_beq,
  input  inst_bne,
  input  inst_blez,
  input  inst_bgtz,
  input  inst_bltz,
  input  inst_bgez,
  input  inst_bltzal,
  input  inst_bgezal,
  input  inst_jalr,
  input  equ,
  output jal,
  output jtsel1,
  output jtsel0
);

  or or_1 (jal, inst_bltzal, inst_jal, inst_bgezal);
  or or_2 (jtsel1, inst_j, inst_jal, equ);
  or or_3 (jtsel0, inst_jr, inst_jalr, equ);
endmodule

module DCU_exc (
  input  inst_j,
  input  inst_jal,
  input  inst_jr,
  input  inst_beq,
  input  inst_bne,
  input  inst_blez,
  input  inst_bgtz,
  input  inst_bltz,
  input  inst_bgez,
  input  inst_bltzal,
  input  inst_bgezal,
  input  inst_jalr,
  input  inst_syscall,
  input  inst_eret,
  input  inst_mfc0,
  input  inst_mtc0,
  output next_delay,
  output [4:0] exc_code
);

  wire [1:0] priority_encoder_1_out;

  Priority_Encoder #(.select(2)) priority_encoder_1 (
    .in0(1'b1), .in1(inst_syscall), .in2(inst_eret), .out(priority_encoder_1_out));  // open: in3, gs, en_out, en_in
  Multiplexer #(.select(2), .width(5), .enable("false")) multiplexer_1 (
    .in0({5{1'b0}}), .in1(5'b01000), .in2(5'b10001), .out(exc_code), .sel(priority_encoder_1_out));  // open: in3
  or or_1 (next_delay, inst_j, inst_jal, inst_jr, inst_beq, inst_bne, inst_blez, inst_bgtz, inst_bltz, inst_bgez, inst_bltzal, inst_bgezal, inst_jalr);
endmodule

module HILO (
  input  we,
  input  [31:0] in_2,
  input  [31:0] in_3,
  input  clk,
  output [31:0] out_5,
  output [31:0] out_6
);

  Register #(.width(32)) hi (.D(in_2), .en(we), .Q(out_5), .clk(clk));  // open: clr
  Register #(.width(32)) lo (.D(in_3), .en(we), .Q(out_6), .clk(clk));  // open: clr
endmodule

module ALU (
  input  [7:0] aluop,
  input  [31:0] src1,
  input  [31:0] src2,
  input  clk,
  output [31:0] logicres,
  output [31:0] arithres,
  output [31:0] shiftres,
  output [31:0] mulres_lo,
  output [31:0] mulres_hi,
  output stallreq_exe,
  output [31:0] divres_hi,
  output [31:0] divres_lo
);

  wire adder_1_cout, and_1_out, and_2_out, comparator_1_eq;
  wire [31:0] adder_1_out, adder_2_out, multiplexer_1_out, multiplexer_2_out, multiplier_1_cout,
       multiplier_1_out, negator_1_out, negator_2_out, not_1_out, not_2_out;

  ALU_logicres alu_logicres_1 (.aluop(aluop), .src1(src1), .src2(src2), .logicres(logicres));
  ALU_arithres alu_arithres_1 (.aluop(aluop), .src1(src1), .src2(src2), .arithres(arithres));
  ALU_shiftres alu_shiftres_1 (.aluop(aluop), .src1(src1), .src2(src2), .shiftres(shiftres));
  Comparator #(.mode("unsigned")) comparator_1 (.a(8'h14), .b(aluop), .eq(comparator_1_eq));  // open: gt, lt
  ALU_divres alu_divres_1 (
    .aluop(aluop), .src1(src1), .src2(src2), .clk(clk), .stallreq_exe(stallreq_exe), .divres_hi(divres_hi),
    .divres_lo(divres_lo));
  Negator #(.width(32)) negator_1 (.in(src1), .out(negator_1_out));
  Negator #(.width(32)) negator_2 (.in(src2), .out(negator_2_out));
  and and_1 (and_1_out, comparator_1_eq, src1[31]);
  and and_2 (and_2_out, src2[31], comparator_1_eq);
  Multiplexer #(.width(32), .enable("false")) multiplexer_1 (
    .in0(src1), .in1(negator_1_out), .out(multiplexer_1_out), .sel(and_1_out));
  Multiplexer #(.width(32), .enable("false")) multiplexer_2 (
    .in0(src2), .in1(negator_2_out), .out(multiplexer_2_out), .sel(and_2_out));
  Multiplier #(.width(32)) multiplier_1 (
    .a(multiplexer_1_out), .b(multiplexer_2_out), .out(multiplier_1_out), .cout(multiplier_1_cout));  // open: cin
  assign not_1_out = ~multiplier_1_out;  // NOT_Gate not_1, 32 bits wide
  assign not_2_out = ~multiplier_1_cout;  // NOT_Gate not_2, 32 bits wide
  Adder #(.width(32)) adder_1 (.a(32'h1), .b(not_1_out), .out(adder_1_out), .cout(adder_1_cout));  // open: cin
  Adder #(.width(32)) adder_2 (.a({32{1'b0}}), .b(not_2_out), .out(adder_2_out), .cin(adder_1_cout));  // open: cout
  Multiplexer #(.width(32), .enable("false")) multiplexer_3 (
    .in0(multiplier_1_out), .in1(adder_1_out), .out(mulres_lo), .sel(comparator_1_eq));
  Multiplexer #(.width(32), .enable("false")) multiplexer_4 (
    .in0(multiplier_1_cout), .in1(adder_2_out), .out(mulres_hi), .sel(comparator_1_eq));

  // Notes on the sheet:
  //   divres
endmodule

module ALU_logicres (
  input  [7:0] aluop,
  input  [31:0] src1,
  input  [31:0] src2,
  output [31:0] logicres
);

  wire comparator_1_eq, comparator_2_eq, comparator_3_eq, comparator_4_eq, comparator_5_eq, comparator_6_eq,
       comparator_7_eq, comparator_8_eq, or_2_out, or_3_out, or_4_out, priority_encoder_1_gs;
  wire [2:0] priority_encoder_1_out;
  wire [31:0] and_1_out, nor_1_out, or_1_out, xor_1_out;

  Comparator comparator_1 (.a(8'h5), .b(aluop), .eq(comparator_1_eq));  // open: gt, lt
  Comparator comparator_2 (.a(8'h1c), .b(aluop), .eq(comparator_2_eq));  // open: gt, lt
  Comparator comparator_3 (.a(8'h4c), .b(aluop), .eq(comparator_3_eq));  // open: gt, lt
  Comparator comparator_4 (.a(8'h1d), .b(aluop), .eq(comparator_4_eq));  // open: gt, lt
  Comparator comparator_5 (.a(8'h4d), .b(aluop), .eq(comparator_5_eq));  // open: gt, lt
  Comparator comparator_6 (.a(8'h1e), .b(aluop), .eq(comparator_6_eq));  // open: gt, lt
  Comparator comparator_7 (.a(8'h4e), .b(aluop), .eq(comparator_7_eq));  // open: gt, lt
  Comparator comparator_8 (.a(8'h1f), .b(aluop), .eq(comparator_8_eq));  // open: gt, lt
  assign and_1_out = src1 & src2;  // AND_Gate and_1, 32 bits wide
  assign or_1_out = src1 | src2;  // OR_Gate or_1, 32 bits wide
  assign xor_1_out = src1 ^ src2;  // XOR_Gate xor_1, 32 bits wide
  assign nor_1_out = ~(src1 | src2);  // NOR_Gate nor_1, 32 bits wide
  or or_2 (or_2_out, comparator_2_eq, comparator_3_eq);
  or or_3 (or_3_out, comparator_4_eq, comparator_5_eq);
  or or_4 (or_4_out, comparator_6_eq, comparator_7_eq);
  Priority_Encoder priority_encoder_1 (
    .in0(comparator_1_eq), .in1(or_2_out), .in2(or_3_out), .in3(or_4_out), .in4(comparator_8_eq),
    .out(priority_encoder_1_out), .gs(priority_encoder_1_gs));  // open: in5, in6, in7, en_in, en_out
  Multiplexer #(.select(3), .width(32), .disabled(0)) multiplexer_1 (
    .in0(src2), .in1(and_1_out), .in2(or_1_out), .in3(xor_1_out), .in4(nor_1_out), .out(logicres),
    .sel(priority_encoder_1_out), .en(priority_encoder_1_gs));  // open: in5, in6, in7
endmodule

module ALU_arithres (
  input  [7:0] aluop,
  input  [31:0] src1,
  input  [31:0] src2,
  output [31:0] arithres
);

  wire comparator_1_lt, comparator_2_lt, comparator_3_eq, comparator_4_eq, comparator_5_eq, comparator_6_eq,
       comparator_7_eq, comparator_8_eq, comparator_9_eq, comparator_10_eq, comparator_11_eq,
       comparator_12_eq, comparator_13_eq, comparator_14_eq, comparator_15_eq, comparator_16_eq,
       comparator_17_eq, comparator_18_eq, comparator_19_eq, comparator_20_eq, or_1_out, or_2_out, or_3_out,
       or_4_out, or_5_out, priority_encoder_1_gs;
  wire [2:0] priority_encoder_1_out;
  wire [31:0] adder_1_out, adder_2_out, bit_extender_1_out, bit_extender_2_out, subtractor_1_out;

  Adder #(.width(32)) adder_1 (.a(src1), .b(src2), .out(adder_1_out));  // open: cin, cout
  Adder #(.width(32)) adder_2 (.a(src1), .b(src2), .out(adder_2_out));  // open: cin, cout
  Subtractor #(.width(32)) subtractor_1 (.a(src1), .b(src2), .out(subtractor_1_out));  // open: bin, bout
  Comparator #(.width(32)) comparator_1 (.a(src1), .b(src2), .lt(comparator_1_lt));  // open: gt, eq
  assign bit_extender_1_out = {{31{1'b0}}, comparator_1_lt};  // Bit_Extender bit_extender_1
  Comparator #(.width(32), .mode("unsigned")) comparator_2 (.a(src1), .b(src2), .lt(comparator_2_lt));  // open: gt, eq
  assign bit_extender_2_out = {{31{1'b0}}, comparator_2_lt};  // Bit_Extender bit_extender_2
  Comparator comparator_3 (.a(8'h18), .b(aluop), .eq(comparator_3_eq));  // open: gt, lt
  Comparator comparator_4 (.a(8'h19), .b(aluop), .eq(comparator_4_eq));  // open: gt, lt
  Comparator comparator_5 (.a(8'h48), .b(aluop), .eq(comparator_5_eq));  // open: gt, lt
  Comparator comparator_6 (.a(8'h49), .b(aluop), .eq(comparator_6_eq));  // open: gt, lt
  Comparator comparator_7 (.a(8'h1b), .b(aluop), .eq(comparator_7_eq));  // open: gt, lt
  Comparator comparator_8 (.a(8'h4b), .b(aluop), .eq(comparator_8_eq));  // open: gt, lt
  Comparator comparator_9 (.a(8'h26), .b(aluop), .eq(comparator_9_eq));  // open: gt, lt
  Comparator comparator_10 (.a(8'h28), .b(aluop), .eq(comparator_10_eq));  // open: gt, lt
  Comparator comparator_11 (.a(8'h27), .b(aluop), .eq(comparator_11_eq));  // open: gt, lt
  Comparator comparator_12 (.a(8'h29), .b(aluop), .eq(comparator_12_eq));  // open: gt, lt
  Comparator comparator_13 (.a(8'h90), .b(aluop), .eq(comparator_13_eq));  // open: gt, lt
  Comparator comparator_14 (.a(8'h92), .b(aluop), .eq(comparator_14_eq));  // open: gt, lt
  Comparator comparator_15 (.a(8'h98), .b(aluop), .eq(comparator_15_eq));  // open: gt, lt
  Comparator comparator_16 (.a(8'h9a), .b(aluop), .eq(comparator_16_eq));  // open: gt, lt
  Comparator comparator_17 (.a(8'h91), .b(aluop), .eq(comparator_17_eq));  // open: gt, lt
  Comparator comparator_18 (.a(8'h99), .b(aluop), .eq(comparator_18_eq));  // open: gt, lt
  Comparator comparator_19 (.a(8'h9b), .b(aluop), .eq(comparator_19_eq));  // open: gt, lt
  Comparator comparator_20 (.a(8'h9c), .b(aluop), .eq(comparator_20_eq));  // open: gt, lt
  or or_1 (or_1_out, comparator_3_eq, comparator_4_eq, comparator_5_eq, comparator_6_eq);
  or or_2 (or_2_out, comparator_7_eq, comparator_8_eq);
  or or_3 (or_3_out, comparator_9_eq, comparator_10_eq);
  or or_4 (or_4_out, comparator_11_eq, comparator_12_eq);
  or or_5 (or_5_out, comparator_13_eq, comparator_14_eq, comparator_15_eq, comparator_16_eq, comparator_17_eq, comparator_18_eq, comparator_19_eq, comparator_20_eq);
  Priority_Encoder priority_encoder_1 (
    .in0(or_1_out), .in1(or_2_out), .in2(or_3_out), .in3(or_4_out), .in4(or_5_out),
    .out(priority_encoder_1_out), .gs(priority_encoder_1_gs));  // open: in5, in6, in7, en_in, en_out
  Multiplexer #(.select(3), .width(32), .disabled(0)) multiplexer_1 (
    .in0(adder_2_out), .in1(subtractor_1_out), .in2(bit_extender_1_out), .in3(bit_extender_2_out),
    .in4(adder_1_out), .out(arithres), .sel(priority_encoder_1_out), .en(priority_encoder_1_gs));  // open: in5, in6, in7
endmodule

module ALU_shiftres (
  input  [7:0] aluop,
  input  [31:0] src1,
  input  [31:0] src2,
  output [31:0] shiftres
);

  wire comparator_1_eq, comparator_2_eq, comparator_3_eq, comparator_4_eq, comparator_5_eq, comparator_6_eq,
       or_1_out, or_2_out, or_3_out, priority_encoder_1_gs;
  wire [1:0] priority_encoder_1_out;
  wire [31:0] shifter_1_out, shifter_2_out, shifter_3_out;

  Comparator comparator_1 (.a(8'h11), .b(aluop), .eq(comparator_1_eq));  // open: gt, lt
  Comparator comparator_2 (.a(8'h41), .b(aluop), .eq(comparator_2_eq));  // open: gt, lt
  Comparator comparator_3 (.a(8'h12), .b(aluop), .eq(comparator_3_eq));  // open: gt, lt
  Comparator comparator_4 (.a(8'h42), .b(aluop), .eq(comparator_4_eq));  // open: gt, lt
  Comparator comparator_5 (.a(8'h13), .b(aluop), .eq(comparator_5_eq));  // open: gt, lt
  Comparator comparator_6 (.a(8'h43), .b(aluop), .eq(comparator_6_eq));  // open: gt, lt
  Shifter #(.width(32)) shifter_1 (.in(src2), .\dist (src1[4:0]), .out(shifter_1_out));
  Shifter #(.width(32), .shift("lr")) shifter_2 (.in(src2), .\dist (src1[4:0]), .out(shifter_2_out));
  Shifter #(.width(32), .shift("ar")) shifter_3 (.in(src2), .\dist (src1[4:0]), .out(shifter_3_out));
  or or_1 (or_1_out, comparator_1_eq, comparator_2_eq);
  or or_2 (or_2_out, comparator_3_eq, comparator_4_eq);
  or or_3 (or_3_out, comparator_5_eq, comparator_6_eq);
  Priority_Encoder #(.select(2)) priority_encoder_1 (
    .in0(or_1_out), .in1(or_2_out), .in2(or_3_out), .out(priority_encoder_1_out), .gs(priority_encoder_1_gs));  // open: in3, en_out, en_in
  Multiplexer #(.select(2), .width(32), .disabled(0)) multiplexer_1 (
    .in0(shifter_1_out), .in1(shifter_2_out), .in2(shifter_3_out), .out(shiftres),
    .sel(priority_encoder_1_out), .en(priority_encoder_1_gs));  // open: in3
endmodule

module ALU_divres (
  input  [7:0] aluop,
  input  [31:0] src1,
  input  [31:0] src2,
  input  clk,
  output stallreq_exe,
  output [31:0] divres_hi,
  output [31:0] divres_lo
);

  wire cnt_en, comparator_1_eq, comparator_2_eq, dividend_en, end_en, not_1_out, or_1_out, ready, ready_q,
       state_en, temp_op_en;
  wire [1:0] state, state_out;
  wire [5:0] cnt, cnt_out;
  wire [31:0] divres_hi_t, divres_lo_t, quotient, quotient_out, remainder, remainder_out, temp_op1,
       temp_op1_out, temp_op2, temp_op2_out;

  Comparator comparator_1 (.a(8'h16), .b(aluop), .eq(comparator_1_eq));  // open: gt, lt
  Comparator comparator_2 (.a(8'h17), .b(aluop), .eq(comparator_2_eq));  // open: gt, lt
  or or_1 (or_1_out, comparator_1_eq, comparator_2_eq);
  Register #(.width(1)) u_ready (.D(ready), .en(end_en), .Q(ready_q), .clk(clk));  // open: clr
  Register #(.width(2)) u_state (.D(state_out), .en(state_en), .Q(state), .clk(clk));  // open: clr
  Register #(.width(6)) u_cnt (.D(cnt_out), .en(cnt_en), .Q(cnt), .clk(clk));  // open: clr
  Register #(.width(32)) u_temp_op1 (.D(temp_op1_out), .en(temp_op_en), .Q(temp_op1), .clk(clk));  // open: clr
  Register #(.width(32)) u_temp_op2 (.D(temp_op2_out), .en(temp_op_en), .Q(temp_op2), .clk(clk));  // open: clr
  Register #(.width(32)) u_remainder (.D(remainder_out), .en(dividend_en), .Q(remainder), .clk(clk));  // open: clr
  Register #(.width(32)) u_quotient (.D(quotient_out), .en(dividend_en), .Q(quotient), .clk(clk));  // open: clr
  not not_1 (not_1_out, ready_q);
  and and_1 (stallreq_exe, or_1_out, not_1_out);
  ALU_divres_state alu_divres_state_1 (
    .div_start(stallreq_exe), .state(state), .src2(src2), .cnt(cnt), .state_en(state_en),
    .state_out(state_out));
  ALU_divres_cnt alu_divres_cnt_1 (
    .cnt(cnt), .state(state), .div_start(stallreq_exe), .src2(src2), .cnt_en(cnt_en), .cnt_out(cnt_out));
  ALU_divres_op alu_divres_op_1 (
    .src1(src1), .src2(src2), .state(state), .div_start(stallreq_exe), .temp_op1(temp_op1_out),
    .temp_op2(temp_op2_out), .op_en(temp_op_en), .aluop(aluop));
  ALU_divres_dividend alu_divres_dividend_1 (
    .div_start(stallreq_exe), .src2(src1), .state(state), .cnt(cnt), .temp_op1(temp_op1_out),
    .temp_op2(temp_op2), .remainder(remainder), .quotient(quotient), .src1(src2),
    .remainder_out(remainder_out), .en(dividend_en), .quotient_out(quotient_out), .aluop(aluop));
  ALU_divres_end alu_divres_end_1 (
    .state(state), .div_start(stallreq_exe), .remainder(remainder), .quotient(quotient), .en(end_en),
    .ready_out(ready), .divres_hi(divres_hi_t), .divres_lo(divres_lo_t));
  Register #(.width(32)) u_divres_hi (.D(divres_hi_t), .en(end_en), .Q(divres_hi), .clk(clk));  // open: clr
  Register #(.width(32)) u_divres_lo (.D(divres_lo_t), .en(end_en), .Q(divres_lo), .clk(clk));  // open: clr

  // Other names for the same wires on the sheet: start = stallreq_exe

  // Notes on the sheet:
  //   div_free
  //   div_on
  //   div_end
  //   div_by_zero
endmodule

module ALU_divres_state (
  input  div_start,
  input  [1:0] state,
  input  [31:0] src2,
  input  [5:0] cnt,
  output state_en,
  output [1:0] state_out
);

  wire and_1_out, and_2_out, and_3_out, and_4_out, comparator_1_eq, comparator_2_eq, comparator_3_eq,
       comparator_4_eq, comparator_5_eq, comparator_6_eq, not_1_out, not_2_out;
  wire [1:0] truemux2_1_out_3, truemux2_2_out_3, truemux2_3_out_3, truemux2_4_out_3, truemux2_5_out_3;

  Comparator #(.width(2)) comparator_1 (.a(2'b11), .b(state), .eq(comparator_1_eq));  // open: gt, lt
  Comparator #(.width(2)) comparator_2 (.a(2'b00), .b(state), .eq(comparator_2_eq));  // open: gt, lt
  Comparator #(.width(2)) comparator_3 (.a(2'b01), .b(state), .eq(comparator_3_eq));  // open: gt, lt
  Comparator #(.width(2)) comparator_4 (.a(2'b10), .b(state), .eq(comparator_4_eq));  // open: gt, lt
  Comparator #(.width(32)) comparator_5 (.a({32{1'b0}}), .b(src2), .eq(comparator_5_eq));  // open: gt, lt
  Comparator #(.width(6)) comparator_6 (.a(6'b100000), .b(cnt), .eq(comparator_6_eq));  // open: gt, lt
  not not_1 (not_1_out, div_start);
  not not_2 (not_2_out, comparator_5_eq);
  and and_1 (and_1_out, comparator_1_eq, not_1_out);
  and and_2 (and_2_out, div_start, comparator_2_eq, comparator_5_eq);
  and and_3 (and_3_out, div_start, comparator_2_eq, not_2_out);
  and and_4 (and_4_out, comparator_4_eq, comparator_6_eq);
  TrueMux2 truemux2_1 (.in_1(and_1_out), .in_2(2'b00), .out_3(truemux2_1_out_3));
  TrueMux2 truemux2_2 (.in_1(and_2_out), .in_2(2'b01), .out_3(truemux2_2_out_3));
  TrueMux2 truemux2_3 (.in_1(comparator_3_eq), .in_2(2'b11), .out_3(truemux2_3_out_3));
  TrueMux2 truemux2_4 (.in_1(and_3_out), .in_2(2'b10), .out_3(truemux2_4_out_3));
  TrueMux2 truemux2_5 (.in_1(and_4_out), .in_2(2'b11), .out_3(truemux2_5_out_3));
  or or_1 (state_en, and_1_out, and_2_out, comparator_3_eq, and_3_out, and_4_out);
  assign state_out = truemux2_1_out_3 | truemux2_2_out_3 | truemux2_3_out_3 | truemux2_4_out_3 | truemux2_5_out_3;  // OR_Gate or_2, 2 bits wide

  // Notes on the sheet:
  //   div_free
  //   div_by_zero
  //   div_on
  //   div_end
endmodule

module ALU_divres_cnt (
  input  [5:0] cnt,
  input  [1:0] state,
  input  div_start,
  input  [31:0] src2,
  output cnt_en,
  output [5:0] cnt_out
);

  wire and_1_out, and_2_out, and_3_out, comparator_1_eq, comparator_2_eq, comparator_3_eq, comparator_4_eq,
       not_1_out, not_2_out;
  wire [5:0] adder_1_out, truemux6_1_out_3, truemux6_2_out_3, truemux6_3_out_3;

  Comparator #(.width(6)) comparator_1 (.a(6'b100000), .b(cnt), .eq(comparator_1_eq));  // open: gt, lt
  Comparator #(.width(2)) comparator_2 (.a(2'b10), .b(state), .eq(comparator_2_eq));  // open: gt, lt
  Comparator #(.width(2)) comparator_3 (.a(2'b00), .b(state), .eq(comparator_3_eq));  // open: gt, lt
  Comparator #(.width(32)) comparator_4 (.a({32{1'b0}}), .b(src2), .eq(comparator_4_eq));  // open: gt, lt
  not not_1 (not_1_out, comparator_4_eq);
  Adder #(.width(6)) adder_1 (.a(cnt), .b(6'b000010), .out(adder_1_out));  // open: cin, cout
  not not_2 (not_2_out, comparator_1_eq);
  and and_1 (and_1_out, comparator_2_eq, not_2_out);
  and and_2 (and_2_out, comparator_1_eq, comparator_2_eq);
  and and_3 (and_3_out, comparator_3_eq, div_start, not_1_out);
  TrueMux6 truemux6_1 (.in_1(and_1_out), .in_2(adder_1_out), .out_3(truemux6_1_out_3));
  TrueMux6 truemux6_2 (.in_1(and_2_out), .in_2({6{1'b0}}), .out_3(truemux6_2_out_3));
  TrueMux6 truemux6_3 (.in_1(and_3_out), .in_2({6{1'b0}}), .out_3(truemux6_3_out_3));
  or or_1 (cnt_en, and_1_out, and_2_out, and_3_out);
  assign cnt_out = truemux6_1_out_3 | truemux6_2_out_3 | truemux6_3_out_3;  // OR_Gate or_2, 6 bits wide
endmodule

module ALU_divres_op (
  input  [7:0] aluop,
  input  [31:0] src1,
  input  [31:0] src2,
  input  [1:0] state,
  input  div_start,
  output [31:0] temp_op1,
  output [31:0] temp_op2,
  output op_en
);

  wire and_1_out, and_2_out, comparator_1_eq, comparator_2_eq, comparator_3_eq, not_1_out;
  wire [31:0] negator_1_out, negator_2_out;

  Comparator comparator_1 (.a(8'h16), .b(aluop), .eq(comparator_1_eq));  // open: gt, lt
  Negator #(.width(32)) negator_1 (.in(src1), .out(negator_1_out));
  Negator #(.width(32)) negator_2 (.in(src2), .out(negator_2_out));
  and and_1 (and_1_out, src1[31], comparator_1_eq);
  and and_2 (and_2_out, src2[31], comparator_1_eq);
  Comparator #(.width(2)) comparator_2 (.a(2'b00), .b(state), .eq(comparator_2_eq));  // open: gt, lt
  Comparator #(.width(32)) comparator_3 (.a({32{1'b0}}), .b(src2), .eq(comparator_3_eq));  // open: gt, lt
  not not_1 (not_1_out, comparator_3_eq);
  Multiplexer #(.width(32), .enable("false")) multiplexer_1 (
    .in0(src1), .in1(negator_1_out), .out(temp_op1), .sel(and_1_out));
  Multiplexer #(.width(32), .enable("false")) multiplexer_2 (
    .in0(src2), .in1(negator_2_out), .out(temp_op2), .sel(and_2_out));
  and and_3 (op_en, comparator_2_eq, div_start, not_1_out);
endmodule

module ALU_divres_dividend (
  input  div_start,
  input  [31:0] src2,
  input  [1:0] state,
  input  [5:0] cnt,
  input  [31:0] temp_op1,
  input  [31:0] temp_op2,
  input  [31:0] remainder,
  input  [31:0] quotient,
  input  [7:0] aluop,
  input  [31:0] src1,
  output [31:0] remainder_out,
  output en,
  output [31:0] quotient_out
);

  wire adder_1_cout, and_1_out, and_2_out, and_3_out, and_4_out, and_5_out, comparator_1_eq, comparator_2_eq,
       comparator_3_eq, comparator_4_eq, comparator_5_eq, comparator_6_eq, comparator_7_lt, comparator_8_lt,
       comparator_9_lt, comparator_10_eq, nor_1_out, nor_2_out, not_1_out, not_2_out, not_3_out, xor_1_out,
       xor_2_out;
  wire [1:0] priority_encoder_1_out, priority_encoder_2_out;
  wire [31:0] adder_1_out, bit_extender_2_out, bit_extender_3_out, multiplexer_5_out, negator_1_out,
       negator_2_out, or_1_out, quotient_out1, quotient_out3, quotient_out4, remainder_out1, remainder_out3,
       remainder_out4, shifter_1_out, shifter_2_out, shifter_4_out, shifter_5_out, subtractor_1_out,
       subtractor_2_out, subtractor_3_out;

  Comparator comparator_1 (.a(8'h16), .b(aluop), .eq(comparator_1_eq));  // open: gt, lt
  Comparator #(.width(32)) comparator_2 (.a({32{1'b0}}), .b(src2), .eq(comparator_2_eq));  // open: gt, lt
  Comparator #(.width(2)) comparator_3 (.a(2'b00), .b(state), .eq(comparator_3_eq));  // open: gt, lt
  Comparator #(.width(2)) comparator_4 (.a(2'b01), .b(state), .eq(comparator_4_eq));  // open: gt, lt
  Comparator #(.width(2)) comparator_5 (.a(2'b10), .b(state), .eq(comparator_5_eq));  // open: gt, lt
  Comparator #(.width(6)) comparator_6 (.a(6'b100000), .b(cnt), .eq(comparator_6_eq));  // open: gt, lt
  Shifter #(.width(32)) shifter_1 (.in(temp_op2), .\dist (5'b00001), .out(shifter_1_out));
  Shifter #(.width(32)) shifter_2 (.in(temp_op2), .\dist (5'b00001), .out(shifter_2_out));
  Negator #(.width(32)) negator_1 (.in(remainder), .out(negator_1_out));
  not not_1 (not_1_out, comparator_2_eq);
  assign remainder_out1 = {{30{1'b0}}, temp_op1[31:30]};  // Bit_Extender bit_extender_1
  Shifter #(.width(32)) shifter_3 (.in(temp_op1), .\dist (5'b00010), .out(quotient_out1));
  Adder #(.width(32)) adder_1 (.a(temp_op2), .b(shifter_2_out), .out(adder_1_out), .cout(adder_1_cout));  // open: cin
  Negator #(.width(32)) negator_2 (.in(quotient), .out(negator_2_out));
  not not_2 (not_2_out, comparator_6_eq);
  xor xor_1 (xor_1_out, src1[31], src2[31]);
  xor xor_2 (xor_2_out, src1[31], remainder[31]);
  and and_1 (and_1_out, div_start, not_1_out, comparator_3_eq);
  and and_2 (and_2_out, comparator_1_eq, xor_1_out);
  Multiplexer #(.width(32), .enable("false")) multiplexer_1 (
    .in0(quotient), .in1(negator_2_out), .out(quotient_out4), .sel(and_2_out));
  and and_3 (and_3_out, comparator_1_eq, xor_2_out);
  Multiplexer #(.width(32), .enable("false")) multiplexer_2 (
    .in0(remainder), .in1(negator_1_out), .out(remainder_out4), .sel(and_3_out));
  and and_4 (and_4_out, comparator_5_eq, not_2_out);
  and and_5 (and_5_out, comparator_5_eq, comparator_6_eq);
  Priority_Encoder #(.select(2)) priority_encoder_1 (
    .in0(and_1_out), .in1(comparator_4_eq), .in2(and_4_out), .in3(and_5_out), .out(priority_encoder_1_out),
    .gs(en), .en_in(1'b1));  // open: en_out
  Comparator #(.width(32), .mode("unsigned")) comparator_7 (
    .a(remainder), .b(temp_op2), .lt(comparator_7_lt));  // open: gt, eq
  Comparator #(.width(32), .mode("unsigned")) comparator_8 (
    .a(remainder), .b(shifter_1_out), .lt(comparator_8_lt));  // open: gt, eq
  Comparator #(.width(32), .mode("unsigned")) comparator_9 (
    .a(remainder), .b(adder_1_out), .lt(comparator_9_lt));  // open: gt, eq
  Subtractor #(.width(32)) subtractor_1 (.a(remainder), .b(temp_op2), .out(subtractor_1_out));  // open: bin, bout
  Subtractor #(.width(32)) subtractor_2 (.a(remainder), .b(shifter_1_out), .out(subtractor_2_out));  // open: bin, bout
  Subtractor #(.width(32)) subtractor_3 (.a(remainder), .b(adder_1_out), .out(subtractor_3_out));  // open: bin, bout
  not not_3 (not_3_out, comparator_7_lt);
  nor nor_1 (nor_1_out, comparator_8_lt, temp_op2[31]);
  nor nor_2 (nor_2_out, comparator_9_lt, temp_op2[31], adder_1_cout);
  Shifter #(.width(32)) shifter_4 (.in(quotient), .\dist (5'b00010), .out(shifter_4_out));
  Multiplexer #(.select(2), .width(32), .enable("false")) multiplexer_3 (
    .in0(remainder_out1), .in1({32{1'b0}}), .in2(remainder_out3), .in3(remainder_out4), .out(remainder_out),
    .sel(priority_encoder_1_out));
  Multiplexer #(.select(2), .width(32), .enable("false")) multiplexer_4 (
    .in0(quotient_out1), .in1({32{1'b0}}), .in2(quotient_out3), .in3(quotient_out4), .out(quotient_out),
    .sel(priority_encoder_1_out));
  assign bit_extender_2_out = {{30{1'b0}}, quotient[31:30]};  // Bit_Extender bit_extender_2
  Priority_Encoder #(.select(2)) priority_encoder_2 (
    .in0(1'b1), .in1(not_3_out), .in2(nor_1_out), .in3(nor_2_out), .out(priority_encoder_2_out));  // open: gs, en_out, en_in
  Multiplexer #(.select(2), .width(32), .enable("false")) multiplexer_5 (
    .in0(remainder), .in1(subtractor_1_out), .in2(subtractor_2_out), .in3(subtractor_3_out),
    .out(multiplexer_5_out), .sel(priority_encoder_2_out));
  assign bit_extender_3_out = {{30{1'b0}}, priority_encoder_2_out};  // Bit_Extender bit_extender_3
  Shifter #(.width(32)) shifter_5 (.in(multiplexer_5_out), .\dist (5'b00010), .out(shifter_5_out));
  assign or_1_out = shifter_5_out | bit_extender_2_out;  // OR_Gate or_1, 32 bits wide
  Comparator #(.width(6)) comparator_10 (.a(6'b011110), .b(cnt), .eq(comparator_10_eq));  // open: gt, lt
  assign quotient_out3 = bit_extender_3_out | shifter_4_out;  // OR_Gate or_2, 32 bits wide
  Multiplexer #(.width(32), .enable("false")) multiplexer_6 (
    .in0(or_1_out), .in1(multiplexer_5_out), .out(remainder_out3), .sel(comparator_10_eq));
endmodule

module ALU_divres_end (
  input  [1:0] state,
  input  div_start,
  input  [31:0] remainder,
  input  [31:0] quotient,
  output en,
  output ready_out,
  output [31:0] divres_hi,
  output [31:0] divres_lo
);

  Comparator #(.width(2)) comparator_1 (.a(2'b11), .b(state), .eq(en));  // open: gt, lt
  Multiplexer #(.width(32), .enable("false")) multiplexer_1 (
    .in0({32{1'b0}}), .in1(remainder), .out(divres_hi), .sel(div_start));
  Multiplexer #(.width(32), .enable("false")) multiplexer_2 (
    .in0({32{1'b0}}), .in1(quotient), .out(divres_lo), .sel(div_start));
  Multiplexer #(.enable("false")) multiplexer_3 (.in0(1'b0), .in1(1'b1), .out(ready_out), .sel(div_start));
endmodule

module MCU (
  input  [31:0] maddr,
  input  [7:0] aluop,
  output [3:0] dre,
  output [3:0] we,
  output dce
);

  wire comparator_1_eq, comparator_2_eq, comparator_3_eq, comparator_4_eq, comparator_5_eq, comparator_6_eq,
       comparator_7_eq, comparator_8_eq;
  wire [1:0] bitselector_1_out;

  BitSelector #(.width(32), .group(2)) bitselector_1 (.in(maddr), .out(bitselector_1_out), .sel(4'b0000));
  MCU_dre mcu_dre_1 (.maddr2(bitselector_1_out), .aluop(aluop), .dre(dre));
  MCU_we mcu_we_1 (.maddr2(bitselector_1_out), .aluop(aluop), .we(we));
  Comparator comparator_1 (.a(8'h90), .b(aluop), .eq(comparator_1_eq));  // open: gt, lt
  Comparator comparator_2 (.a(8'h92), .b(aluop), .eq(comparator_2_eq));  // open: gt, lt
  Comparator comparator_3 (.a(8'h98), .b(aluop), .eq(comparator_3_eq));  // open: gt, lt
  Comparator comparator_4 (.a(8'h9a), .b(aluop), .eq(comparator_4_eq));  // open: gt, lt
  Comparator comparator_5 (.a(8'h91), .b(aluop), .eq(comparator_5_eq));  // open: gt, lt
  Comparator comparator_6 (.a(8'h99), .b(aluop), .eq(comparator_6_eq));  // open: gt, lt
  Comparator comparator_7 (.a(8'h9b), .b(aluop), .eq(comparator_7_eq));  // open: gt, lt
  Comparator comparator_8 (.a(8'h9c), .b(aluop), .eq(comparator_8_eq));  // open: gt, lt
  or or_1 (dce, comparator_1_eq, comparator_2_eq, comparator_3_eq, comparator_4_eq, comparator_5_eq, comparator_6_eq, comparator_7_eq, comparator_8_eq);
endmodule

module MCU_dre (
  input  [1:0] maddr2,
  input  [7:0] aluop,
  output [3:0] dre
);

  wire and_1_out, and_2_out, and_3_out, and_4_out, and_5_out, and_6_out, equal2_1_eq, equal2_2_eq,
       equal2_3_eq, equal2_4_eq, equal2_5_eq, equal2_6_eq, equal8_1_eq, equal8_2_eq, equal8_3_eq,
       equal8_4_eq, equal8_5_eq, or_1_out, or_2_out, priority_encoder_1_gs;
  wire [2:0] priority_encoder_1_out;

  Equal8 equal8_1 (.a(aluop), .b(8'h90), .eq(equal8_1_eq));
  Equal8 equal8_2 (.a(aluop), .b(8'h9b), .eq(equal8_2_eq));
  Equal8 equal8_3 (.a(aluop), .b(8'h91), .eq(equal8_3_eq));
  Equal8 equal8_4 (.a(aluop), .b(8'h9c), .eq(equal8_4_eq));
  Equal8 equal8_5 (.a(aluop), .b(8'h92), .eq(equal8_5_eq));
  Equal2 equal2_1 (.a(maddr2), .b(2'b11), .eq(equal2_1_eq));
  Equal2 equal2_2 (.a(maddr2), .b(2'b10), .eq(equal2_2_eq));
  Equal2 equal2_3 (.a(maddr2), .b(2'b01), .eq(equal2_3_eq));
  Equal2 equal2_4 (.a(maddr2), .b(2'b00), .eq(equal2_4_eq));
  Equal2 equal2_5 (.a(maddr2), .b(2'b10), .eq(equal2_5_eq));
  Equal2 equal2_6 (.a(maddr2), .b(2'b00), .eq(equal2_6_eq));
  or or_1 (or_1_out, equal8_1_eq, equal8_2_eq);
  or or_2 (or_2_out, equal8_3_eq, equal8_4_eq);
  and and_1 (and_1_out, equal2_1_eq, or_1_out);
  and and_2 (and_2_out, equal2_2_eq, or_1_out);
  and and_3 (and_3_out, equal2_3_eq, or_1_out);
  and and_4 (and_4_out, equal2_4_eq, or_1_out);
  and and_5 (and_5_out, equal2_5_eq, or_2_out);
  and and_6 (and_6_out, equal2_6_eq, or_2_out);
  Priority_Encoder priority_encoder_1 (
    .in0(and_1_out), .in1(and_2_out), .in2(and_3_out), .in3(and_4_out), .in4(and_5_out), .in5(and_6_out),
    .in6(equal8_5_eq), .out(priority_encoder_1_out), .gs(priority_encoder_1_gs));  // open: in7, en_in, en_out
  Multiplexer #(.select(3), .width(4), .disabled(0)) multiplexer_1 (
    .in0(4'b0001), .in1(4'b0010), .in2(4'b0100), .in3(4'b1000), .in4(4'b0011), .in5(4'b1100), .in6(4'b1111),
    .out(dre), .sel(priority_encoder_1_out), .en(priority_encoder_1_gs));  // open: in7
endmodule

module MCU_we (
  input  [1:0] maddr2,
  input  [7:0] aluop,
  output [3:0] we
);

  wire and_1_out, and_2_out, and_3_out, and_4_out, and_5_out, and_6_out, equal2_1_eq, equal2_2_eq,
       equal2_3_eq, equal2_4_eq, equal2_5_eq, equal2_6_eq, equal8_1_eq, equal8_2_eq, equal8_3_eq,
       priority_encoder_1_gs;
  wire [2:0] priority_encoder_1_out;

  Equal2 equal2_1 (.a(maddr2), .b(2'b11), .eq(equal2_1_eq));
  Equal2 equal2_2 (.a(maddr2), .b(2'b10), .eq(equal2_2_eq));
  Equal2 equal2_3 (.a(maddr2), .b(2'b01), .eq(equal2_3_eq));
  Equal2 equal2_4 (.a(maddr2), .b(2'b00), .eq(equal2_4_eq));
  Equal2 equal2_5 (.a(maddr2), .b(2'b10), .eq(equal2_5_eq));
  Equal2 equal2_6 (.a(maddr2), .b(2'b00), .eq(equal2_6_eq));
  Equal8 equal8_1 (.a(aluop), .b(8'h98), .eq(equal8_1_eq));
  Equal8 equal8_2 (.b(8'h99), .eq(equal8_2_eq));  // open: a
  Equal8 equal8_3 (.a(aluop), .b(8'h9a), .eq(equal8_3_eq));
  and and_1 (and_1_out, equal2_1_eq, equal8_1_eq);
  and and_2 (and_2_out, equal2_2_eq, equal8_1_eq);
  and and_3 (and_3_out, equal2_3_eq, equal8_1_eq);
  and and_4 (and_4_out, equal2_4_eq, equal8_1_eq);
  and and_5 (and_5_out, equal2_5_eq, equal8_2_eq);
  and and_6 (and_6_out, equal2_6_eq, equal8_2_eq);
  Priority_Encoder priority_encoder_1 (
    .in0(and_1_out), .in1(and_2_out), .in2(and_3_out), .in3(and_4_out), .in4(and_5_out), .in5(and_6_out),
    .in6(equal8_3_eq), .out(priority_encoder_1_out), .gs(priority_encoder_1_gs));  // open: in7, en_in, en_out
  Multiplexer #(.select(3), .width(4), .disabled(0)) multiplexer_1 (
    .in0(4'b0001), .in1(4'b0010), .in2(4'b0100), .in3(4'b1000), .in4(4'b0011), .in5(4'b1100), .in6(4'b1111),
    .out(we), .sel(priority_encoder_1_out), .en(priority_encoder_1_gs));  // open: in7
endmodule

module SCU (
  input  stallreq_id,
  input  stallreq_exe,
  output [3:0] stall
);

  wire comparator_1_eq, comparator_2_eq;
  wire [1:0] priority_encoder_1_out;

  Comparator #(.width(1), .mode("unsigned")) comparator_1 (
    .a(stallreq_id), .b(1'b1), .eq(comparator_1_eq));  // open: gt, lt
  Comparator #(.width(1), .mode("unsigned")) comparator_2 (
    .a(stallreq_exe), .b(1'b1), .eq(comparator_2_eq));  // open: gt, lt
  Priority_Encoder #(.select(2)) priority_encoder_1 (
    .in0(1'b1), .in1(comparator_1_eq), .in2(comparator_2_eq), .out(priority_encoder_1_out));  // open: in3, gs, en_out, en_in
  Multiplexer #(.select(2), .width(4), .enable("false")) multiplexer_1 (
    .in0(4'b0000), .in1(4'b0111), .in2(4'b1111), .out(stall), .sel(priority_encoder_1_out));  // open: in3
endmodule

module cp0_reg (
  input  clk,
  input  rst,
  input  we,
  input  [31:0] badvaddr_i,
  input  [4:0] waddr,
  input  [31:0] wdata,
  input  in_delay_i,
  input  [4:0] raddr,
  input  re,
  input  [7:0] int_i,
  input  [31:0] pc_i,
  input  [4:0] exccode_i,
  output [31:0] status_o,
  output [31:0] cause_o,
  output [31:0] data_o,
  output flush_im,
  output flush,
  output [31:0] cp0_excaddr
);

  wire and_1_out, and_2_out, and_3_out, comparator_4_eq, comparator_5_eq, comparator_6_eq, comparator_7_eq,
       comparator_8_eq, comparator_9_eq, comparator_10_eq, comparator_11_eq, comparator_12_eq,
       comparator_13_eq, exc_adel, exc_ades, exc_none, not_1_out, not_3_out, or_1_out, or_2_out,
       priority_encoder_1_gs, priority_encoder_1_out, priority_encoder_2_gs, priority_encoder_3_gs;
  wire [1:0] priority_encoder_2_out, priority_encoder_3_out;
  wire [31:0] badvaddr_o, cp0_reg_cause_1_cause, cp0_reg_epc_1_epc, cp0_reg_status_1_status, epc_o,
       multiplexer_1_out, multiplexer_3_out, multiplexer_4_out, multiplexer_5_out, multiplexer_6_out;

  Comparator #(.width(5), .mode("unsigned")) comparator_1 (
    .a({5{1'b0}}), .b(exccode_i), .eq(exc_none));  // open: gt, lt
  Comparator #(.width(5), .mode("unsigned")) comparator_2 (.a(5'b00100), .b(exccode_i), .eq(exc_adel));  // open: gt, lt
  Comparator #(.width(5), .mode("unsigned")) comparator_3 (.a(5'b00101), .b(exccode_i), .eq(exc_ades));  // open: gt, lt
  Comparator #(.width(5), .mode("unsigned")) comparator_4 (
    .a({5{1'b0}}), .b(exccode_i), .eq(comparator_4_eq));  // open: gt, lt
  Comparator #(.width(5), .mode("unsigned")) comparator_5 (
    .a(5'b10001), .b(exccode_i), .eq(comparator_5_eq));  // open: gt, lt
  Comparator #(.width(5), .mode("unsigned")) comparator_6 (
    .a(5'b10001), .b(exccode_i), .eq(comparator_6_eq));  // open: gt, lt
  Comparator #(.width(5), .mode("unsigned")) comparator_7 (
    .a(5'b01110), .b(waddr), .eq(comparator_7_eq));  // open: gt, lt
  Comparator #(.width(5), .mode("unsigned")) comparator_8 (
    .a(5'b10000), .b(exccode_i), .eq(comparator_8_eq));  // open: gt, lt
  not not_1 (not_1_out, comparator_4_eq);
  Comparator #(.width(5), .mode("unsigned")) comparator_9 (
    .a(5'b01000), .b(waddr), .eq(comparator_9_eq));  // open: gt, lt
  or or_1 (or_1_out, exc_adel, exc_ades);
  and and_1 (and_1_out, comparator_6_eq, we, comparator_7_eq);
  and and_2 (and_2_out, exc_none, we, comparator_9_eq);
  not not_2 (flush, exc_none);
  cp0_reg_status cp0_reg_status_1 (
    .exc_none(exc_none), .we(we), .waddr(waddr), .exc_code(exccode_i), .status_o(status_o), .wdata(wdata),
    .status(cp0_reg_status_1_status));
  cp0_reg_cause cp0_reg_cause_1 (
    .status_o(status_o), .in_delay(in_delay_i), .exc_none(exc_none), .we(we), .waddr(waddr),
    .cause_o(cause_o), .exc_code(exccode_i), .\int (int_i), .wdata(wdata), .cause(cp0_reg_cause_1_cause));
  cp0_reg_epc cp0_reg_epc_1 (
    .status_o(status_o), .in_delay(in_delay_i), .exc_none(exc_none), .we(we), .waddr(waddr), .epc_o(epc_o),
    .pc(pc_i), .wdata(wdata), .epc(cp0_reg_epc_1_epc), .exc_code(exccode_i));
  Priority_Encoder #(.select(1)) priority_encoder_1 (
    .in0(or_1_out), .in1(and_2_out), .out(priority_encoder_1_out), .gs(priority_encoder_1_gs));  // open: en_out, en_in
  Comparator #(.width(5), .mode("unsigned")) comparator_10 (
    .a(5'b01000), .b(raddr), .eq(comparator_10_eq));  // open: gt, lt
  Comparator #(.width(5), .mode("unsigned")) comparator_11 (
    .a(5'b01100), .b(raddr), .eq(comparator_11_eq));  // open: gt, lt
  Comparator #(.width(5), .mode("unsigned")) comparator_12 (
    .a(5'b01101), .b(raddr), .eq(comparator_12_eq));  // open: gt, lt
  Comparator #(.width(5), .mode("unsigned")) comparator_13 (
    .a(5'b01110), .b(raddr), .eq(comparator_13_eq));  // open: gt, lt
  Register #(.width(1)) u_flush_im (.D(flush), .Q(flush_im));  // open: en, clk, clr
  Priority_Encoder #(.select(2)) priority_encoder_2 (
    .in0(not_1_out), .in1(comparator_5_eq), .in2(and_1_out), .in3(comparator_8_eq),
    .out(priority_encoder_2_out), .gs(priority_encoder_2_gs));  // open: en_out, en_in
  Multiplexer #(.width(32), .disabled(0), .enable("false")) multiplexer_1 (
    .in0(badvaddr_i), .in1(wdata), .out(multiplexer_1_out), .sel(priority_encoder_1_out));
  Priority_Encoder #(.select(2)) priority_encoder_3 (
    .in0(comparator_10_eq), .in1(comparator_11_eq), .in2(comparator_12_eq), .in3(comparator_13_eq),
    .out(priority_encoder_3_out), .gs(priority_encoder_3_gs));  // open: en_out, en_in
  Multiplexer #(.select(2), .width(32), .disabled(0)) multiplexer_2 (
    .in0(32'h100), .in1(epc_o), .in2(wdata), .in3(32'h40), .out(cp0_excaddr), .sel(priority_encoder_2_out),
    .en(priority_encoder_2_gs));
  Multiplexer #(.width(32), .enable("false")) multiplexer_3 (
    .in0({32{1'b0}}), .in1(multiplexer_1_out), .out(multiplexer_3_out), .sel(rst));
  Multiplexer #(.width(32), .enable("false")) multiplexer_4 (
    .in0(32'h10000000), .in1(cp0_reg_status_1_status), .out(multiplexer_4_out), .sel(rst));
  Multiplexer #(.width(32), .enable("false")) multiplexer_5 (
    .in0({32{1'b0}}), .in1(cp0_reg_cause_1_cause), .out(multiplexer_5_out), .sel(rst));
  Multiplexer #(.width(32), .enable("false")) multiplexer_6 (
    .in0({32{1'b0}}), .in1(cp0_reg_epc_1_epc), .out(multiplexer_6_out), .sel(rst));
  not not_3 (not_3_out, rst);
  or or_2 (or_2_out, not_3_out, priority_encoder_1_gs);
  Multiplexer #(.select(2), .width(32), .disabled(0)) multiplexer_7 (
    .in0(badvaddr_o), .in1(status_o), .in2(cause_o), .in3(epc_o), .out(data_o), .sel(priority_encoder_3_out),
    .en(and_3_out));
  and and_3 (and_3_out, re, priority_encoder_3_gs, rst);
  Register #(.width(32)) badvaddr (.D(multiplexer_3_out), .en(or_2_out), .Q(badvaddr_o), .clk(clk));  // open: clr
  Register #(.width(32)) status (.D(multiplexer_4_out), .en(1'b1), .Q(status_o), .clk(clk));  // open: clr
  Register #(.width(32)) cause (.D(multiplexer_5_out), .en(1'b1), .Q(cause_o), .clk(clk));  // open: clr
  Register #(.width(32)) epc (.D(multiplexer_6_out), .en(1'b1), .Q(epc_o), .clk(clk));  // open: clr

  // Other names for the same wires on the sheet: exc_code[4:0] = exccode_i
endmodule

module cp0_reg_status (
  input  [4:0] exc_code,
  input  exc_none,
  input  we,
  input  [4:0] waddr,
  input  [31:0] status_o,
  input  [31:0] wdata,
  output [31:0] status
);

  wire and_1_out, comparator_1_eq, comparator_2_eq, not_1_out;
  wire [1:0] priority_encoder_1_out;

  not not_1 (not_1_out, exc_none);
  Comparator #(.width(5), .mode("unsigned")) comparator_1 (
    .a(5'b10001), .b(exc_code), .eq(comparator_1_eq));  // open: gt, lt
  Comparator #(.width(5), .mode("unsigned")) comparator_2 (
    .a(5'b01100), .b(waddr), .eq(comparator_2_eq));  // open: gt, lt
  and and_1 (and_1_out, exc_none, we, comparator_2_eq);
  Priority_Encoder #(.select(2)) priority_encoder_1 (
    .in0(1'b1), .in1(not_1_out), .in2(comparator_1_eq), .in3(and_1_out), .out(priority_encoder_1_out));  // open: gs, en_out, en_in
  Multiplexer #(.select(2), .width(32), .enable("false")) multiplexer_1 (
    .in0(status_o), .in1({status_o[31:2], 1'b1, status_o[0]}), .in2({status_o[31:2], 1'b0, status_o[0]}),
    .in3(wdata), .out(status), .sel(priority_encoder_1_out));
endmodule

module cp0_reg_cause (
  input  [31:0] status_o,
  input  in_delay,
  input  exc_none,
  input  we,
  input  [4:0] waddr,
  input  [31:0] cause_o,
  input  [4:0] exc_code,
  input  [7:0] \int ,
  input  [31:0] wdata,
  output [31:0] cause
);

  wire and_1_out, and_2_out, and_3_out, and_4_out, comparator_1_eq, comparator_2_eq, not_1_out, not_2_out,
       not_3_out, not_4_out;
  wire [2:0] priority_encoder_1_out;

  Comparator #(.width(5), .mode("unsigned")) comparator_1 (
    .a(5'b10001), .b(exc_code), .eq(comparator_1_eq));  // open: gt, lt
  Comparator #(.width(5), .mode("unsigned")) comparator_2 (
    .a(5'b01101), .b(waddr), .eq(comparator_2_eq));  // open: gt, lt
  not not_1 (not_1_out, comparator_1_eq);
  not not_2 (not_2_out, exc_none);
  and and_1 (and_1_out, not_1_out, not_2_out);
  not not_3 (not_3_out, status_o[1]);
  and and_2 (and_2_out, exc_none, we, comparator_2_eq);
  and and_3 (and_3_out, not_3_out, and_1_out, in_delay);
  and and_4 (and_4_out, not_3_out, and_1_out, not_4_out);
  not not_4 (not_4_out, in_delay);
  Priority_Encoder priority_encoder_1 (
    .in0(1'b1), .in1(and_1_out), .in2(and_3_out), .in3(and_4_out), .in4(and_2_out),
    .out(priority_encoder_1_out));  // open: in5, in6, in7, en_in, gs, en_out
  Multiplexer #(.select(3), .width(32), .enable("false")) multiplexer_1 (
    .in0({cause_o[31:16], \int , cause_o[7:0]}),
    .in1({cause_o[31:16], \int , cause_o[7], exc_code, cause_o[1:0]}),
    .in2({1'b1, cause_o[30:16], \int , cause_o[7], exc_code, cause_o[1:0]}),
    .in3({1'b0, cause_o[30:16], \int , cause_o[7], exc_code, cause_o[1:0]}), .in4(wdata), .out(cause),
    .sel(priority_encoder_1_out));  // open: in5, in6, in7
endmodule

module cp0_reg_epc (
  input  [4:0] exc_code,
  input  [31:0] status_o,
  input  in_delay,
  input  exc_none,
  input  we,
  input  [4:0] waddr,
  input  [31:0] epc_o,
  input  [31:0] pc,
  input  [31:0] wdata,
  output [31:0] epc
);

  wire and_1_out, and_2_out, and_3_out, and_4_out, comparator_1_eq, comparator_2_eq, not_1_out, not_2_out,
       not_3_out, not_4_out;
  wire [1:0] priority_encoder_1_out;
  wire [31:0] subtractor_1_out;

  Comparator #(.width(5), .mode("unsigned")) comparator_1 (
    .a(5'b10001), .b(exc_code), .eq(comparator_1_eq));  // open: gt, lt
  Comparator #(.width(5), .mode("unsigned")) comparator_2 (
    .a(5'b01110), .b(waddr), .eq(comparator_2_eq));  // open: gt, lt
  not not_1 (not_1_out, comparator_1_eq);
  not not_2 (not_2_out, exc_none);
  and and_1 (and_1_out, not_1_out, not_2_out);
  not not_3 (not_3_out, status_o[1]);
  and and_2 (and_2_out, exc_none, we, comparator_2_eq);
  and and_3 (and_3_out, not_3_out, and_1_out, in_delay);
  and and_4 (and_4_out, not_3_out, and_1_out, not_4_out);
  not not_4 (not_4_out, in_delay);
  Subtractor #(.width(32)) subtractor_1 (.a(pc), .b(32'h4), .out(subtractor_1_out));  // open: bin, bout
  Priority_Encoder #(.select(2)) priority_encoder_1 (
    .in0(1'b1), .in1(and_3_out), .in2(and_4_out), .in3(and_2_out), .out(priority_encoder_1_out));  // open: gs, en_out, en_in
  Multiplexer #(.select(2), .width(32), .enable("false")) multiplexer_1 (
    .in0(epc_o), .in1(subtractor_1_out), .in2(pc), .in3(wdata), .out(epc), .sel(priority_encoder_1_out));
endmodule

module EqualMux (
  input  [31:0] src,
  input  [7:0] en1,
  input  [7:0] en2,
  output [31:0] out_4
);

  wire nor_1_out;
  wire [7:0] xor_1_out;

  assign xor_1_out = en1 ^ en2;  // XOR_Gate xor_1, 8 bits wide
  Multiplexer #(.width(32), .enable("false")) multiplexer_1 (.in0({32{1'b0}}), .in1(src), .out(out_4), .sel(nor_1_out));
  nor nor_1 (nor_1_out, xor_1_out[0], xor_1_out[1], xor_1_out[2], xor_1_out[3], xor_1_out[4], xor_1_out[5], xor_1_out[6], xor_1_out[7]);
endmodule

module TrueMux6 (
  input  in_1,
  input  [5:0] in_2,
  output [5:0] out_3
);

  Multiplexer #(.width(6), .enable("false")) multiplexer_1 (.in0({6{1'b0}}), .in1(in_2), .out(out_3), .sel(in_1));
endmodule

module TrueMux2 (
  input  in_1,
  input  [1:0] in_2,
  output [1:0] out_3
);

  Multiplexer #(.width(2), .enable("false")) multiplexer_1 (.in0(2'b00), .in1(in_2), .out(out_3), .sel(in_1));
endmodule

module Equal8 (
  input  [7:0] a,
  input  [7:0] b,
  output eq
);

  wire [7:0] xor_1_out;

  assign xor_1_out = a ^ b;  // XOR_Gate xor_1, 8 bits wide
  nor nor_1 (eq, xor_1_out[0], xor_1_out[1], xor_1_out[2], xor_1_out[3], xor_1_out[4], xor_1_out[5], xor_1_out[6], xor_1_out[7]);
endmodule

module Equal2 (
  input  [1:0] a,
  input  [1:0] b,
  output eq
);

  wire [1:0] xor_1_out;

  assign xor_1_out = a ^ b;  // XOR_Gate xor_1, 2 bits wide
  nor nor_1 (eq, xor_1_out[0], xor_1_out[1]);
endmodule
